// Logisim project heart.circ as structural Verilog: 1 circuit, main circuit main
module main (
);

  DotMatrix #(.inputtype("row"), .matrixcols(8)) dotmatrix_1 (
    .row0(8'h66), .row1({8{1'b1}}), .row2({8{1'b1}}), .row3({8{1'b1}}), .row4(8'h7e), .row5(8'h3c),
    .row6(8'h18));
endmodule
