// Logisim project project.circ as structural Verilog
module main (
  input  clk,
  input  initgame,
  input  [6:0] moving,
  output [31:0] out_4,
  output [31:0] out_5,
  output [31:0] out_6,
  output [31:0] out_7,
  output [31:0] out_8,
  output [31:0] out_9,
  output [31:0] out_10,
  output [31:0] out_11,
  output [31:0] out_12,
  output [31:0] out_13,
  output [31:0] out_14,
  output [31:0] out_15,
  output [31:0] out_16,
  output [31:0] out_17,
  output [31:0] out_18,
  output [31:0] out_19,
  output [31:0] out_20,
  output [31:0] out_21,
  output [31:0] out_22,
  output [31:0] out_23,
  output [31:0] out_24,
  output [31:0] out_25,
  output gameover,
  output [31:0] out_27,
  output win,
  output [31:0] out_29,
  output [31:0] out_30,
  output [31:0] out_31,
  output [31:0] out_32,
  output [31:0] out_33,
  output [31:0] out_34,
  output [31:0] out_35,
  output [31:0] out_36,
  output [31:0] out_37
);

  wire comparator_1_eq, comparator_2_eq, comparator_3_eq, enemies_1_p20, enemies_1_p72, or_2_out,
       oradd32_1_out, oradd32_2_out, oradd32_3_out, \стенки_1_out_5 , \стенки_1_out_6 ;
  wire [4:0] bullcoord, height, plcoord, \стрельба_1_номер ;
  wire [31:0] _0_prime_prime, _1_prime, _1_prime_prime, _2_prime, _3_prime, _3_prime_prime, _4_prime,
       _4_prime_prime, _5_prime, _5_prime_prime, _6_prime, _6_prime_prime, _7_prime, _7_prime_prime,
       _8_prime, _8_prime_prime, _9_prime, _9_prime_prime, _10_prime, _10_prime_prime, _11_prime,
       _11_prime_prime, _12_prime, _12_prime_prime, _13_prime, _13_prime_prime, _14_prime, _14_prime_prime,
       _15_prime, _15_prime_prime, _16_prime, _16_prime_prime, _17_prime, _17_prime_prime, _18_prime,
       _18_prime_prime, _19_prime, _19_prime_prime, _20_prime, _20_prime_prime, _21_prime, _21_prime_prime,
       _22_prime, _22_prime_prime, _23_prime, _23_prime_prime, _24_prime, _24_prime_prime, _25_prime,
       _25_prime_prime, _26_prime, _26_prime_prime, _27_prime, _27_prime_prime, _28_prime, _28_prime_prime,
       _29_prime, _29_prime_prime, _30_prime, _30_prime_prime, _31_prime, _31_prime_prime, _32_prime,
       _32_prime_prime, and_1_out, and_2_out, enemies_1_p5, wall;

  assign and_1_out = _0_prime_prime & _1_prime;  // AND_Gate and_1, 32 bits wide
  assign and_2_out = _1_prime_prime & _2_prime;  // AND_Gate and_2, 32 bits wide
  oradd32 oradd32_1 (.in(and_1_out), .out(oradd32_1_out));
  or or_1 (gameover, oradd32_1_out, oradd32_2_out, oradd32_3_out);
  oradd32 oradd32_2 (.in(enemies_1_p5), .out(oradd32_2_out));
  oradd32 oradd32_3 (.in(and_2_out), .out(oradd32_3_out));
  // Probe on moving
  \стенки  \u_стенки_1  (
    .clk(clk), .bull_2(_5_prime_prime), .wall(wall), .init(initgame), .out_6(\стенки_1_out_6 ),
    .bull(_4_prime), .out_5(\стенки_1_out_5 ));
  Comparator #(.width(7), .mode("unsigned")) comparator_1 (
    .a(moving), .b(7'b1100001), .eq(comparator_1_eq));  // open: gt, lt
  Comparator #(.width(7), .mode("unsigned")) comparator_2 (
    .a(moving), .b(7'b0100000), .eq(comparator_2_eq));  // open: gt, lt
  Player_Move player_move_1 (
    .counter(plcoord), .l(comparator_1_eq), .r(comparator_3_eq), ._0(_0_prime_prime), ._1(_1_prime_prime));
  Comparator #(.width(7), .mode("unsigned")) comparator_3 (
    .a(moving), .b(7'b1100100), .eq(comparator_3_eq));  // open: gt, lt
  // Probe on plcoord
  or or_2 (or_2_out, enemies_1_p72, \стенки_1_out_6 );
  \стрельба  \u_стрельба_1  (
    ._2(_3_prime_prime), ._3(_4_prime_prime), .out_7(_5_prime_prime), .coord(plcoord),
    .out_8(_6_prime_prime), .out_9(_7_prime_prime), .out_10(_8_prime_prime), .fire(comparator_2_eq),
    .out_12(_9_prime_prime), .out_13(_10_prime_prime), .out_14(_11_prime_prime), .out_15(_12_prime_prime),
    .out_16(_13_prime_prime), .out_17(_14_prime_prime), .out_18(_15_prime_prime), .out_19(_16_prime_prime),
    .out_20(_17_prime_prime), .out_21(_18_prime_prime), .out_22(_19_prime_prime), .out_23(_20_prime_prime),
    .out_24(_21_prime_prime), .out_25(_22_prime_prime), .out_26(_23_prime_prime), .out_27(_24_prime_prime),
    .out_28(_25_prime_prime), .out_29(_26_prime_prime), .out_30(_27_prime_prime), .out_31(_28_prime_prime),
    .out_32(_29_prime_prime), .out_33(_30_prime_prime), .out_34(_31_prime_prime), ._31(_32_prime_prime),
    .clk(clk), .\Номер (\стрельба_1_номер ), .reset(or_2_out));
  // enemies enemies_1: pin names not known; wires that end beside it: clk, initgame, \стенки_1_out_5 , \стрельба_1_номер , enemies_1_p5, bullcoord, _32_prime_prime, _32_prime, _31_prime_prime, _31_prime, _30_prime_prime, _30_prime, _29_prime_prime, _29_prime, _28_prime_prime, _28_prime, _27_prime_prime, _27_prime, _26_prime_prime, enemies_1_p20, _26_prime, _25_prime_prime, _25_prime, _24_prime_prime, enemies_1_p20, _24_prime, _23_prime_prime, _23_prime, _22_prime_prime, _22_prime, _21_prime_prime, _21_prime, _20_prime_prime, _20_prime, _19_prime_prime, _19_prime, _18_prime_prime, _18_prime, _17_prime_prime, _17_prime, _16_prime_prime, _16_prime, _15_prime_prime, _15_prime, _14_prime_prime, _14_prime, _13_prime_prime, _13_prime, _12_prime_prime, _12_prime, _11_prime_prime, _11_prime, _10_prime_prime, _10_prime, _9_prime_prime, _9_prime, _8_prime_prime, _8_prime, _7_prime_prime, _7_prime, _6_prime_prime, _6_prime, _5_prime_prime, _5_prime, _4_prime_prime, _4_prime, _3_prime_prime, _3_prime, height, _2_prime, _1_prime, enemies_1_p72, win
  assign out_37 = _32_prime | _32_prime_prime;  // OR_Gate or_3, 32 bits wide
  assign out_36 = _31_prime | _31_prime_prime;  // OR_Gate or_4, 32 bits wide
  assign out_35 = _30_prime | _30_prime_prime;  // OR_Gate or_5, 32 bits wide
  assign out_34 = _29_prime | _29_prime_prime;  // OR_Gate or_6, 32 bits wide
  assign out_33 = _28_prime | _28_prime_prime;  // OR_Gate or_7, 32 bits wide
  assign out_32 = _27_prime | _27_prime_prime;  // OR_Gate or_8, 32 bits wide
  assign out_31 = _26_prime | _26_prime_prime;  // OR_Gate or_9, 32 bits wide
  assign out_30 = _25_prime | _25_prime_prime;  // OR_Gate or_10, 32 bits wide
  assign out_29 = _24_prime | _24_prime_prime;  // OR_Gate or_11, 32 bits wide
  assign out_27 = _23_prime | _23_prime_prime;  // OR_Gate or_12, 32 bits wide
  assign out_25 = _22_prime | _22_prime_prime;  // OR_Gate or_13, 32 bits wide
  assign out_24 = _21_prime | _21_prime_prime;  // OR_Gate or_14, 32 bits wide
  assign out_23 = _20_prime | _20_prime_prime;  // OR_Gate or_15, 32 bits wide
  assign out_22 = _19_prime | _19_prime_prime;  // OR_Gate or_16, 32 bits wide
  assign out_21 = _18_prime | _18_prime_prime;  // OR_Gate or_17, 32 bits wide
  assign out_20 = _17_prime | _17_prime_prime;  // OR_Gate or_18, 32 bits wide
  assign out_19 = _16_prime | _16_prime_prime;  // OR_Gate or_19, 32 bits wide
  assign out_18 = _15_prime | _15_prime_prime;  // OR_Gate or_20, 32 bits wide
  assign out_17 = _14_prime | _14_prime_prime;  // OR_Gate or_21, 32 bits wide
  assign out_16 = _13_prime | _13_prime_prime;  // OR_Gate or_22, 32 bits wide
  assign out_15 = _12_prime | _12_prime_prime;  // OR_Gate or_23, 32 bits wide
  assign out_14 = _11_prime | _11_prime_prime;  // OR_Gate or_24, 32 bits wide
  assign out_13 = _10_prime | _10_prime_prime;  // OR_Gate or_25, 32 bits wide
  assign out_12 = _9_prime | _9_prime_prime;  // OR_Gate or_26, 32 bits wide
  assign out_11 = _8_prime_prime | _8_prime;  // OR_Gate or_27, 32 bits wide
  assign out_10 = _7_prime_prime | _7_prime;  // OR_Gate or_28, 32 bits wide
  assign out_9 = _6_prime_prime | _6_prime;  // OR_Gate or_29, 32 bits wide
  assign out_8 = _5_prime_prime | _5_prime;  // OR_Gate or_30, 32 bits wide
  assign out_7 = wall | _4_prime | _4_prime_prime;  // OR_Gate or_31, 32 bits wide
  assign out_6 = _3_prime_prime | _3_prime;  // OR_Gate or_32, 32 bits wide
  assign out_5 = _2_prime | _1_prime_prime;  // OR_Gate or_33, 32 bits wide
  assign out_4 = _1_prime | _0_prime_prime;  // OR_Gate or_34, 32 bits wide

  // Other names for the same wires on the sheet: _0[31:0] = out_4; _1[31:0] = out_5; _2[31:0] = out_6;
  //   _3[31:0] = out_7; _4[31:0] = out_8; _5[31:0] = out_9; _6[31:0] = out_10; _7[31:0] = out_11; _8[31:0] = out_12;
  //   _9[31:0] = out_13; _10[31:0] = out_14; _11[31:0] = out_15; _12[31:0] = out_16; _13[31:0] = out_17;
  //   _14[31:0] = out_18; _15[31:0] = out_19; _16[31:0] = out_20; _17[31:0] = out_21; _18[31:0] = out_22;
  //   _19[31:0] = out_23; _20[31:0] = out_24; _21[31:0] = out_25; _22[31:0] = out_27; _23[31:0] = out_29;
  //   _24[31:0] = out_30; _25[31:0] = out_31; _26[31:0] = out_32; _27[31:0] = out_33; _28[31:0] = out_34;
  //   _29[31:0] = out_35; _30[31:0] = out_36; _31[31:0] = out_37; init = initgame
endmodule

module inc5 (
  input  [4:0] X,
  output [4:0] R,
  output Cout
);

  wire [4:1] and_1_out;

  assign {Cout, and_1_out} = {and_1_out, 1'b1} & X;  // AND_Gate and_1, 5 bits wide
  assign R = X ^ {and_1_out, 1'b1};  // XOR_Gate xor_1, 5 bits wide
endmodule

module Player_Move (
  input  l,
  input  r,
  output [4:0] counter,
  output [31:0] _1,
  output [31:0] _0
);

  wire or_1_out;
  wire [31:0] shifter_1_out, shifter_2_out;

  or or_1 (or_1_out, l, r);
  Counter #(.width(5), .max('h1f)) counter_1 (.load(l), .Q(counter), .clk(or_1_out));  // open: D, count, carry, clr
  Decoder #(.select(5), .enable("false")) decoder_1 (
    .out0(_1[31]), .out1(_1[30]), .out2(_1[29]), .out3(_1[28]), .out4(_1[27]), .out5(_1[26]), .out6(_1[25]),
    .out7(_1[24]), .out8(_1[23]), .out9(_1[22]), .out10(_1[21]), .out11(_1[20]), .out12(_1[19]),
    .out13(_1[18]), .out14(_1[17]), .out15(_1[16]), .out16(_1[15]), .out17(_1[14]), .out18(_1[13]),
    .out19(_1[12]), .out20(_1[11]), .out21(_1[10]), .out22(_1[9]), .out23(_1[8]), .out24(_1[7]),
    .out25(_1[6]), .out26(_1[5]), .out27(_1[4]), .out28(_1[3]), .out29(_1[2]), .out30(_1[1]), .out31(_1[0]),
    .sel(counter));
  Shifter #(.width(32), .shift("lr")) shifter_1 (.in(_1), .\dist (5'b00001), .out(shifter_1_out));
  Shifter #(.width(32)) shifter_2 (.in(_1), .\dist (5'b00001), .out(shifter_2_out));
  assign _0 = shifter_2_out | _1 | shifter_1_out;  // OR_Gate or_2, 32 bits wide
endmodule

module transpon (
  input  [31:0] in_1,
  input  [31:0] in_2,
  input  [31:0] in_3,
  input  [31:0] in_4,
  input  [31:0] in_5,
  input  [31:0] in_6,
  input  [31:0] in_7,
  input  [31:0] in_8,
  input  [31:0] in_9,
  input  [31:0] in_10,
  input  [31:0] in_11,
  input  [31:0] in_12,
  input  [31:0] in_13,
  input  [31:0] in_14,
  input  [31:0] in_15,
  input  [31:0] in_16,
  input  [31:0] in_17,
  input  [31:0] in_18,
  input  [31:0] in_19,
  input  [31:0] in_20,
  input  [31:0] in_21,
  input  [31:0] in_22,
  input  [31:0] in_23,
  input  [31:0] in_24,
  input  [31:0] in_25,
  input  [31:0] in_26,
  input  [31:0] in_27,
  input  [31:0] in_28,
  input  [31:0] in_29,
  input  [31:0] in_30,
  input  [31:0] in_31,
  input  [31:0] in_32,
  output [31:0] _0,
  output [31:0] _1,
  output [31:0] _2,
  output [31:0] _3,
  output [31:0] _4,
  output [31:0] _5,
  output [31:0] _6,
  output [31:0] _7,
  output [31:0] _8,
  output [31:0] _9,
  output [31:0] _10,
  output [31:0] _11,
  output [31:0] _12,
  output [31:0] _13,
  output [31:0] _14,
  output [31:0] _15,
  output [31:0] _16,
  output [31:0] _17,
  output [31:0] _18,
  output [31:0] _19,
  output [31:0] _20,
  output [31:0] _21,
  output [31:0] _22,
  output [31:0] _23,
  output [31:0] _24,
  output [31:0] _25,
  output [31:0] _26,
  output [31:0] _27,
  output [31:0] _28,
  output [31:0] _29,
  output [31:0] _30,
  output [31:0] _31
);


  assign _0 = {in_1[0], in_2[0], in_3[0], in_4[0], in_5[0], in_6[0], in_7[0], in_8[0], in_9[0], in_10[0], in_11[0], in_12[0], in_13[0], in_14[0], in_15[0], in_16[0], in_17[0], in_18[0], in_19[0], in_20[0], in_21[0], in_22[0], in_23[0], in_24[0], in_25[0], in_26[0], in_27[0], in_28[0], in_29[0], in_30[0], in_31[0], in_32[0]};
  assign _1 = {in_1[1], in_2[1], in_3[1], in_4[1], in_5[1], in_6[1], in_7[1], in_8[1], in_9[1], in_10[1], in_11[1], in_12[1], in_13[1], in_14[1], in_15[1], in_16[1], in_17[1], in_18[1], in_19[1], in_20[1], in_21[1], in_22[1], in_23[1], in_24[1], in_25[1], in_26[1], in_27[1], in_28[1], in_29[1], in_30[1], in_31[1], in_32[1]};
  assign _2 = {in_1[2], in_2[2], in_3[2], in_4[2], in_5[2], in_6[2], in_7[2], in_8[2], in_9[2], in_10[2], in_11[2], in_12[2], in_13[2], in_14[2], in_15[2], in_16[2], in_17[2], in_18[2], in_19[2], in_20[2], in_21[2], in_22[2], in_23[2], in_24[2], in_25[2], in_26[2], in_27[2], in_28[2], in_29[2], in_30[2], in_31[2], in_32[2]};
  assign _3 = {in_1[3], in_2[3], in_3[3], in_4[3], in_5[3], in_6[3], in_7[3], in_8[3], in_9[3], in_10[3], in_11[3], in_12[3], in_13[3], in_14[3], in_15[3], in_16[3], in_17[3], in_18[3], in_19[3], in_20[3], in_21[3], in_22[3], in_23[3], in_24[3], in_25[3], in_26[3], in_27[3], in_28[3], in_29[3], in_30[3], in_31[3], in_32[3]};
  assign _4 = {in_1[4], in_2[4], in_3[4], in_4[4], in_5[4], in_6[4], in_7[4], in_8[4], in_9[4], in_10[4], in_11[4], in_12[4], in_13[4], in_14[4], in_15[4], in_16[4], in_17[4], in_18[4], in_19[4], in_20[4], in_21[4], in_22[4], in_23[4], in_24[4], in_25[4], in_26[4], in_27[4], in_28[4], in_29[4], in_30[4], in_31[4], in_32[4]};
  assign _5 = {in_1[5], in_2[5], in_3[5], in_4[5], in_5[5], in_6[5], in_7[5], in_8[5], in_9[5], in_10[5], in_11[5], in_12[5], in_13[5], in_14[5], in_15[5], in_16[5], in_17[5], in_18[5], in_19[5], in_20[5], in_21[5], in_22[5], in_23[5], in_24[5], in_25[5], in_26[5], in_27[5], in_28[5], in_29[5], in_30[5], in_31[5], in_32[5]};
  assign _6 = {in_1[6], in_2[6], in_3[6], in_4[6], in_5[6], in_6[6], in_7[6], in_8[6], in_9[6], in_10[6], in_11[6], in_12[6], in_13[6], in_14[6], in_15[6], in_16[6], in_17[6], in_18[6], in_19[6], in_20[6], in_21[6], in_22[6], in_23[6], in_24[6], in_25[6], in_26[6], in_27[6], in_28[6], in_29[6], in_30[6], in_31[6], in_32[6]};
  assign _7 = {in_1[7], in_2[7], in_3[7], in_4[7], in_5[7], in_6[7], in_7[7], in_8[7], in_9[7], in_10[7], in_11[7], in_12[7], in_13[7], in_14[7], in_15[7], in_16[7], in_17[7], in_18[7], in_19[7], in_20[7], in_21[7], in_22[7], in_23[7], in_24[7], in_25[7], in_26[7], in_27[7], in_28[7], in_29[7], in_30[7], in_31[7], in_32[7]};
  assign _8 = {in_1[8], in_2[8], in_3[8], in_4[8], in_5[8], in_6[8], in_7[8], in_8[8], in_9[8], in_10[8], in_11[8], in_12[8], in_13[8], in_14[8], in_15[8], in_16[8], in_17[8], in_18[8], in_19[8], in_20[8], in_21[8], in_22[8], in_23[8], in_24[8], in_25[8], in_26[8], in_27[8], in_28[8], in_29[8], in_30[8], in_31[8], in_32[8]};
  assign _9 = {in_1[9], in_2[9], in_3[9], in_4[9], in_5[9], in_6[9], in_7[9], in_8[9], in_9[9], in_10[9], in_11[9], in_12[9], in_13[9], in_14[9], in_15[9], in_16[9], in_17[9], in_18[9], in_19[9], in_20[9], in_21[9], in_22[9], in_23[9], in_24[9], in_25[9], in_26[9], in_27[9], in_28[9], in_29[9], in_30[9], in_31[9], in_32[9]};
  assign _10 = {in_1[10], in_2[10], in_3[10], in_4[10], in_5[10], in_6[10], in_7[10], in_8[10], in_9[10], in_10[10], in_11[10], in_12[10], in_13[10], in_14[10], in_15[10], in_16[10], in_17[10], in_18[10], in_19[10], in_20[10], in_21[10], in_22[10], in_23[10], in_24[10], in_25[10], in_26[10], in_27[10], in_28[10], in_29[10], in_30[10], in_31[10], in_32[10]};
  assign _11 = {in_1[11], in_2[11], in_3[11], in_4[11], in_5[11], in_6[11], in_7[11], in_8[11], in_9[11], in_10[11], in_11[11], in_12[11], in_13[11], in_14[11], in_15[11], in_16[11], in_17[11], in_18[11], in_19[11], in_20[11], in_21[11], in_22[11], in_23[11], in_24[11], in_25[11], in_26[11], in_27[11], in_28[11], in_29[11], in_30[11], in_31[11], in_32[11]};
  assign _12 = {in_1[12], in_2[12], in_3[12], in_4[12], in_5[12], in_6[12], in_7[12], in_8[12], in_9[12], in_10[12], in_11[12], in_12[12], in_13[12], in_14[12], in_15[12], in_16[12], in_17[12], in_18[12], in_19[12], in_20[12], in_21[12], in_22[12], in_23[12], in_24[12], in_25[12], in_26[12], in_27[12], in_28[12], in_29[12], in_30[12], in_31[12], in_32[12]};
  assign _13 = {in_1[13], in_2[13], in_3[13], in_4[13], in_5[13], in_6[13], in_7[13], in_8[13], in_9[13], in_10[13], in_11[13], in_12[13], in_13[13], in_14[13], in_15[13], in_16[13], in_17[13], in_18[13], in_19[13], in_20[13], in_21[13], in_22[13], in_23[13], in_24[13], in_25[13], in_26[13], in_27[13], in_28[13], in_29[13], in_30[13], in_31[13], in_32[13]};
  assign _14 = {in_1[14], in_2[14], in_3[14], in_4[14], in_5[14], in_6[14], in_7[14], in_8[14], in_9[14], in_10[14], in_11[14], in_12[14], in_13[14], in_14[14], in_15[14], in_16[14], in_17[14], in_18[14], in_19[14], in_20[14], in_21[14], in_22[14], in_23[14], in_24[14], in_25[14], in_26[14], in_27[14], in_28[14], in_29[14], in_30[14], in_31[14], in_32[14]};
  assign _15 = {in_1[15], in_2[15], in_3[15], in_4[15], in_5[15], in_6[15], in_7[15], in_8[15], in_9[15], in_10[15], in_11[15], in_12[15], in_13[15], in_14[15], in_15[15], in_16[15], in_17[15], in_18[15], in_19[15], in_20[15], in_21[15], in_22[15], in_23[15], in_24[15], in_25[15], in_26[15], in_27[15], in_28[15], in_29[15], in_30[15], in_31[15], in_32[15]};
  assign _16 = {in_1[16], in_2[16], in_3[16], in_4[16], in_5[16], in_6[16], in_7[16], in_8[16], in_9[16], in_10[16], in_11[16], in_12[16], in_13[16], in_14[16], in_15[16], in_16[16], in_17[16], in_18[16], in_19[16], in_20[16], in_21[16], in_22[16], in_23[16], in_24[16], in_25[16], in_26[16], in_27[16], in_28[16], in_29[16], in_30[16], in_31[16], in_32[16]};
  assign _17 = {in_1[17], in_2[17], in_3[17], in_4[17], in_5[17], in_6[17], in_7[17], in_8[17], in_9[17], in_10[17], in_11[17], in_12[17], in_13[17], in_14[17], in_15[17], in_16[17], in_17[17], in_18[17], in_19[17], in_20[17], in_21[17], in_22[17], in_23[17], in_24[17], in_25[17], in_26[17], in_27[17], in_28[17], in_29[17], in_30[17], in_31[17], in_32[17]};
  assign _18 = {in_1[18], in_2[18], in_3[18], in_4[18], in_5[18], in_6[18], in_7[18], in_8[18], in_9[18], in_10[18], in_11[18], in_12[18], in_13[18], in_14[18], in_15[18], in_16[18], in_17[18], in_18[18], in_19[18], in_20[18], in_21[18], in_22[18], in_23[18], in_24[18], in_25[18], in_26[18], in_27[18], in_28[18], in_29[18], in_30[18], in_31[18], in_32[18]};
  assign _19 = {in_1[19], in_2[19], in_3[19], in_4[19], in_5[19], in_6[19], in_7[19], in_8[19], in_9[19], in_10[19], in_11[19], in_12[19], in_13[19], in_14[19], in_15[19], in_16[19], in_17[19], in_18[19], in_19[19], in_20[19], in_21[19], in_22[19], in_23[19], in_24[19], in_25[19], in_26[19], in_27[19], in_28[19], in_29[19], in_30[19], in_31[19], in_32[19]};
  assign _20 = {in_1[20], in_2[20], in_3[20], in_4[20], in_5[20], in_6[20], in_7[20], in_8[20], in_9[20], in_10[20], in_11[20], in_12[20], in_13[20], in_14[20], in_15[20], in_16[20], in_17[20], in_18[20], in_19[20], in_20[20], in_21[20], in_22[20], in_23[20], in_24[20], in_25[20], in_26[20], in_27[20], in_28[20], in_29[20], in_30[20], in_31[20], in_32[20]};
  assign _21 = {in_1[21], in_2[21], in_3[21], in_4[21], in_5[21], in_6[21], in_7[21], in_8[21], in_9[21], in_10[21], in_11[21], in_12[21], in_13[21], in_14[21], in_15[21], in_16[21], in_17[21], in_18[21], in_19[21], in_20[21], in_21[21], in_22[21], in_23[21], in_24[21], in_25[21], in_26[21], in_27[21], in_28[21], in_29[21], in_30[21], in_31[21], in_32[21]};
  assign _22 = {in_1[22], in_2[22], in_3[22], in_4[22], in_5[22], in_6[22], in_7[22], in_8[22], in_9[22], in_10[22], in_11[22], in_12[22], in_13[22], in_14[22], in_15[22], in_16[22], in_17[22], in_18[22], in_19[22], in_20[22], in_21[22], in_22[22], in_23[22], in_24[22], in_25[22], in_26[22], in_27[22], in_28[22], in_29[22], in_30[22], in_31[22], in_32[22]};
  assign _23 = {in_1[23], in_2[23], in_3[23], in_4[23], in_5[23], in_6[23], in_7[23], in_8[23], in_9[23], in_10[23], in_11[23], in_12[23], in_13[23], in_14[23], in_15[23], in_16[23], in_17[23], in_18[23], in_19[23], in_20[23], in_21[23], in_22[23], in_23[23], in_24[23], in_25[23], in_26[23], in_27[23], in_28[23], in_29[23], in_30[23], in_31[23], in_32[23]};
  assign _24 = {in_1[24], in_2[24], in_3[24], in_4[24], in_5[24], in_6[24], in_7[24], in_8[24], in_9[24], in_10[24], in_11[24], in_12[24], in_13[24], in_14[24], in_15[24], in_16[24], in_17[24], in_18[24], in_19[24], in_20[24], in_21[24], in_22[24], in_23[24], in_24[24], in_25[24], in_26[24], in_27[24], in_28[24], in_29[24], in_30[24], in_31[24], in_32[24]};
  assign _25 = {in_1[25], in_2[25], in_3[25], in_4[25], in_5[25], in_6[25], in_7[25], in_8[25], in_9[25], in_10[25], in_11[25], in_12[25], in_13[25], in_14[25], in_15[25], in_16[25], in_17[25], in_18[25], in_19[25], in_20[25], in_21[25], in_22[25], in_23[25], in_24[25], in_25[25], in_26[25], in_27[25], in_28[25], in_29[25], in_30[25], in_31[25], in_32[25]};
  assign _26 = {in_1[26], in_2[26], in_3[26], in_4[26], in_5[26], in_6[26], in_7[26], in_8[26], in_9[26], in_10[26], in_11[26], in_12[26], in_13[26], in_14[26], in_15[26], in_16[26], in_17[26], in_18[26], in_19[26], in_20[26], in_21[26], in_22[26], in_23[26], in_24[26], in_25[26], in_26[26], in_27[26], in_28[26], in_29[26], in_30[26], in_31[26], in_32[26]};
  assign _27 = {in_1[27], in_2[27], in_3[27], in_4[27], in_5[27], in_6[27], in_7[27], in_8[27], in_9[27], in_10[27], in_11[27], in_12[27], in_13[27], in_14[27], in_15[27], in_16[27], in_17[27], in_18[27], in_19[27], in_20[27], in_21[27], in_22[27], in_23[27], in_24[27], in_25[27], in_26[27], in_27[27], in_28[27], in_29[27], in_30[27], in_31[27], in_32[27]};
  assign _28 = {in_1[28], in_2[28], in_3[28], in_4[28], in_5[28], in_6[28], in_7[28], in_8[28], in_9[28], in_10[28], in_11[28], in_12[28], in_13[28], in_14[28], in_15[28], in_16[28], in_17[28], in_18[28], in_19[28], in_20[28], in_21[28], in_22[28], in_23[28], in_24[28], in_25[28], in_26[28], in_27[28], in_28[28], in_29[28], in_30[28], in_31[28], in_32[28]};
  assign _29 = {in_1[29], in_2[29], in_3[29], in_4[29], in_5[29], in_6[29], in_7[29], in_8[29], in_9[29], in_10[29], in_11[29], in_12[29], in_13[29], in_14[29], in_15[29], in_16[29], in_17[29], in_18[29], in_19[29], in_20[29], in_21[29], in_22[29], in_23[29], in_24[29], in_25[29], in_26[29], in_27[29], in_28[29], in_29[29], in_30[29], in_31[29], in_32[29]};
  assign _30 = {in_1[30], in_2[30], in_3[30], in_4[30], in_5[30], in_6[30], in_7[30], in_8[30], in_9[30], in_10[30], in_11[30], in_12[30], in_13[30], in_14[30], in_15[30], in_16[30], in_17[30], in_18[30], in_19[30], in_20[30], in_21[30], in_22[30], in_23[30], in_24[30], in_25[30], in_26[30], in_27[30], in_28[30], in_29[30], in_30[30], in_31[30], in_32[30]};
  assign _31 = {in_1[31], in_2[31], in_3[31], in_4[31], in_5[31], in_6[31], in_7[31], in_8[31], in_9[31], in_10[31], in_11[31], in_12[31], in_13[31], in_14[31], in_15[31], in_16[31], in_17[31], in_18[31], in_19[31], in_20[31], in_21[31], in_22[31], in_23[31], in_24[31], in_25[31], in_26[31], in_27[31], in_28[31], in_29[31], in_30[31], in_31[31], in_32[31]};

  // Other names for the same wires on the sheet: _15_t[31:0] = in_16; _14_t[31:0] = in_15; _13_t[31:0] = in_14;
  //   _12_t[31:0] = in_13; _11_t[31:0] = in_12; _10_t[31:0] = in_11; _9_t[31:0] = in_10; _8_t[31:0] = in_9;
  //   _7_t[31:0] = in_8; _6_t[31:0] = in_7; _5_t[31:0] = in_6; _4_t[31:0] = in_5; _3_t[31:0] = in_4;
  //   _2_t[31:0] = in_3; _1_t[31:0] = in_2; _0_t[31:0] = in_1; _31_t[31:0] = in_32; _30_t[31:0] = in_31;
  //   _29_t[31:0] = in_30; _28_t[31:0] = in_29; _27_t[31:0] = in_28; _26_t[31:0] = in_27; _25_t[31:0] = in_26;
  //   _24_t[31:0] = in_25; _23_t[31:0] = in_24; _22_t[31:0] = in_23; _21_t[31:0] = in_22; _20_t[31:0] = in_21;
  //   _19_t[31:0] = in_20; _18_t[31:0] = in_19; _17_t[31:0] = in_18; _16_t[31:0] = in_17
endmodule

module \стенки  (
  input  clk,
  input  [31:0] bull,
  input  [31:0] bull_2,
  input  init,
  output out_5,
  output out_6,
  output [31:0] wall
);

  wire and_2_out, and_3_out, and_4_out, cdm_8_mark5_1_data_inst, cdm_8_mark5_1_mem_cycle, clk_t, clr,
       comparator_1_eq, comparator_2_eq, d_ff_1_q, d_ff_2_q, decoder_1_out0, decoder_1_out1, decoder_3_out0,
       decoder_3_out1, decoder_3_out2, decoder_3_out3, decoder_3_out4, decoder_3_out5, decoder_3_out6,
       decoder_3_out7, decoder_3_out15, DONE, I_O_sel, multiplexer_1_out, not_1_out, not_2_out, not_3_out,
       not_4_out, or_1_out, or_3_out, or_4_out, or_5_out, or_6_out, or_7_out, oradd32_1_out, r, r_w,
       register_1_q, register_2_q, w, \попадание_1_trigger , \попадание_2_trigger ;
  wire [2:0] counter_1_q;
  wire [7:0] addr, arr0, arr1, arr2, arr3, arr4, arr5, arr6, arr7, arr8, cdm_8_mark5_1_data_out,
       cdm_8_mark5_1_ps, cdm_8_mark5_1_r0, cdm_8_mark5_1_r1, cdm_8_mark5_1_r2, cdm_8_mark5_1_r3,
       cdm_8_mark5_1_sp, controlled_buffer_2_out, controlled_buffer_3_out, demultiplexer_1_out0,
       demultiplexer_1_out1, demultiplexer_1_out2, demultiplexer_1_out3, io_data, multiplexer_2_out, Oarr4,
       Oarr5, Oarr6, Oarr7, Oarr8, PC;
  wire [31:0] or_2_out, \попадание_1_out , \попадание_2_out ;

  and and_1 (I_O_sel, and_3_out, decoder_1_out1);
  // Probe on PC
  and and_2 (and_2_out, out_6, ~not_1_out, init);  // AND_Gate
  Clock \u_Частота_процессора  (.out(clk_t));
  D_Flip_Flop #(.trigger("falling")) d_ff_1 (
    .Q(d_ff_1_q), .preset(comparator_1_eq), .reset(d_ff_2_q));  // open: clk, D, Qn, en
  Comparator comparator_1 (.a(PC), .b(8'hc), .eq(comparator_1_eq));  // open: gt, lt
  D_Flip_Flop #(.trigger("falling")) d_ff_2 (.clk(clk_t), .D(and_2_out), .Q(d_ff_2_q));  // open: Qn, preset, en, reset
  D_Flip_Flop d_ff_3 (.Q(out_6), .preset(register_1_q), .reset(DONE));  // open: clk, D, Qn, en
  Register #(.width(1)) register_1 (.D(or_1_out), .Q(register_1_q), .clk(clk));  // open: en, clr
  or or_1 (or_1_out, \попадание_1_trigger , \попадание_2_trigger );
  and and_3 (and_3_out, addr[4], addr[5], addr[6], addr[7], decoder_1_out1);
  // Probe on cdm_8_mark5_1_r1
  // Probe on cdm_8_mark5_1_r3
  // Probe on cdm_8_mark5_1_r2
  // Probe on cdm_8_mark5_1_r0
  Multiplexer #(.enable("false")) multiplexer_1 (.in0(1'b0), .in1(clk_t), .out(multiplexer_1_out), .sel(not_1_out));
  \попадание  \u_попадание_1  (.OUT(\попадание_1_out ), .A(bull_2), .B(wall), .Trigger(\попадание_1_trigger ));
  and and_4 (and_4_out, decoder_1_out1, ~and_3_out);  // AND_Gate
  // Probe on cdm_8_mark5_1_ps
  // Probe on cdm_8_mark5_1_sp
  // Probe on PC
  CdM_8_mark5 cdm_8_mark5_1 (
    .clock(multiplexer_1_out), .addr(addr), .mem_read(r_w), .mem_cycle(cdm_8_mark5_1_mem_cycle),
    .data_inst(cdm_8_mark5_1_data_inst), .data_out(cdm_8_mark5_1_data_out),
    .data_in(controlled_buffer_2_out), .r0(cdm_8_mark5_1_r0), .r1(cdm_8_mark5_1_r1), .r2(cdm_8_mark5_1_r2),
    .r3(cdm_8_mark5_1_r3), .PC(PC), .SP(cdm_8_mark5_1_sp), .PS(cdm_8_mark5_1_ps));  // open: IAck, IRQ, vec, reset
  not not_1 (not_1_out, d_ff_1_q);
  \попадание  \u_попадание_2  (.OUT(\попадание_2_out ), .A(bull), .B(wall), .Trigger(\попадание_2_trigger ));
  Register #(.width(1)) register_2 (.D(\попадание_2_trigger ), .Q(register_2_q), .clk(clk));  // open: en, clr
  Decoder #(.disabled(0)) decoder_1 (
    .out0(decoder_1_out0), .out1(decoder_1_out1), .sel(cdm_8_mark5_1_data_inst), .en(cdm_8_mark5_1_mem_cycle));
  not not_2 (not_2_out, r_w);
  assign io_data = not_2_out ? cdm_8_mark5_1_data_out : 8'bz;  // Controlled_Buffer controlled_buffer_1
  assign controlled_buffer_2_out = r_w ? io_data : 8'bz;  // Controlled_Buffer controlled_buffer_2
  D_Flip_Flop d_ff_4 (.Q(out_5), .preset(register_2_q), .reset(DONE));  // open: clk, D, Qn, en
  oradd32 oradd32_1 (.in(or_2_out), .out(oradd32_1_out));
  assign or_2_out = \попадание_2_out  | \попадание_1_out ;  // OR_Gate or_2, 32 bits wide
  // Probe on addr
  Register #(.width(32)) register_3 (
    .D(or_2_out), .en(oradd32_1_out), .Q({arr7, arr6, arr5, arr4}), .clk(clk));  // open: clr
  RAM ram_1 (.addr(addr), .data(io_data), .sel(and_4_out), .clk(clk_t), .ld(r_w), .clr(clr));
  ROM rom_1 (.addr(addr), .data(io_data), .sel(decoder_1_out0));
  // Probe on io_data
  Decoder decoder_2 (.out0(r), .out1(w), .sel(r_w), .en(I_O_sel));
  Pull_Resistor pull_resistor_1 (.node(r));
  Pull_Resistor pull_resistor_2 (.node(w));
  // Probe on addr[3:0]
  or or_3 (or_3_out, r, w);
  Decoder #(.select(4)) decoder_3 (
    .out0(decoder_3_out0), .out1(decoder_3_out1), .out2(decoder_3_out2), .out3(decoder_3_out3),
    .out4(decoder_3_out4), .out5(decoder_3_out5), .out6(decoder_3_out6), .out7(decoder_3_out7),
    .out15(decoder_3_out15), .sel(addr[3:0]), .en(or_3_out));  // open: out8, out9, out10, out11, out12, out13, out14
  assign controlled_buffer_3_out = r ? io_data : 8'bz;  // Controlled_Buffer controlled_buffer_3
  // Probe on controlled_buffer_3_out
  Pull_Resistor pull_resistor_3 (.node(decoder_3_out0));
  Pull_Resistor pull_resistor_4 (.node(decoder_3_out1));
  Pull_Resistor pull_resistor_5 (.node(decoder_3_out2));
  Pull_Resistor pull_resistor_6 (.node(decoder_3_out3));
  Pull_Resistor pull_resistor_7 (.node(decoder_3_out4));
  Pull_Resistor pull_resistor_8 (.node(decoder_3_out5));
  Pull_Resistor pull_resistor_9 (.node(decoder_3_out6));
  Pull_Resistor pull_resistor_10 (.node(decoder_3_out15));
  // Probe on addr[3:0]
  Demultiplexer #(.select(4), .width(8)) demultiplexer_1 (
    .out0(demultiplexer_1_out0), .out1(demultiplexer_1_out1), .out2(demultiplexer_1_out2),
    .out3(demultiplexer_1_out3), .out15(arr8), .in(controlled_buffer_3_out), .sel(addr[3:0]), .en(r));  // open: out4, out5, out6, out7, out8, out9, out10, out11, out12, out13, out14
  Pull_Resistor pull_resistor_11 (.node(decoder_3_out7));
  assign arr0 = r ? demultiplexer_1_out0 : 8'bz;  // Controlled_Buffer controlled_buffer_4
  assign arr1 = r ? demultiplexer_1_out1 : 8'bz;  // Controlled_Buffer controlled_buffer_5
  assign arr2 = r ? demultiplexer_1_out2 : 8'bz;  // Controlled_Buffer controlled_buffer_6
  assign arr3 = r ? demultiplexer_1_out3 : 8'bz;  // Controlled_Buffer controlled_buffer_7
  Counter #(.width(3), .max('h2)) counter_1 (
    .count(decoder_3_out3), .Q(counter_1_q), .clk(decoder_3_out3), .clr(not_3_out));  // open: load, D, carry
  not not_3 (not_3_out, out_6);
  or or_4 (or_4_out, decoder_3_out4, out_6);
  or or_5 (or_5_out, decoder_3_out5, out_6);
  or or_6 (or_6_out, decoder_3_out6, out_6);
  or or_7 (or_7_out, decoder_3_out7, out_6);
  Comparator #(.width(3), .mode("unsigned")) comparator_2 (
    .a(counter_1_q), .b(3'b010), .eq(comparator_2_eq));  // open: gt, lt
  assign io_data = w ? multiplexer_2_out : 8'bz;  // Controlled_Buffer controlled_buffer_8
  Multiplexer #(.select(4), .width(8)) multiplexer_2 (
    .in0(wall[7:0]), .in1(wall[15:8]), .in2(wall[23:16]), .in3(wall[31:24]), .in4(arr4), .in5(arr5),
    .in6(arr6), .in7(arr7), .in15(arr8), .out(multiplexer_2_out), .sel(addr[3:0]), .en(w));  // open: in8, in9, in10, in11, in12, in13, in14
  Register register_4 (.D(arr0), .en(decoder_3_out0), .Q(wall[7:0]), .clk(clk_t));  // open: clr
  Register register_5 (.D(arr1), .en(decoder_3_out1), .Q(wall[15:8]), .clk(clk_t));  // open: clr
  Register register_6 (.D(arr2), .en(decoder_3_out2), .Q(wall[23:16]), .clk(clk_t));  // open: clr
  Register register_7 (.D(arr3), .en(decoder_3_out3), .Q(wall[31:24]), .clk(clk_t));  // open: clr
  Register register_8 (.D(arr4), .en(or_4_out), .Q(Oarr4), .clk(clk_t));  // open: clr
  Register register_9 (.D(arr5), .en(or_5_out), .Q(Oarr5), .clk(clk_t));  // open: clr
  Register register_10 (.D(arr6), .en(or_6_out), .Q(Oarr6), .clk(clk_t));  // open: clr
  Register register_11 (.D(arr7), .en(or_7_out), .Q(Oarr7), .clk(clk_t));  // open: clr
  Register register_12 (.D(arr8), .en(decoder_3_out15), .Q(Oarr8), .clk(clk_t));  // open: clr
  Register #(.width(1)) register_13 (
    .D(comparator_2_eq), .Q(DONE), .clk(comparator_2_eq), .clr(not_4_out));  // open: en
  not not_4 (not_4_out, out_6);

  // Other names for the same wires on the sheet: IOaddr[3:0] = addr[3:0]; BOOM = out_6; BOOMmon = out_5; gen = clk;
  //   StartGame = init; Oarr0[7:0] = wall[7:0]; Oarr1[7:0] = wall[15:8]; Oarr2[7:0] = wall[23:16];
  //   Oarr3[7:0] = wall[31:24]

  // Notes on the sheet:
  //   contents of rom_1 (hex, n*v repeats v):
  //   d0 3c d1 f0 a4 8d a4 8d a4 8d a4 c0 c4 d0 f0 d1 f4 d3 3 f eb 21 c3 b2 b7 6b a3 8c 8d c7 8b ee 13 d6
  //   c d4 209*0 4 4
  //   Указывает, завершилась ли обработка попадания
  //   stack
  //   hits
  //   walls
endmodule

module \попадание  (
  input  [31:0] A,
  input  [31:0] B,
  output [31:0] OUT,
  output Trigger
);

  wire [31:0] xnor_1_out;

  assign xnor_1_out = ~(A ^ B);  // XNOR_Gate xnor_1, 32 bits wide
  and and_1 (OUT[0], xnor_1_out[0], B[0]);
  and and_2 (OUT[1], xnor_1_out[1], B[1]);
  and and_3 (OUT[2], xnor_1_out[2], B[2]);
  and and_4 (OUT[3], xnor_1_out[3], B[3]);
  and and_5 (OUT[4], xnor_1_out[4], B[4]);
  and and_6 (OUT[5], xnor_1_out[5], B[5]);
  and and_7 (OUT[6], xnor_1_out[6], B[6]);
  and and_8 (OUT[7], xnor_1_out[7], B[7]);
  and and_9 (OUT[8], xnor_1_out[8], B[8]);
  and and_10 (OUT[9], xnor_1_out[9], B[9]);
  and and_11 (OUT[10], xnor_1_out[10], B[10]);
  and and_12 (OUT[11], xnor_1_out[11], B[11]);
  and and_13 (OUT[12], xnor_1_out[12], B[12]);
  and and_14 (OUT[13], xnor_1_out[13], B[13]);
  and and_15 (OUT[14], xnor_1_out[14], B[14]);
  and and_16 (OUT[15], xnor_1_out[15], B[15]);
  and and_17 (OUT[16], xnor_1_out[16], B[16]);
  and and_18 (OUT[17], xnor_1_out[17], B[17]);
  and and_19 (OUT[18], xnor_1_out[18], B[18]);
  and and_20 (OUT[19], xnor_1_out[19], B[19]);
  and and_21 (OUT[20], xnor_1_out[20], B[20]);
  and and_22 (OUT[21], xnor_1_out[21], B[21]);
  and and_23 (OUT[22], xnor_1_out[22], B[22]);
  and and_24 (OUT[23], xnor_1_out[23], B[23]);
  and and_25 (OUT[24], xnor_1_out[24], B[24]);
  and and_26 (OUT[25], xnor_1_out[25], B[25]);
  and and_27 (OUT[26], xnor_1_out[26], B[26]);
  and and_28 (OUT[27], xnor_1_out[27], B[27]);
  and and_29 (OUT[28], xnor_1_out[28], B[28]);
  and and_30 (OUT[29], xnor_1_out[29], B[29]);
  and and_31 (OUT[30], xnor_1_out[30], B[30]);
  and and_32 (OUT[31], xnor_1_out[31], B[31]);
  oradd32 oradd32_1 (.in(OUT), .out(Trigger));

  // Other names for the same wires on the sheet: _0 = OUT[0]; _1 = OUT[1]; _2 = OUT[2]; _3 = OUT[3]; _4 = OUT[4];
  //   _5 = OUT[5]; _6 = OUT[6]; _7 = OUT[7]; _8 = OUT[8]; _9 = OUT[9]; _10 = OUT[10]; _11 = OUT[11]; _12 = OUT[12];
  //   _13 = OUT[13]; _14 = OUT[14]; _15 = OUT[15]; _16 = OUT[16]; _17 = OUT[17]; _18 = OUT[18]; _19 = OUT[19];
  //   _20 = OUT[20]; _21 = OUT[21]; _22 = OUT[22]; _23 = OUT[23]; _24 = OUT[24]; _25 = OUT[25]; _26 = OUT[26];
  //   _27 = OUT[27]; _28 = OUT[28]; _29 = OUT[29]; _30 = OUT[30]; _31 = OUT[31]
endmodule

module \стрельба  (
  input  [4:0] coord,
  input  clk,
  input  fire,
  input  reset,
  output [31:0] _2,
  output [31:0] _3,
  output [31:0] out_7,
  output [31:0] out_8,
  output [31:0] out_9,
  output [31:0] out_10,
  output [4:0] \Номер ,
  output [31:0] out_12,
  output [31:0] out_13,
  output [31:0] out_14,
  output [31:0] out_15,
  output [31:0] out_16,
  output [31:0] out_17,
  output [31:0] out_18,
  output [31:0] out_19,
  output [31:0] out_20,
  output [31:0] out_21,
  output [31:0] out_22,
  output [31:0] out_23,
  output [31:0] out_24,
  output [31:0] out_25,
  output [31:0] out_26,
  output [31:0] out_27,
  output [31:0] out_28,
  output [31:0] out_29,
  output [31:0] out_30,
  output [31:0] out_31,
  output [31:0] out_32,
  output [31:0] out_33,
  output [31:0] out_34,
  output [31:0] _31
);

  wire A0, controlled_buffer_3_out, counter_1_carry, fire_t, not_1_out, or_1_out, or_2_out,
       pull_resistor_1_node, started;
  wire [4:0] counter_1_q, register_1_q;
  wire [31:0] demultiplexer_1_out0, demultiplexer_1_out1, demultiplexer_1_out2, demultiplexer_1_out3,
       demultiplexer_1_out4, demultiplexer_1_out5, demultiplexer_1_out6, demultiplexer_1_out7,
       demultiplexer_1_out8, demultiplexer_1_out9, demultiplexer_1_out10, demultiplexer_1_out11,
       demultiplexer_1_out12, demultiplexer_1_out13, demultiplexer_1_out14, demultiplexer_1_out15,
       demultiplexer_1_out16, demultiplexer_1_out17, demultiplexer_1_out18, demultiplexer_1_out19,
       demultiplexer_1_out20, demultiplexer_1_out21, demultiplexer_1_out22, demultiplexer_1_out23,
       demultiplexer_1_out24, demultiplexer_1_out25, demultiplexer_1_out26, demultiplexer_1_out27,
       demultiplexer_1_out28, demultiplexer_1_out29, demultiplexer_1_out30, demultiplexer_1_out31, st;

  not not_1 (not_1_out, started);
  Pull_Resistor pull_resistor_1 (.node(pull_resistor_1_node));
  assign pull_resistor_1_node = not_1_out ? fire : 1'bz;  // Controlled_Buffer controlled_buffer_1
  got1 got1_1 (.in_1(pull_resistor_1_node), .out_2(fire_t));
  // Probe on coord
  Demultiplexer #(.select(5), .width(32)) demultiplexer_1 (
    .out0(demultiplexer_1_out0), .out1(demultiplexer_1_out1), .out2(demultiplexer_1_out2),
    .out3(demultiplexer_1_out3), .out4(demultiplexer_1_out4), .out5(demultiplexer_1_out5),
    .out6(demultiplexer_1_out6), .out7(demultiplexer_1_out7), .out8(demultiplexer_1_out8),
    .out9(demultiplexer_1_out9), .out10(demultiplexer_1_out10), .out11(demultiplexer_1_out11),
    .out12(demultiplexer_1_out12), .out13(demultiplexer_1_out13), .out14(demultiplexer_1_out14),
    .out15(demultiplexer_1_out15), .out16(demultiplexer_1_out16), .out17(demultiplexer_1_out17),
    .out18(demultiplexer_1_out18), .out19(demultiplexer_1_out19), .out20(demultiplexer_1_out20),
    .out21(demultiplexer_1_out21), .out22(demultiplexer_1_out22), .out23(demultiplexer_1_out23),
    .out24(demultiplexer_1_out24), .out25(demultiplexer_1_out25), .out26(demultiplexer_1_out26),
    .out27(demultiplexer_1_out27), .out28(demultiplexer_1_out28), .out29(demultiplexer_1_out29),
    .out30(demultiplexer_1_out30), .out31(demultiplexer_1_out31), .in(st), .sel(register_1_q));  // open: en
  Register #(.width(5)) register_1 (.D(coord), .en(fire_t), .Q(register_1_q), .clk(fire_t));  // open: clr
  transpon transpon_1 (
    .in_1(demultiplexer_1_out0), .in_2(demultiplexer_1_out1), .in_3(demultiplexer_1_out2),
    .in_4(demultiplexer_1_out3), .in_5(demultiplexer_1_out4), .in_6(demultiplexer_1_out5),
    .in_7(demultiplexer_1_out6), .in_8(demultiplexer_1_out7), .in_9(demultiplexer_1_out8),
    .in_10(demultiplexer_1_out9), .in_11(demultiplexer_1_out10), .in_12(demultiplexer_1_out11),
    .in_13(demultiplexer_1_out12), .in_14(demultiplexer_1_out13), .in_15(demultiplexer_1_out14),
    .in_16(demultiplexer_1_out15), .in_17(demultiplexer_1_out16), .in_18(demultiplexer_1_out17),
    .in_19(demultiplexer_1_out18), .in_20(demultiplexer_1_out19), .in_21(demultiplexer_1_out20),
    .in_22(demultiplexer_1_out21), .in_23(demultiplexer_1_out22), .in_24(demultiplexer_1_out23),
    .in_25(demultiplexer_1_out24), .in_26(demultiplexer_1_out25), .in_27(demultiplexer_1_out26),
    .in_28(demultiplexer_1_out27), .in_29(demultiplexer_1_out28), .in_30(demultiplexer_1_out29),
    .in_31(demultiplexer_1_out30), .in_32(demultiplexer_1_out31), ._2(_2), ._3(_3), ._4(out_7), ._5(out_8),
    ._6(out_9), ._7(out_10), ._8(out_12), ._9(out_13), ._10(out_14), ._11(out_15), ._12(out_16),
    ._13(out_17), ._14(out_18), ._15(out_19), ._16(out_20), ._17(out_21), ._18(out_22), ._19(out_23),
    ._20(out_24), ._21(out_25), ._22(out_26), ._23(out_27), ._24(out_28), ._25(out_29), ._26(out_30),
    ._27(out_31), ._29(out_33), ._30(out_34), ._31(_31), ._28(out_32));  // open: _0, _1
  assign A0 = fire_t ? fire_t : 1'bz;  // Controlled_Buffer controlled_buffer_2
  D_Flip_Flop d_ff_1 (.Q(started), .preset(fire_t), .reset(or_1_out));  // open: clk, D, Qn, en
  or or_1 (or_1_out, reset, counter_1_carry);
  assign controlled_buffer_3_out = started ? clk : 1'bz;  // Controlled_Buffer controlled_buffer_3
  Counter #(.width(5), .max('h1e)) counter_1 (
    .Q(counter_1_q), .carry(counter_1_carry), .clk(controlled_buffer_3_out), .clr(or_2_out));  // open: load, D, count
  or or_2 (or_2_out, reset, ~started);  // OR_Gate
  Decoder #(.select(5), .enable("false")) decoder_1 (
    .out0(st[0]), .out1(st[1]), .out2(st[2]), .out3(st[3]), .out4(st[4]), .out5(st[5]), .out6(st[6]),
    .out7(st[7]), .out8(st[8]), .out9(st[9]), .out10(st[10]), .out11(st[11]), .out12(st[12]), .out13(st[13]),
    .out14(st[14]), .out15(st[15]), .out16(st[16]), .out17(st[17]), .out18(st[18]), .out19(st[19]),
    .out20(st[20]), .out21(st[21]), .out22(st[22]), .out23(st[23]), .out24(st[24]), .out25(st[25]),
    .out26(st[26]), .out27(st[27]), .out28(st[28]), .out29(st[29]), .out30(st[30]), .out31(st[31]),
    .sel(\Номер ));
  inc5 inc5_1 (.X(counter_1_q), .R(\Номер ));  // open: Cout

  // Other names for the same wires on the sheet: _4[31:0] = out_7; _5[31:0] = out_8; _6[31:0] = out_9;
  //   _7[31:0] = out_10; _8[31:0] = out_12; _9[31:0] = out_13; _10[31:0] = out_14; _11[31:0] = out_15;
  //   _12[31:0] = out_16; _13[31:0] = out_17; _14[31:0] = out_18; _15[31:0] = out_19; _16[31:0] = out_20;
  //   _17[31:0] = out_21; _18[31:0] = out_22; _19[31:0] = out_23; _20[31:0] = out_24; _21[31:0] = out_25;
  //   _22[31:0] = out_26; _23[31:0] = out_27; _24[31:0] = out_28; _25[31:0] = out_29; _26[31:0] = out_30;
  //   _27[31:0] = out_31; _28[31:0] = out_32; _29[31:0] = out_33; _30[31:0] = out_34; A1 = A0; A2 = A0; A3 = A0

  // Notes on the sheet:
  //   Столбец из пуль
endmodule

module menu (
  input  [4:0] in,
  output [31:0] out
);

  wire decoder_1_out0, decoder_1_out1, decoder_1_out2, decoder_1_out3, decoder_1_out4, decoder_1_out5,
       decoder_1_out6, decoder_1_out7, decoder_1_out8, decoder_1_out9, decoder_1_out10, decoder_1_out11,
       decoder_1_out12, decoder_1_out13, decoder_1_out14, decoder_1_out15, decoder_1_out16, decoder_1_out17,
       decoder_1_out18, decoder_1_out19, decoder_1_out20, decoder_1_out21, decoder_1_out22, decoder_1_out23,
       decoder_1_out24, decoder_1_out25, decoder_1_out26, decoder_1_out27, decoder_1_out28, decoder_1_out29,
       decoder_1_out30, decoder_1_out31;
  wire [31:0] pull_resistor_1_node, pull_resistor_2_node, pull_resistor_3_node;

  Pull_Resistor pull_resistor_1 (.node(pull_resistor_1_node));
  Pull_Resistor pull_resistor_2 (.node(pull_resistor_2_node));
  Pull_Resistor pull_resistor_3 (.node(pull_resistor_3_node));
  Decoder #(.select(5), .disabled(0), .enable("false")) decoder_1 (
    .out0(decoder_1_out0), .out1(decoder_1_out1), .out2(decoder_1_out2), .out3(decoder_1_out3),
    .out4(decoder_1_out4), .out5(decoder_1_out5), .out6(decoder_1_out6), .out7(decoder_1_out7),
    .out8(decoder_1_out8), .out9(decoder_1_out9), .out10(decoder_1_out10), .out11(decoder_1_out11),
    .out12(decoder_1_out12), .out13(decoder_1_out13), .out14(decoder_1_out14), .out15(decoder_1_out15),
    .out16(decoder_1_out16), .out17(decoder_1_out17), .out18(decoder_1_out18), .out19(decoder_1_out19),
    .out20(decoder_1_out20), .out21(decoder_1_out21), .out22(decoder_1_out22), .out23(decoder_1_out23),
    .out24(decoder_1_out24), .out25(decoder_1_out25), .out26(decoder_1_out26), .out27(decoder_1_out27),
    .out28(decoder_1_out28), .out29(decoder_1_out29), .out30(decoder_1_out30), .out31(decoder_1_out31),
    .sel(in));
  assign out = decoder_1_out28 ? pull_resistor_3_node : 32'bz;  // Controlled_Buffer controlled_buffer_1
  assign out = decoder_1_out29 ? pull_resistor_3_node : 32'bz;  // Controlled_Buffer controlled_buffer_2
  assign out = decoder_1_out30 ? pull_resistor_3_node : 32'bz;  // Controlled_Buffer controlled_buffer_3
  assign out = decoder_1_out31 ? pull_resistor_3_node : 32'bz;  // Controlled_Buffer controlled_buffer_4
  assign out = decoder_1_out25 ? 32'h45141040 : 32'bz;  // Controlled_Buffer controlled_buffer_5
  assign out = decoder_1_out26 ? 32'h45141040 : 32'bz;  // Controlled_Buffer controlled_buffer_6
  assign out = decoder_1_out27 ? 32'h7df7df7c : 32'bz;  // Controlled_Buffer controlled_buffer_7
  assign out = decoder_1_out22 ? 32'h41840104 : 32'bz;  // Controlled_Buffer controlled_buffer_8
  assign out = decoder_1_out23 ? 32'h7df7df7c : 32'bz;  // Controlled_Buffer controlled_buffer_9
  assign out = decoder_1_out24 ? 32'h45141040 : 32'bz;  // Controlled_Buffer controlled_buffer_10
  assign out = decoder_1_out19 ? pull_resistor_2_node : 32'bz;  // Controlled_Buffer controlled_buffer_11
  assign out = decoder_1_out20 ? 32'h4117df7c : 32'bz;  // Controlled_Buffer controlled_buffer_12
  assign out = decoder_1_out21 ? 32'h41240104 : 32'bz;  // Controlled_Buffer controlled_buffer_13
  assign out = decoder_1_out15 ? pull_resistor_2_node : 32'bz;  // Controlled_Buffer controlled_buffer_14
  assign out = decoder_1_out16 ? pull_resistor_2_node : 32'bz;  // Controlled_Buffer controlled_buffer_15
  assign out = decoder_1_out17 ? pull_resistor_2_node : 32'bz;  // Controlled_Buffer controlled_buffer_16
  assign out = decoder_1_out18 ? pull_resistor_2_node : 32'bz;  // Controlled_Buffer controlled_buffer_17
  assign out = decoder_1_out12 ? 32'h7df7dfbe : 32'bz;  // Controlled_Buffer controlled_buffer_18
  assign out = decoder_1_out13 ? pull_resistor_2_node : 32'bz;  // Controlled_Buffer controlled_buffer_19
  assign out = decoder_1_out14 ? pull_resistor_2_node : 32'bz;  // Controlled_Buffer controlled_buffer_20
  assign out = decoder_1_out9 ? 32'h40445088 : 32'bz;  // Controlled_Buffer controlled_buffer_21
  assign out = decoder_1_out10 ? 32'h40445088 : 32'bz;  // Controlled_Buffer controlled_buffer_22
  assign out = decoder_1_out11 ? 32'h40445088 : 32'bz;  // Controlled_Buffer controlled_buffer_23
  assign out = decoder_1_out5 ? 32'h7c445108 : 32'bz;  // Controlled_Buffer controlled_buffer_24
  assign out = decoder_1_out6 ? 32'h4445208 : 32'bz;  // Controlled_Buffer controlled_buffer_25
  assign out = decoder_1_out7 ? 32'h4445808 : 32'bz;  // Controlled_Buffer controlled_buffer_26
  assign out = decoder_1_out8 ? 32'h7c47df88 : 32'bz;  // Controlled_Buffer controlled_buffer_27
  assign out = decoder_1_out1 ? pull_resistor_1_node : 32'bz;  // Controlled_Buffer controlled_buffer_28
  assign out = decoder_1_out2 ? pull_resistor_1_node : 32'bz;  // Controlled_Buffer controlled_buffer_29
  assign out = decoder_1_out3 ? pull_resistor_1_node : 32'bz;  // Controlled_Buffer controlled_buffer_30
  assign out = decoder_1_out4 ? pull_resistor_1_node : 32'bz;  // Controlled_Buffer controlled_buffer_31
  assign out = decoder_1_out0 ? pull_resistor_1_node : 32'bz;  // Controlled_Buffer controlled_buffer_32
endmodule

module circ (
  input  on,
  input  isgameover,
  input  start,
  input  [4:0] counter,
  input  [31:0] game,
  input  endgame,
  output [31:0] out_7
);

  wire and_1_out, and_2_out, not_1_out;
  wire [31:0] gameover_1_out, menu_1_out;

  not not_1 (not_1_out, on);
  and and_1 (and_1_out, on, ~start);  // AND_Gate
  menu menu_1 (.in(counter), .out(menu_1_out));
  and and_2 (and_2_out, on, ~endgame, start);  // AND_Gate
  assign out_7 = not_1_out ? {32{1'b0}} : 32'bz;  // Controlled_Buffer controlled_buffer_1
  assign out_7 = and_1_out ? menu_1_out : 32'bz;  // Controlled_Buffer controlled_buffer_2
  assign out_7 = and_2_out ? game : 32'bz;  // Controlled_Buffer controlled_buffer_3
  gameover gameover_1 (.in(counter), .isGameOver(isgameover), .out(gameover_1_out));
  assign out_7 = endgame ? gameover_1_out : 32'bz;  // Controlled_Buffer controlled_buffer_4
endmodule

module menumega (
  input  gameover,
  input  endgame,
  input  on,
  input  [4:0] beg,
  input  start,
  input  [31:0] in_6,
  input  [31:0] in_7,
  input  [31:0] in_8,
  input  [31:0] in_9,
  input  [31:0] in_10,
  input  [31:0] in_11,
  input  [31:0] in_12,
  input  [31:0] in_13,
  output [31:0] out_14,
  output [31:0] out_15,
  output [31:0] out_16,
  output [31:0] out_17,
  output [31:0] out_18,
  output [31:0] out_19,
  output [31:0] out_20,
  output [31:0] out_21,
  output [4:0] \end 
);

  wire [4:0] inc5_1_r, inc5_2_r, inc5_3_r, inc5_4_r, inc5_5_r, inc5_7_r;

  circ circ_1 (
    .on(on), .start(start), .counter(beg), .game(in_6), .out_7(out_14), .isgameover(gameover),
    .endgame(endgame));
  circ circ_2 (
    .on(on), .start(start), .counter(inc5_1_r), .game(in_7), .out_7(out_15), .isgameover(gameover),
    .endgame(endgame));
  circ circ_3 (
    .on(on), .start(start), .counter(inc5_2_r), .game(in_10), .out_7(out_18), .isgameover(gameover),
    .endgame(endgame));
  inc5 inc5_1 (.X(inc5_2_r), .R(inc5_1_r));  // open: Cout
  inc5 inc5_2 (.X(beg), .R(inc5_2_r));  // open: Cout
  circ circ_4 (
    .on(on), .start(start), .counter(inc5_4_r), .game(in_11), .out_7(out_19), .isgameover(gameover),
    .endgame(endgame));
  inc5 inc5_3 (.X(inc5_4_r), .R(inc5_3_r));  // open: Cout
  inc5 inc5_4 (.X(inc5_1_r), .R(inc5_4_r));  // open: Cout
  circ circ_5 (
    .on(on), .start(start), .counter(inc5_3_r), .game(in_8), .out_7(out_16), .isgameover(gameover),
    .endgame(endgame));
  circ circ_6 (
    .on(on), .start(start), .counter(inc5_5_r), .game(in_12), .out_7(out_20), .isgameover(gameover),
    .endgame(endgame));
  inc5 inc5_5 (.X(inc5_3_r), .R(inc5_5_r));  // open: Cout
  circ circ_7 (
    .on(on), .start(start), .counter(inc5_7_r), .game(in_9), .out_7(out_17), .isgameover(gameover),
    .endgame(endgame));
  inc5 inc5_6 (.X(inc5_7_r), .R(\end ));  // open: Cout
  inc5 inc5_7 (.X(inc5_5_r), .R(inc5_7_r));  // open: Cout
  circ circ_8 (
    .on(on), .start(start), .counter(\end ), .game(in_13), .out_7(out_21), .isgameover(gameover),
    .endgame(endgame));
endmodule

module pentamenu (
  input  start,
  input  on,
  input  [6:0] control,
  output [31:0] out_4,
  output [31:0] out_5,
  output [31:0] out_6,
  output [31:0] out_7,
  output [31:0] out_8,
  output [31:0] out_9,
  output clk,
  output [31:0] out_11,
  output [31:0] out_12,
  output [31:0] out_13,
  output [31:0] out_14,
  output [31:0] out_15,
  output [31:0] out_16,
  output [31:0] out_17,
  output [31:0] out_18,
  output [31:0] out_19,
  output [31:0] out_20,
  output [31:0] out_21,
  output [31:0] out_22,
  output [31:0] out_23,
  output [31:0] out_24,
  output [31:0] out_25,
  output [31:0] out_26,
  output [31:0] out_27,
  output [31:0] out_28,
  output [31:0] out_29,
  output [31:0] out_30,
  output [31:0] out_31,
  output [31:0] out_32,
  output [31:0] out_33,
  output [31:0] out_34,
  output [31:0] out_35,
  output [31:0] out_36
);

  wire d_ff_1_q, d_ff_2_q, eg, go, main_1_gameover, main_1_win, multiplexer_1_out, not_1_out, on_t, start_t;
  wire [4:0] menumega_1_end, menumega_2_end, menumega_3_end;
  wire [31:0] main_1_out_4, main_1_out_5, main_1_out_6, main_1_out_7, main_1_out_8, main_1_out_9,
       main_1_out_10, main_1_out_11, main_1_out_12, main_1_out_13, main_1_out_14, main_1_out_15,
       main_1_out_16, main_1_out_17, main_1_out_18, main_1_out_19, main_1_out_20, main_1_out_21,
       main_1_out_22, main_1_out_23, main_1_out_24, main_1_out_25, main_1_out_27, main_1_out_29,
       main_1_out_30, main_1_out_31, main_1_out_32, main_1_out_33, main_1_out_34, main_1_out_35,
       main_1_out_36, main_1_out_37;

  Counter #(.width(1), .max('h1)) counter_1 (.count(start), .Q(start_t), .clk(start));  // open: load, D, carry, clr
  Counter #(.width(1), .max('h1)) counter_2 (.count(on), .Q(on_t), .clk(on));  // open: load, D, carry, clr
  main main_1 (
    .out_4(main_1_out_4), .out_5(main_1_out_5), .out_6(main_1_out_6), .out_7(main_1_out_7),
    .out_8(main_1_out_8), .out_9(main_1_out_9), .out_10(main_1_out_10), .out_11(main_1_out_11),
    .out_12(main_1_out_12), .out_13(main_1_out_13), .clk(clk), .out_14(main_1_out_14),
    .out_15(main_1_out_15), .out_16(main_1_out_16), .out_17(main_1_out_17), .initgame(start_t),
    .out_18(main_1_out_18), .out_19(main_1_out_19), .moving(control), .out_20(main_1_out_20),
    .out_21(main_1_out_21), .out_22(main_1_out_22), .out_23(main_1_out_23), .out_24(main_1_out_24),
    .out_25(main_1_out_25), .gameover(main_1_gameover), .out_27(main_1_out_27), .win(main_1_win),
    .out_29(main_1_out_29), .out_30(main_1_out_30), .out_31(main_1_out_31), .out_32(main_1_out_32),
    .out_33(main_1_out_33), .out_34(main_1_out_34), .out_35(main_1_out_35), .out_36(main_1_out_36),
    .out_37(main_1_out_37));
  D_Flip_Flop d_ff_1 (.clk(main_1_win), .D(main_1_win), .Q(d_ff_1_q));  // open: Qn, preset, en, reset
  menumega menumega_1 (
    .beg({5{1'b0}}), .on(on_t), .start(start_t), .out_14(out_4), .out_18(out_5), .out_15(out_6),
    .out_19(out_7), .out_16(out_8), .out_20(out_9), .out_17(out_11), .out_21(out_12), .\end (menumega_1_end),
    .in_6(main_1_out_4), .in_7(main_1_out_6), .in_8(main_1_out_8), .in_9(main_1_out_10),
    .in_10(main_1_out_5), .in_11(main_1_out_7), .in_12(main_1_out_9), .in_13(main_1_out_11), .endgame(eg),
    .gameover(go));
  assign eg = not_1_out ? d_ff_1_q : 1'bz;  // Controlled_Buffer controlled_buffer_1
  Pull_Resistor pull_resistor_1 (.node(eg));
  menumega menumega_2 (
    .beg(menumega_1_end), .on(on_t), .start(start_t), .out_14(out_13), .out_18(out_14), .out_15(out_15),
    .out_19(out_16), .out_16(out_17), .out_20(out_18), .out_17(out_19), .out_21(out_20),
    .\end (menumega_2_end), .in_6(main_1_out_12), .in_7(main_1_out_14), .in_8(main_1_out_16),
    .in_9(main_1_out_18), .in_10(main_1_out_13), .in_11(main_1_out_15), .in_12(main_1_out_17),
    .in_13(main_1_out_19), .endgame(eg), .gameover(go));
  menumega menumega_3 (
    .beg(menumega_2_end), .on(on_t), .start(start_t), .out_14(out_21), .out_18(out_22), .out_15(out_23),
    .out_19(out_24), .out_16(out_25), .out_20(out_26), .out_17(out_27), .out_21(out_28),
    .\end (menumega_3_end), .in_6(main_1_out_20), .in_7(main_1_out_22), .in_8(main_1_out_24),
    .in_9(main_1_out_27), .in_10(main_1_out_21), .in_11(main_1_out_23), .in_12(main_1_out_25),
    .in_13(main_1_out_29), .endgame(eg), .gameover(go));
  menumega menumega_4 (
    .beg(menumega_3_end), .on(on_t), .start(start_t), .out_14(out_29), .out_18(out_30), .out_15(out_31),
    .out_19(out_32), .out_16(out_33), .out_20(out_34), .out_17(out_35), .out_21(out_36),
    .in_6(main_1_out_30), .in_7(main_1_out_32), .in_8(main_1_out_34), .in_9(main_1_out_36),
    .in_10(main_1_out_31), .in_11(main_1_out_33), .in_12(main_1_out_35), .in_13(main_1_out_37), .endgame(eg),
    .gameover(go));  // open: end
  Clock clock_1 (.out(clk));
  assign eg = d_ff_2_q ? d_ff_2_q : 1'bz;  // Controlled_Buffer controlled_buffer_2
  Pull_Resistor pull_resistor_2 (.node(eg));
  D_Flip_Flop d_ff_2 (.clk(main_1_gameover), .D(main_1_gameover), .Q(d_ff_2_q));  // open: Qn, preset, en, reset
  assign go = multiplexer_1_out ? d_ff_2_q : 1'bz;  // Controlled_Buffer controlled_buffer_3
  Multiplexer multiplexer_1 (.in0(d_ff_2_q), .in1(1'b0), .out(multiplexer_1_out), .sel(d_ff_1_q));  // open: en
  not not_1 (not_1_out, d_ff_2_q);
  Pull_Resistor pull_resistor_3 (.node(go));

  // Other names for the same wires on the sheet: _0[31:0] = out_4; _1[31:0] = out_5; _2[31:0] = out_6;
  //   _3[31:0] = out_7; _4[31:0] = out_8; _5[31:0] = out_9; _6[31:0] = out_11; _7[31:0] = out_12; _8[31:0] = out_13;
  //   _9[31:0] = out_14; _10[31:0] = out_15; _11[31:0] = out_16; _12[31:0] = out_17; _13[31:0] = out_18;
  //   _14[31:0] = out_19; _15[31:0] = out_20; _16[31:0] = out_21; _17[31:0] = out_22; _18[31:0] = out_23;
  //   _19[31:0] = out_24; _20[31:0] = out_25; _21[31:0] = out_26; _22[31:0] = out_27; _23[31:0] = out_28;
  //   _24[31:0] = out_29; _25[31:0] = out_30; _26[31:0] = out_31; _27[31:0] = out_32; _28[31:0] = out_33;
  //   _29[31:0] = out_34; _30[31:0] = out_35; _31[31:0] = out_36
endmodule

module MAIN (
);

  wire keyboard_1_avail, ON_OFF_out, pentamenu_1_clk, START_out;
  wire [6:0] keyboard_1_data;
  wire [31:0] pentamenu_1_out_4, pentamenu_1_out_5, pentamenu_1_out_6, pentamenu_1_out_7, pentamenu_1_out_8,
       pentamenu_1_out_9, pentamenu_1_out_11, pentamenu_1_out_12, pentamenu_1_out_13, pentamenu_1_out_14,
       pentamenu_1_out_15, pentamenu_1_out_16, pentamenu_1_out_17, pentamenu_1_out_18, pentamenu_1_out_19,
       pentamenu_1_out_20, pentamenu_1_out_21, pentamenu_1_out_22, pentamenu_1_out_23, pentamenu_1_out_24,
       pentamenu_1_out_25, pentamenu_1_out_26, pentamenu_1_out_27, pentamenu_1_out_28, pentamenu_1_out_29,
       pentamenu_1_out_30, pentamenu_1_out_31, pentamenu_1_out_32, pentamenu_1_out_33, pentamenu_1_out_34,
       pentamenu_1_out_35, pentamenu_1_out_36;

  DotMatrix #(.inputtype("row"), .matrixcols(32), .matrixrows(32)) dotmatrix_1 (
    .row0(pentamenu_1_out_36), .row1(pentamenu_1_out_35), .row2(pentamenu_1_out_34),
    .row3(pentamenu_1_out_33), .row4(pentamenu_1_out_32), .row5(pentamenu_1_out_31),
    .row6(pentamenu_1_out_30), .row7(pentamenu_1_out_29), .row8(pentamenu_1_out_28),
    .row9(pentamenu_1_out_27), .row10(pentamenu_1_out_26), .row11(pentamenu_1_out_25),
    .row12(pentamenu_1_out_24), .row13(pentamenu_1_out_23), .row14(pentamenu_1_out_22),
    .row15(pentamenu_1_out_21), .row16(pentamenu_1_out_20), .row17(pentamenu_1_out_19),
    .row18(pentamenu_1_out_18), .row19(pentamenu_1_out_17), .row20(pentamenu_1_out_16),
    .row21(pentamenu_1_out_15), .row22(pentamenu_1_out_14), .row23(pentamenu_1_out_13),
    .row24(pentamenu_1_out_12), .row25(pentamenu_1_out_11), .row26(pentamenu_1_out_9),
    .row27(pentamenu_1_out_8), .row28(pentamenu_1_out_7), .row29(pentamenu_1_out_6),
    .row30(pentamenu_1_out_5), .row31(pentamenu_1_out_4));
  pentamenu pentamenu_1 (
    .out_4(pentamenu_1_out_4), .out_5(pentamenu_1_out_5), .start(START_out), .out_6(pentamenu_1_out_6),
    .on(ON_OFF_out), .out_7(pentamenu_1_out_7), .out_8(pentamenu_1_out_8), .out_9(pentamenu_1_out_9),
    .out_11(pentamenu_1_out_11), .control(keyboard_1_data), .out_12(pentamenu_1_out_12),
    .out_13(pentamenu_1_out_13), .out_14(pentamenu_1_out_14), .out_15(pentamenu_1_out_15),
    .out_16(pentamenu_1_out_16), .out_17(pentamenu_1_out_17), .out_18(pentamenu_1_out_18),
    .out_19(pentamenu_1_out_19), .out_20(pentamenu_1_out_20), .out_21(pentamenu_1_out_21),
    .out_22(pentamenu_1_out_22), .out_23(pentamenu_1_out_23), .out_24(pentamenu_1_out_24),
    .out_25(pentamenu_1_out_25), .out_26(pentamenu_1_out_26), .out_27(pentamenu_1_out_27),
    .out_28(pentamenu_1_out_28), .out_29(pentamenu_1_out_29), .out_30(pentamenu_1_out_30),
    .out_31(pentamenu_1_out_31), .out_32(pentamenu_1_out_32), .out_33(pentamenu_1_out_33),
    .out_34(pentamenu_1_out_34), .out_35(pentamenu_1_out_35), .out_36(pentamenu_1_out_36),
    .clk(pentamenu_1_clk));
  Keyboard keyboard_1 (
    .clk(pentamenu_1_clk), .clr(keyboard_1_avail), .avail(keyboard_1_avail), .data(keyboard_1_data));  // open: re
  cosmsirc_nonuse cosmsirc_nonuse_1 ();
  Button ON_OFF (.out(ON_OFF_out));
  Button START (.out(START_out));
endmodule

module gameover (
  input  [4:0] in,
  input  isGameOver,
  output [31:0] out
);

  wire decoder_1_out0, decoder_1_out1, decoder_1_out2, decoder_1_out3, decoder_1_out4, decoder_1_out5,
       decoder_1_out6, decoder_1_out7, decoder_1_out8, decoder_1_out9, decoder_1_out10, decoder_1_out11,
       decoder_1_out12, decoder_1_out13, decoder_1_out14, decoder_1_out15, decoder_1_out16, decoder_1_out17,
       decoder_1_out18, decoder_1_out19, decoder_1_out20, decoder_1_out21, decoder_1_out22, decoder_1_out23,
       decoder_1_out24, decoder_1_out25, decoder_1_out26, decoder_1_out27, decoder_1_out28, decoder_1_out29,
       decoder_1_out30, decoder_1_out31;
  wire [31:0] multiplexer_1_out, multiplexer_2_out, multiplexer_3_out, multiplexer_4_out, multiplexer_5_out,
       multiplexer_6_out, multiplexer_7_out, multiplexer_8_out, multiplexer_9_out, multiplexer_10_out,
       multiplexer_11_out, multiplexer_12_out, multiplexer_13_out, multiplexer_14_out, multiplexer_15_out,
       pull_resistor_1_node, pull_resistor_2_node, pull_resistor_3_node;

  Pull_Resistor pull_resistor_1 (.node(pull_resistor_1_node));
  Multiplexer #(.width(32)) multiplexer_1 (
    .in0(32'h1c3e840), .in1(32'h7e187e44), .out(multiplexer_1_out), .sel(isGameOver));  // open: en
  Multiplexer #(.width(32)) multiplexer_2 (
    .in0(32'h2a088c0), .in1(32'h42184048), .out(multiplexer_2_out), .sel(isGameOver));  // open: en
  Multiplexer #(.width(32)) multiplexer_3 (
    .in0(32'h2a089c0), .in1(32'h42247c60), .out(multiplexer_3_out), .sel(isGameOver));  // open: en
  Multiplexer #(.width(32)) multiplexer_4 (
    .in0(32'h6b08940), .in1(32'h2466407c), .out(multiplexer_4_out), .sel(isGameOver));  // open: en
  Multiplexer #(.width(32)) multiplexer_5 (
    .in0(32'h6b08b40), .in1(32'h42424042), .out(multiplexer_5_out), .sel(isGameOver));  // open: en
  Multiplexer #(.width(32)) multiplexer_6 (
    .in0(32'hc988e40), .in1(32'h42c34042), .out(multiplexer_6_out), .sel(isGameOver));  // open: en
  Multiplexer #(.width(32)) multiplexer_7 (
    .in0(32'hc988c40), .in1(32'h7e817e7c), .out(multiplexer_7_out), .sel(isGameOver));  // open: en
  Multiplexer #(.width(32)) multiplexer_8 (
    .in0(32'h80be840), .in1(pull_resistor_2_node), .out(multiplexer_8_out), .sel(isGameOver));  // open: en
  Pull_Resistor pull_resistor_2 (.node(pull_resistor_2_node));
  Multiplexer #(.width(32)) multiplexer_9 (
    .in0(32'h1f7df00), .in1(32'h7e42817e), .out(multiplexer_9_out), .sel(isGameOver));  // open: en
  Multiplexer #(.width(32)) multiplexer_10 (
    .in0(32'h145100), .in1(32'h42428140), .out(multiplexer_10_out), .sel(isGameOver));  // open: en
  Multiplexer #(.width(32)) multiplexer_11 (
    .in0(32'h145100), .in1(32'h407e817c), .out(multiplexer_11_out), .sel(isGameOver));  // open: en
  Multiplexer #(.width(32)) multiplexer_12 (
    .in0(32'h1f45100), .in1(32'h40429940), .out(multiplexer_12_out), .sel(isGameOver));  // open: en
  Multiplexer #(.width(32)) multiplexer_13 (
    .in0(32'h1145100), .in1(32'h4242bd40), .out(multiplexer_13_out), .sel(isGameOver));  // open: en
  Multiplexer #(.width(32)) multiplexer_14 (
    .in0(32'h1145100), .in1(32'h4242e740), .out(multiplexer_14_out), .sel(isGameOver));  // open: en
  Multiplexer #(.width(32)) multiplexer_15 (
    .in0(32'h117d100), .in1(32'h7e7ec37e), .out(multiplexer_15_out), .sel(isGameOver));  // open: en
  Pull_Resistor pull_resistor_3 (.node(pull_resistor_3_node));
  Decoder #(.select(5), .disabled(0), .enable("false")) decoder_1 (
    .out0(decoder_1_out0), .out1(decoder_1_out1), .out2(decoder_1_out2), .out3(decoder_1_out3),
    .out4(decoder_1_out4), .out5(decoder_1_out5), .out6(decoder_1_out6), .out7(decoder_1_out7),
    .out8(decoder_1_out8), .out9(decoder_1_out9), .out10(decoder_1_out10), .out11(decoder_1_out11),
    .out12(decoder_1_out12), .out13(decoder_1_out13), .out14(decoder_1_out14), .out15(decoder_1_out15),
    .out16(decoder_1_out16), .out17(decoder_1_out17), .out18(decoder_1_out18), .out19(decoder_1_out19),
    .out20(decoder_1_out20), .out21(decoder_1_out21), .out22(decoder_1_out22), .out23(decoder_1_out23),
    .out24(decoder_1_out24), .out25(decoder_1_out25), .out26(decoder_1_out26), .out27(decoder_1_out27),
    .out28(decoder_1_out28), .out29(decoder_1_out29), .out30(decoder_1_out30), .out31(decoder_1_out31),
    .sel(in));
  assign out = decoder_1_out28 ? pull_resistor_3_node : 32'bz;  // Controlled_Buffer controlled_buffer_1
  assign out = decoder_1_out29 ? pull_resistor_3_node : 32'bz;  // Controlled_Buffer controlled_buffer_2
  assign out = decoder_1_out30 ? pull_resistor_3_node : 32'bz;  // Controlled_Buffer controlled_buffer_3
  assign out = decoder_1_out31 ? pull_resistor_3_node : 32'bz;  // Controlled_Buffer controlled_buffer_4
  assign out = decoder_1_out26 ? multiplexer_14_out : 32'bz;  // Controlled_Buffer controlled_buffer_5
  assign out = decoder_1_out27 ? multiplexer_15_out : 32'bz;  // Controlled_Buffer controlled_buffer_6
  assign out = decoder_1_out23 ? multiplexer_11_out : 32'bz;  // Controlled_Buffer controlled_buffer_7
  assign out = decoder_1_out24 ? multiplexer_12_out : 32'bz;  // Controlled_Buffer controlled_buffer_8
  assign out = decoder_1_out25 ? multiplexer_13_out : 32'bz;  // Controlled_Buffer controlled_buffer_9
  assign out = decoder_1_out19 ? pull_resistor_2_node : 32'bz;  // Controlled_Buffer controlled_buffer_10
  assign out = decoder_1_out20 ? pull_resistor_2_node : 32'bz;  // Controlled_Buffer controlled_buffer_11
  assign out = decoder_1_out21 ? multiplexer_9_out : 32'bz;  // Controlled_Buffer controlled_buffer_12
  assign out = decoder_1_out22 ? multiplexer_10_out : 32'bz;  // Controlled_Buffer controlled_buffer_13
  assign out = decoder_1_out15 ? pull_resistor_2_node : 32'bz;  // Controlled_Buffer controlled_buffer_14
  assign out = decoder_1_out16 ? pull_resistor_2_node : 32'bz;  // Controlled_Buffer controlled_buffer_15
  assign out = decoder_1_out17 ? pull_resistor_2_node : 32'bz;  // Controlled_Buffer controlled_buffer_16
  assign out = decoder_1_out18 ? pull_resistor_2_node : 32'bz;  // Controlled_Buffer controlled_buffer_17
  assign out = decoder_1_out12 ? multiplexer_8_out : 32'bz;  // Controlled_Buffer controlled_buffer_18
  assign out = decoder_1_out13 ? pull_resistor_2_node : 32'bz;  // Controlled_Buffer controlled_buffer_19
  assign out = decoder_1_out14 ? pull_resistor_2_node : 32'bz;  // Controlled_Buffer controlled_buffer_20
  assign out = decoder_1_out9 ? multiplexer_5_out : 32'bz;  // Controlled_Buffer controlled_buffer_21
  assign out = decoder_1_out10 ? multiplexer_6_out : 32'bz;  // Controlled_Buffer controlled_buffer_22
  assign out = decoder_1_out11 ? multiplexer_7_out : 32'bz;  // Controlled_Buffer controlled_buffer_23
  assign out = decoder_1_out5 ? multiplexer_1_out : 32'bz;  // Controlled_Buffer controlled_buffer_24
  assign out = decoder_1_out6 ? multiplexer_2_out : 32'bz;  // Controlled_Buffer controlled_buffer_25
  assign out = decoder_1_out7 ? multiplexer_3_out : 32'bz;  // Controlled_Buffer controlled_buffer_26
  assign out = decoder_1_out8 ? multiplexer_4_out : 32'bz;  // Controlled_Buffer controlled_buffer_27
  assign out = decoder_1_out2 ? pull_resistor_1_node : 32'bz;  // Controlled_Buffer controlled_buffer_28
  assign out = decoder_1_out3 ? pull_resistor_1_node : 32'bz;  // Controlled_Buffer controlled_buffer_29
  assign out = decoder_1_out4 ? pull_resistor_1_node : 32'bz;  // Controlled_Buffer controlled_buffer_30
  assign out = decoder_1_out0 ? pull_resistor_1_node : 32'bz;  // Controlled_Buffer controlled_buffer_31
  assign out = decoder_1_out1 ? pull_resistor_1_node : 32'bz;  // Controlled_Buffer controlled_buffer_32
  DotMatrix #(.inputtype("row"), .matrixcols(32), .matrixrows(32)) dotmatrix_1 (
    .row19(32'h7e42817e), .row28(32'h42247c60), .row29(32'h42184048), .row30(32'h7e187e44));  // open: row0, row1, row2, row3, row4, row5, row6, row7, row8, row9, row10, row11, row12, row13, row14, row15, row16, row17, row18, row20, row21, row22, row23, row24, row25, row26, row27, row31
endmodule

module oradd32 (
  input  [31:0] in,
  output out
);

  or or_1 (out, in[0], in[1], in[2], in[3], in[4], in[5], in[6], in[7], in[8], in[9], in[10], in[11], in[12], in[13], in[14], in[15], in[16], in[17], in[18], in[19], in[20], in[21], in[22], in[23], in[24], in[25], in[26], in[27], in[28], in[29], in[30], in[31]);
endmodule

module got1 (
  input  in_1,
  output out_2
);

  wire clock_1_out;

  D_Flip_Flop d_ff_1 (.Q(out_2), .preset(in_1), .reset(clock_1_out));  // open: clk, D, Qn, en
  Clock #(.highDuration(2), .lowDuration(2)) clock_1 (.out(clock_1_out));

  // Notes on the sheet:
  //   У этойсхемы частота в 2 раза меньше, для того чтобы поймать мгновенную единичку
endmodule

module enemies (
  input  clk,
  input  [4:0] Num,
  input  wall,
  input  initgame,
  input  [31:0] in_5,
  input  [31:0] in_6,
  input  [31:0] in_7,
  input  [31:0] in_8,
  input  [31:0] in_9,
  input  [31:0] in_10,
  input  [31:0] in_11,
  input  [31:0] in_12,
  input  [31:0] in_13,
  input  [31:0] in_14,
  input  [31:0] in_15,
  input  [31:0] in_16,
  input  [31:0] in_17,
  input  [31:0] in_18,
  input  [31:0] in_19,
  input  [31:0] in_20,
  input  [31:0] in_21,
  input  [31:0] in_22,
  input  [31:0] in_23,
  input  [31:0] in_24,
  input  [31:0] in_25,
  input  [31:0] in_26,
  input  [31:0] in_27,
  input  [31:0] in_28,
  input  [31:0] in_29,
  input  [31:0] in_30,
  input  [31:0] in_31,
  input  [31:0] in_32,
  input  [31:0] in_33,
  input  [31:0] in_34,
  output [4:0] out_35,
  output boom,
  output [31:0] out_37,
  output [31:0] out_38,
  output [31:0] out_39,
  output [31:0] out_40,
  output [4:0] height,
  output [31:0] out_42,
  output [31:0] out_43,
  output [31:0] out_44,
  output [31:0] out_45,
  output [31:0] out_46,
  output [31:0] out_47,
  output [31:0] out_48,
  output [31:0] out_49,
  output [31:0] out_50,
  output [31:0] out_51,
  output [31:0] out_52,
  output [31:0] out_53,
  output [31:0] out_54,
  output [31:0] out_55,
  output [31:0] out_56,
  output [31:0] out_57,
  output [31:0] out_58,
  output [31:0] out_59,
  output [31:0] out_60,
  output [31:0] out_61,
  output [31:0] out_62,
  output [31:0] out_63,
  output [31:0] out_64,
  output win,
  output [31:0] out_66,
  output [31:0] out_67,
  output [31:0] out_68,
  output [31:0] out_69,
  output [31:0] out_70,
  output [31:0] out_71,
  output [7:0] out
);

  wire _1_prime_prime_prime, _2_prime_prime_prime, _3_prime_prime_prime, _4_prime_prime_prime,
       _11_prime_prime_prime, _12_prime_prime_prime, _13_prime_prime_prime, _14_prime_prime_prime, and_2_out,
       and_3_out, and_4_out, cdm_8_mark5_1_data_inst, cdm_8_mark5_1_mem_cycle, clk_t, clock_1_out,
       clock_2_out, clock_3_out, clr, comparator_1_eq, comparator_2_gt, comparator_3_lt, comparator_4_eq,
       comparator_5_eq, controlled_buffer_34_out, controlled_buffer_38_out, d_ff_1_q, d_ff_2_q, d_ff_4_q,
       d_ff_5_q, decoder_1_out0, decoder_1_out1, decoder_3_out0, decoder_3_out1, decoder_3_out2,
       decoder_3_out3, decoder_3_out4, DONE, I_O_sel, init, multiplexer_2_out, multiplexer_5_out, not_1_out,
       not_2_out, not_4_out, not_5_out, not_6_out, not_7_out, not_8_out, or_1_out, or_32_out, or_33_out,
       or_34_out, or_35_out, or_36_out, pull_resistor_33_node, r, r_w, random_1_out, ready, register_3_q,
       transfer, w, \попадание_1_trigger , \Частота_сдвигов_out ;
  wire [1:0] Num1;
  wire [2:0] counter_2_q;
  wire [4:0] counter_1_q, height_t, inc5_1_r, register_2_q;
  wire [7:0] addr, arr0, arr1, arr2, arr3, cdm_8_mark5_1_data_out, cdm_8_mark5_1_ps, cdm_8_mark5_1_r0,
       cdm_8_mark5_1_r1, cdm_8_mark5_1_r2, cdm_8_mark5_1_r3, cdm_8_mark5_1_sp, controlled_buffer_37_out,
       controlled_buffer_39_out, coord, demultiplexer_3_out4, enem, info, io_data, multiplexer_6_out, Oarr0,
       Oarr1, Oarr2, Oarr3, PC, register_5_q, register_6_q, register_7_q, register_8_q, register_9_q,
       register_10_q, register_11_q, register_12_q, register_13_q, register_14_q, register_15_q,
       register_16_q, register_17_q, register_18_q, register_19_q, register_20_q, subtractor_1_out;
  wire [7:5] multiplexer_1_out;
  wire [31:0] _2e, _2f, _3e, _3f, _4f, _5e, _5f, _6e, _6f, _7e, _7f, _8e, _8f, _9e, _9f, _10e, _10f, _11e,
       _11f, _12e, _12f, _13e, _13f, _14e, _14f, _15e, _15f, _16e, _16f, _17e, _17f, _18e, _18f, _19e, _19f,
       _20e, _20f, _21e, _21f, _22e, _22f, _23e, _23f, _24bul, _24e, _24f, _25e, _25f, _26e, _26f, _27e,
       _27f, _28e, _28f, _29e, _29f, _30e, _30f, _31e, _31f, demultiplexer_1_out0, demultiplexer_2_out0,
       demultiplexer_2_out1, demultiplexer_2_out2, demultiplexer_2_out3, demultiplexer_2_out4,
       demultiplexer_2_out5, demultiplexer_2_out6, demultiplexer_2_out7, demultiplexer_2_out8,
       demultiplexer_2_out9, demultiplexer_2_out10, demultiplexer_2_out11, demultiplexer_2_out12,
       demultiplexer_2_out13, demultiplexer_2_out14, demultiplexer_2_out15, demultiplexer_2_out16,
       demultiplexer_2_out17, demultiplexer_2_out18, demultiplexer_2_out19, demultiplexer_2_out20,
       demultiplexer_2_out21, demultiplexer_2_out22, demultiplexer_2_out23, demultiplexer_2_out24,
       demultiplexer_2_out25, demultiplexer_2_out26, demultiplexer_2_out27, demultiplexer_2_out28,
       demultiplexer_2_out29, demultiplexer_2_out30, demultiplexer_2_out31, multiplexer_3_out,
       multiplexer_4_out, pull_resistor_41_node, register_1_q, register_22_q, register_25_q, register_29_q,
       register_36_q, \попадание_1_out ;

  Clock #(.lowDuration(20)) clock_1 (.out(clock_1_out));
  Random #(.width(1)) random_1 (.clk(clock_1_out), .out(random_1_out));  // open: next, clr
  Random #(.width(2)) random_2 (.clk(clock_1_out), .out(Num1));  // open: next, clr
  or or_1 (or_1_out, transfer, wall);
  cdmEnemShoot cdmenemshoot_1 (
    .\rand (Num1), .shift(info), .En(clock_1_out), .out(coord), .\Частота_процессора (clk_t), .Ready(ready));
  D_Flip_Flop d_ff_1 (.Q(d_ff_1_q), .preset(or_1_out), .reset(clock_1_out));  // open: clk, D, Qn, en
  Subtractor subtractor_1 (.a(coord), .b(8'h1), .out(subtractor_1_out));  // open: bin, bout
  D_Flip_Flop d_ff_2 (.D(ready), .Q(d_ff_2_q), .preset(ready), .reset(d_ff_1_q));  // open: clk, Qn, en
  Multiplexer #(.width(8)) multiplexer_1 (
    .in0(coord), .in1(subtractor_1_out), .out({multiplexer_1_out, out_35}), .sel(random_1_out));  // open: en
  Demultiplexer #(.select(5), .enable("false")) demultiplexer_1 (
    .out0(demultiplexer_1_out0[0]), .out1(demultiplexer_1_out0[1]), .out2(demultiplexer_1_out0[2]),
    .out3(demultiplexer_1_out0[3]), .out4(demultiplexer_1_out0[4]), .out5(demultiplexer_1_out0[5]),
    .out6(demultiplexer_1_out0[6]), .out7(demultiplexer_1_out0[7]), .out8(demultiplexer_1_out0[8]),
    .out9(demultiplexer_1_out0[9]), .out10(demultiplexer_1_out0[10]), .out11(demultiplexer_1_out0[11]),
    .out12(demultiplexer_1_out0[12]), .out13(demultiplexer_1_out0[13]), .out14(demultiplexer_1_out0[14]),
    .out15(demultiplexer_1_out0[15]), .out16(demultiplexer_1_out0[16]), .out17(demultiplexer_1_out0[17]),
    .out18(demultiplexer_1_out0[18]), .out19(demultiplexer_1_out0[19]), .out20(demultiplexer_1_out0[20]),
    .out21(demultiplexer_1_out0[21]), .out22(demultiplexer_1_out0[22]), .out23(demultiplexer_1_out0[23]),
    .out24(demultiplexer_1_out0[24]), .out25(demultiplexer_1_out0[25]), .out26(demultiplexer_1_out0[26]),
    .out27(demultiplexer_1_out0[27]), .out28(demultiplexer_1_out0[28]), .out29(demultiplexer_1_out0[29]),
    .out30(demultiplexer_1_out0[30]), .out31(demultiplexer_1_out0[31]), .in(d_ff_2_q), .sel(out_35));
  Register #(.width(32)) register_1 (.D(demultiplexer_1_out0), .Q(register_1_q), .clk(d_ff_1_q));  // open: en, clr
  Clock #(.highDuration(20), .lowDuration(20)) clock_2 (.out(clock_2_out));
  Counter #(.width(5), .max('h1d)) counter_1 (
    .Q(counter_1_q), .carry(transfer), .clk(clock_2_out), .clr(d_ff_1_q));  // open: load, D, count
  Comparator #(.width(5), .mode("unsigned")) comparator_1 (
    .a(counter_1_q), .b({5{1'b0}}), .eq(comparator_1_eq));  // open: gt, lt
  Multiplexer #(.select(2)) multiplexer_2 (
    .in0(out[0]), .in1(out[1]), .in2(out[2]), .in3(out[3]), .out(multiplexer_2_out), .sel(Num1));  // open: en
  // Probe on height
  Adder #(.width(5)) adder_1 (.a(register_2_q), .b(counter_1_q), .out(height));  // open: cin, cout
  Register #(.width(5)) register_2 (
    .D(height_t), .en(comparator_1_eq), .Q(register_2_q), .clk(clock_2_out));  // open: clr
  Demultiplexer #(.select(5), .width(32)) demultiplexer_2 (
    .out0(demultiplexer_2_out0), .out1(demultiplexer_2_out1), .out2(demultiplexer_2_out2),
    .out3(demultiplexer_2_out3), .out4(demultiplexer_2_out4), .out5(demultiplexer_2_out5),
    .out6(demultiplexer_2_out6), .out7(demultiplexer_2_out7), .out8(demultiplexer_2_out8),
    .out9(demultiplexer_2_out9), .out10(demultiplexer_2_out10), .out11(demultiplexer_2_out11),
    .out12(demultiplexer_2_out12), .out13(demultiplexer_2_out13), .out14(demultiplexer_2_out14),
    .out15(demultiplexer_2_out15), .out16(demultiplexer_2_out16), .out17(demultiplexer_2_out17),
    .out18(demultiplexer_2_out18), .out19(demultiplexer_2_out19), .out20(demultiplexer_2_out20),
    .out21(demultiplexer_2_out21), .out22(demultiplexer_2_out22), .out23(demultiplexer_2_out23),
    .out24(demultiplexer_2_out24), .out25(demultiplexer_2_out25), .out26(demultiplexer_2_out26),
    .out27(demultiplexer_2_out27), .out28(demultiplexer_2_out28), .out29(demultiplexer_2_out29),
    .out30(demultiplexer_2_out30), .out31(demultiplexer_2_out31), .in(register_1_q), .sel(height),
    .en(multiplexer_2_out));
  assign _31f = comparator_2_gt ? demultiplexer_2_out0 : 32'bz;  // Controlled_Buffer controlled_buffer_1
  Pull_Resistor pull_resistor_1 (.node(_31f));
  assign _30f = comparator_2_gt ? demultiplexer_2_out1 : 32'bz;  // Controlled_Buffer controlled_buffer_2
  Pull_Resistor pull_resistor_2 (.node(_30f));
  assign _29f = comparator_2_gt ? demultiplexer_2_out2 : 32'bz;  // Controlled_Buffer controlled_buffer_3
  Pull_Resistor pull_resistor_3 (.node(_29f));
  Pull_Resistor pull_resistor_4 (.node(_28f));
  assign _28f = comparator_2_gt ? demultiplexer_2_out3 : 32'bz;  // Controlled_Buffer controlled_buffer_4
  assign _27f = comparator_2_gt ? demultiplexer_2_out4 : 32'bz;  // Controlled_Buffer controlled_buffer_5
  assign _26f = comparator_2_gt ? demultiplexer_2_out5 : 32'bz;  // Controlled_Buffer controlled_buffer_6
  assign _25f = comparator_2_gt ? demultiplexer_2_out6 : 32'bz;  // Controlled_Buffer controlled_buffer_7
  assign _24f = comparator_2_gt ? demultiplexer_2_out7 : 32'bz;  // Controlled_Buffer controlled_buffer_8
  assign _23f = comparator_2_gt ? demultiplexer_2_out8 : 32'bz;  // Controlled_Buffer controlled_buffer_9
  assign _22f = comparator_2_gt ? demultiplexer_2_out9 : 32'bz;  // Controlled_Buffer controlled_buffer_10
  assign _21f = comparator_2_gt ? demultiplexer_2_out10 : 32'bz;  // Controlled_Buffer controlled_buffer_11
  assign _20f = comparator_2_gt ? demultiplexer_2_out11 : 32'bz;  // Controlled_Buffer controlled_buffer_12
  assign _19f = comparator_2_gt ? demultiplexer_2_out12 : 32'bz;  // Controlled_Buffer controlled_buffer_13
  Pull_Resistor pull_resistor_5 (.node(_19f));
  assign _18f = comparator_2_gt ? demultiplexer_2_out13 : 32'bz;  // Controlled_Buffer controlled_buffer_14
  Pull_Resistor pull_resistor_6 (.node(_18f));
  Pull_Resistor pull_resistor_7 (.node(_17f));
  assign _17f = comparator_2_gt ? demultiplexer_2_out14 : 32'bz;  // Controlled_Buffer controlled_buffer_15
  assign _16f = comparator_2_gt ? demultiplexer_2_out15 : 32'bz;  // Controlled_Buffer controlled_buffer_16
  Pull_Resistor pull_resistor_8 (.node(_16f));
  assign _15f = comparator_2_gt ? demultiplexer_2_out16 : 32'bz;  // Controlled_Buffer controlled_buffer_17
  Pull_Resistor pull_resistor_9 (.node(_15f));
  assign _14f = comparator_2_gt ? demultiplexer_2_out17 : 32'bz;  // Controlled_Buffer controlled_buffer_18
  assign _13f = comparator_2_gt ? demultiplexer_2_out18 : 32'bz;  // Controlled_Buffer controlled_buffer_19
  assign _12f = comparator_2_gt ? demultiplexer_2_out19 : 32'bz;  // Controlled_Buffer controlled_buffer_20
  assign _11f = comparator_2_gt ? demultiplexer_2_out20 : 32'bz;  // Controlled_Buffer controlled_buffer_21
  assign _10f = comparator_2_gt ? demultiplexer_2_out21 : 32'bz;  // Controlled_Buffer controlled_buffer_22
  assign _9f = comparator_2_gt ? demultiplexer_2_out22 : 32'bz;  // Controlled_Buffer controlled_buffer_23
  assign _8f = comparator_2_gt ? demultiplexer_2_out23 : 32'bz;  // Controlled_Buffer controlled_buffer_24
  Pull_Resistor pull_resistor_10 (.node(_8f));
  Pull_Resistor pull_resistor_11 (.node(_7f));
  assign _7f = comparator_2_gt ? demultiplexer_2_out24 : 32'bz;  // Controlled_Buffer controlled_buffer_25
  assign _6f = comparator_2_gt ? demultiplexer_2_out25 : 32'bz;  // Controlled_Buffer controlled_buffer_26
  Pull_Resistor pull_resistor_12 (.node(_6f));
  Pull_Resistor pull_resistor_13 (.node(_5f));
  assign _5f = comparator_2_gt ? demultiplexer_2_out26 : 32'bz;  // Controlled_Buffer controlled_buffer_27
  Pull_Resistor pull_resistor_14 (.node(_4f));
  assign _4f = comparator_2_gt ? demultiplexer_2_out27 : 32'bz;  // Controlled_Buffer controlled_buffer_28
  assign _3f = comparator_2_gt ? demultiplexer_2_out28 : 32'bz;  // Controlled_Buffer controlled_buffer_29
  assign _2f = comparator_2_gt ? demultiplexer_2_out29 : 32'bz;  // Controlled_Buffer controlled_buffer_30
  assign out_52 = comparator_2_gt ? demultiplexer_2_out30 : 32'bz;  // Controlled_Buffer controlled_buffer_31
  assign out_48 = comparator_2_gt ? demultiplexer_2_out31 : 32'bz;  // Controlled_Buffer controlled_buffer_32
  Comparator #(.width(5), .mode("unsigned")) comparator_2 (
    .a(height), .b(register_2_q), .gt(comparator_2_gt));  // open: eq, lt
  Pull_Resistor pull_resistor_15 (.node(_27f));
  Pull_Resistor pull_resistor_16 (.node(_26f));
  Pull_Resistor pull_resistor_17 (.node(_25f));
  Pull_Resistor pull_resistor_18 (.node(_24f));
  Pull_Resistor pull_resistor_19 (.node(_23f));
  Pull_Resistor pull_resistor_20 (.node(_22f));
  Pull_Resistor pull_resistor_21 (.node(_21f));
  Pull_Resistor pull_resistor_22 (.node(_20f));
  Pull_Resistor pull_resistor_23 (.node(_14f));
  Pull_Resistor pull_resistor_24 (.node(_13f));
  Pull_Resistor pull_resistor_25 (.node(_12f));
  Pull_Resistor pull_resistor_26 (.node(_11f));
  Pull_Resistor pull_resistor_27 (.node(_10f));
  Pull_Resistor pull_resistor_28 (.node(_9f));
  Pull_Resistor pull_resistor_29 (.node(_3f));
  Pull_Resistor pull_resistor_30 (.node(_2f));
  Pull_Resistor pull_resistor_31 (.node(out_52));
  Pull_Resistor pull_resistor_32 (.node(out_48));
  Clock clock_3 (.out(clock_3_out));
  not not_1 (not_1_out, boom);
  assign init = not_1_out ? clock_3_out : 1'bz;  // Controlled_Buffer controlled_buffer_33
  D_Flip_Flop d_ff_3 (.clk(register_3_q), .D(register_3_q), .Q(boom), .reset(DONE));  // open: Qn, preset, en
  Register #(.width(1)) register_3 (.D(pull_resistor_33_node), .Q(register_3_q), .clk(clk));  // open: en, clr
  Pull_Resistor pull_resistor_33 (.node(pull_resistor_33_node));
  Register #(.width(32)) register_4 (
    .D(\попадание_1_out ), .en(pull_resistor_33_node), .Q({arr3, arr2, arr1, arr0}), .clk(clk));  // open: clr
  // Probe on Num
  not not_2 (not_2_out, initgame);
  \попадание  \u_попадание_1  (
    .OUT(\попадание_1_out ), .A(multiplexer_3_out), .B(multiplexer_4_out), .Trigger(\попадание_1_trigger ));
  Comparator #(.width(5), .mode("unsigned")) comparator_3 (
    .a(5'b00011), .b(inc5_1_r), .lt(comparator_3_lt));  // open: gt, eq
  assign controlled_buffer_34_out = comparator_3_lt ? \попадание_1_trigger  : 1'bz;  // Controlled_Buffer controlled_buffer_34
  buf buffer_1 (pull_resistor_33_node, controlled_buffer_34_out);
  assign enem = not_2_out ? {8{1'b1}} : 8'bz;  // Controlled_Buffer controlled_buffer_35
  assign {_1_prime_prime_prime, _2_prime_prime_prime, _3_prime_prime_prime, _4_prime_prime_prime, _11_prime_prime_prime, _12_prime_prime_prime, _13_prime_prime_prime, _14_prime_prime_prime} = ~out;  // NOT_Gate not_3, 8 bits wide
  inc5 inc5_1 (.X(Num), .R(inc5_1_r));  // open: Cout
  Multiplexer #(.select(5), .width(32), .enable("false")) multiplexer_3 (
    .in0({32{1'b0}}), .in1({32{1'b0}}), .in2(in_17), .in3(in_20), .in4(in_23), .in5(in_26), .in6(in_29),
    .in7(in_32), .in8(in_33), .in9(in_30), .in10(in_27), .in11(in_24), .in12(in_21), .in13(in_18),
    .in14(in_15), .in15(in_13), .in16(in_11), .in17(in_9), .in18(in_7), .in19(in_5), .in20(in_34),
    .in21(in_31), .in22(in_28), .in23(in_25), .in24(_24bul), .in25(in_19), .in26(in_16), .in27(in_14),
    .in28(in_12), .in29(in_10), .in30(in_8), .in31(in_6), .out(multiplexer_3_out), .sel(Num));
  Multiplexer #(.select(5), .width(32), .enable("false")) multiplexer_4 (
    .in0({32{1'b0}}), .in1({32{1'b0}}), .in2(_2e), .in3(_3e), .in4(out_51), .in5(_5e), .in6(_6e), .in7(_7e),
    .in8(_8e), .in9(_9e), .in10(_10e), .in11(_11e), .in12(_12e), .in13(_13e), .in14(_14e), .in15(_15e),
    .in16(_16e), .in17(_17e), .in18(_18e), .in19(_19e), .in20(_20e), .in21(_21e), .in22(_22e), .in23(_23e),
    .in24(_24e), .in25(_25e), .in26(_26e), .in27(_27e), .in28(_28e), .in29(_29e), .in30(_30e), .in31(_31e),
    .out(multiplexer_4_out), .sel(inc5_1_r));
  nor nor_1 (win, out[0], out[1], out[2], out[3], out[4], out[5], out[6], out[7]);
  and and_1 (I_O_sel, and_3_out, decoder_1_out1);
  and and_2 (and_2_out, boom, ~not_4_out, initgame);  // AND_Gate
  Clock \u_Частота_процессора  (.out(clk_t));
  D_Flip_Flop #(.trigger("falling")) d_ff_4 (
    .Q(d_ff_4_q), .preset(comparator_4_eq), .reset(d_ff_5_q));  // open: clk, D, Qn, en
  Comparator comparator_4 (.a(PC), .b(8'h8), .eq(comparator_4_eq));  // open: gt, lt
  D_Flip_Flop #(.trigger("falling")) d_ff_5 (.clk(clk_t), .D(and_2_out), .Q(d_ff_5_q));  // open: Qn, preset, en, reset
  and and_3 (and_3_out, addr[4], addr[5], addr[6], addr[7], decoder_1_out1);
  // Probe on cdm_8_mark5_1_r3
  // Probe on cdm_8_mark5_1_r1
  // Probe on cdm_8_mark5_1_r2
  // Probe on cdm_8_mark5_1_r0
  Multiplexer #(.enable("false")) multiplexer_5 (.in0(1'b0), .in1(clk_t), .out(multiplexer_5_out), .sel(not_4_out));
  and and_4 (and_4_out, decoder_1_out1, ~and_3_out);  // AND_Gate
  // Probe on cdm_8_mark5_1_sp
  // Probe on PC
  // Probe on cdm_8_mark5_1_ps
  CdM_8_mark5 cdm_8_mark5_1 (
    .clock(multiplexer_5_out), .addr(addr), .mem_read(r_w), .mem_cycle(cdm_8_mark5_1_mem_cycle),
    .data_inst(cdm_8_mark5_1_data_inst), .data_out(cdm_8_mark5_1_data_out),
    .data_in(controlled_buffer_37_out), .r0(cdm_8_mark5_1_r0), .r1(cdm_8_mark5_1_r1), .r2(cdm_8_mark5_1_r2),
    .r3(cdm_8_mark5_1_r3), .PC(PC), .SP(cdm_8_mark5_1_sp), .PS(cdm_8_mark5_1_ps));  // open: IAck, IRQ, vec, reset
  not not_4 (not_4_out, d_ff_4_q);
  assign out_38 = _31f | _31e;  // OR_Gate or_2, 32 bits wide
  assign out_40 = _30f | _30e;  // OR_Gate or_3, 32 bits wide
  assign out_43 = _29f | _29e;  // OR_Gate or_4, 32 bits wide
  assign out_45 = _28f | _28e;  // OR_Gate or_5, 32 bits wide
  assign out_47 = _27f | _27e;  // OR_Gate or_6, 32 bits wide
  assign out_50 = _26f | _26e;  // OR_Gate or_7, 32 bits wide
  assign out_54 = _25f | _25e;  // OR_Gate or_8, 32 bits wide
  assign out_57 = _24f | _24e;  // OR_Gate or_9, 32 bits wide
  assign out_60 = _23f | _23e;  // OR_Gate or_10, 32 bits wide
  assign out_63 = _22f | _22e;  // OR_Gate or_11, 32 bits wide
  assign out_67 = _21f | _21e;  // OR_Gate or_12, 32 bits wide
  assign out_70 = _20f | _20e;  // OR_Gate or_13, 32 bits wide
  assign out_37 = _19f | _19e;  // OR_Gate or_14, 32 bits wide
  assign out_39 = _18f | _18e;  // OR_Gate or_15, 32 bits wide
  assign out_42 = _17f | _17e;  // OR_Gate or_16, 32 bits wide
  assign out_44 = _16f | _16e;  // OR_Gate or_17, 32 bits wide
  assign out_46 = _15f | _15e;  // OR_Gate or_18, 32 bits wide
  assign out_49 = _14f | _14e;  // OR_Gate or_19, 32 bits wide
  assign out_53 = _13f | _13e;  // OR_Gate or_20, 32 bits wide
  assign out_56 = _12f | _12e;  // OR_Gate or_21, 32 bits wide
  assign out_59 = _11f | _11e;  // OR_Gate or_22, 32 bits wide
  assign out_62 = _10f | _10e;  // OR_Gate or_23, 32 bits wide
  assign out_66 = _9f | _9e;  // OR_Gate or_24, 32 bits wide
  assign out_69 = _8f | _8e;  // OR_Gate or_25, 32 bits wide
  assign out_71 = _7f | _7e;  // OR_Gate or_26, 32 bits wide
  assign out_68 = _6f | _6e;  // OR_Gate or_27, 32 bits wide
  assign out_64 = _5f | _5e;  // OR_Gate or_28, 32 bits wide
  assign out_61 = _4f | out_51;  // OR_Gate or_29, 32 bits wide
  assign out_58 = _3f | _3e;  // OR_Gate or_30, 32 bits wide
  assign out_55 = _2e | _2f;  // OR_Gate or_31, 32 bits wide
  Decoder #(.disabled(0)) decoder_1 (
    .out0(decoder_1_out0), .out1(decoder_1_out1), .sel(cdm_8_mark5_1_data_inst), .en(cdm_8_mark5_1_mem_cycle));
  not not_5 (not_5_out, r_w);
  assign io_data = not_5_out ? cdm_8_mark5_1_data_out : 8'bz;  // Controlled_Buffer controlled_buffer_36
  assign controlled_buffer_37_out = r_w ? io_data : 8'bz;  // Controlled_Buffer controlled_buffer_37
  // Probe on addr
  Register register_5 (.D(8'h18), .en(init), .Q(register_5_q), .clk(init), .clr(_1_prime_prime_prime));
  Register register_6 (.D(8'h18), .en(init), .Q(register_6_q), .clk(init), .clr(_11_prime_prime_prime));
  Register register_7 (.D(8'h18), .en(init), .Q(register_7_q), .clk(init), .clr(_2_prime_prime_prime));
  Register register_8 (.D(8'h18), .en(init), .Q(register_8_q), .clk(init), .clr(_12_prime_prime_prime));
  Register register_9 (.D(8'h24), .en(init), .Q(register_9_q), .clk(init), .clr(_4_prime_prime_prime));
  Register register_10 (.D(8'h24), .en(init), .Q(register_10_q), .clk(init), .clr(_3_prime_prime_prime));
  Register register_11 (.D(8'h24), .en(init), .Q(register_11_q), .clk(init), .clr(_2_prime_prime_prime));
  Register register_12 (.D(8'h24), .en(init), .Q(register_12_q), .clk(init), .clr(_1_prime_prime_prime));
  RAM ram_1 (.addr(addr), .data(io_data), .sel(and_4_out), .clk(clk_t), .ld(r_w), .clr(clr));
  ROM rom_1 (.addr(addr), .data(io_data), .sel(decoder_1_out0));
  Register register_13 (.D(8'h18), .en(init), .Q(register_13_q), .clk(init), .clr(_3_prime_prime_prime));
  Register register_14 (.D(8'h18), .en(init), .Q(register_14_q), .clk(init), .clr(_13_prime_prime_prime));
  // Probe on io_data
  Register register_15 (.D(8'h18), .en(init), .Q(register_15_q), .clk(init), .clr(_4_prime_prime_prime));
  Register register_16 (.D(8'h18), .en(init), .Q(register_16_q), .clk(init), .clr(_14_prime_prime_prime));
  Register register_17 (.D(8'h24), .en(init), .Q(register_17_q), .clk(init), .clr(_14_prime_prime_prime));
  Register register_18 (.D(8'h24), .en(init), .Q(register_18_q), .clk(init), .clr(_13_prime_prime_prime));
  Register register_19 (.D(8'h24), .en(init), .Q(register_19_q), .clk(init), .clr(_12_prime_prime_prime));
  Register register_20 (.D(8'h24), .en(init), .Q(register_20_q), .clk(init), .clr(_11_prime_prime_prime));
  Decoder decoder_2 (.out0(r), .out1(w), .sel(r_w), .en(I_O_sel));
  Pull_Resistor pull_resistor_34 (.node(r));
  Pull_Resistor pull_resistor_35 (.node(w));
  Register register_21 (.D(8'h5a), .en(init), .Q(register_22_q[7:0]), .clk(init), .clr(_14_prime_prime_prime));
  Register register_22 (.D(8'h24), .en(init), .Q(register_22_q[15:8]), .clk(init), .clr(_13_prime_prime_prime));
  Register register_23 (.D(8'h24), .en(init), .Q(register_22_q[23:16]), .clk(init), .clr(_12_prime_prime_prime));
  Register register_24 (.D(8'h5a), .en(init), .Q(register_22_q[31:24]), .clk(init), .clr(_11_prime_prime_prime));
  Clock #(.highDuration(180), .lowDuration(180)) \u_Частота_сдвигов  (.out(\Частота_сдвигов_out ));
  or or_32 (or_32_out, r, w);
  Decoder #(.select(4)) decoder_3 (
    .out0(decoder_3_out0), .out1(decoder_3_out1), .out2(decoder_3_out2), .out3(decoder_3_out3),
    .out4(decoder_3_out4), .sel(addr[3:0]), .en(or_32_out));  // open: out5, out6, out7, out8, out9, out10, out11, out12, out13, out14, out15
  Register register_25 (.D(8'h5a), .en(init), .Q(register_25_q[7:0]), .clk(init), .clr(_4_prime_prime_prime));
  Register register_26 (.D(8'h24), .en(init), .Q(register_25_q[15:8]), .clk(init), .clr(_3_prime_prime_prime));
  Register register_27 (.D(8'h24), .en(init), .Q(register_25_q[23:16]), .clk(init), .clr(_2_prime_prime_prime));
  Register register_28 (.D(8'h5a), .en(init), .Q(register_25_q[31:24]), .clk(init), .clr(_1_prime_prime_prime));
  not not_6 (not_6_out, boom);
  assign controlled_buffer_38_out = not_6_out ? \Частота_сдвигов_out  : 1'bz;  // Controlled_Buffer controlled_buffer_38
  assign controlled_buffer_39_out = r ? io_data : 8'bz;  // Controlled_Buffer controlled_buffer_39
  Pull_Resistor pull_resistor_36 (.node(decoder_3_out0));
  Pull_Resistor pull_resistor_37 (.node(decoder_3_out1));
  Pull_Resistor pull_resistor_38 (.node(decoder_3_out2));
  Pull_Resistor pull_resistor_39 (.node(decoder_3_out3));
  Demultiplexer #(.select(4), .width(8)) demultiplexer_3 (
    .out4(demultiplexer_3_out4), .in(controlled_buffer_39_out), .sel(addr[3:0]), .en(r));  // open: out0, out1, out2, out3, out5, out6, out7, out8, out9, out10, out11, out12, out13, out14, out15
  Pull_Resistor pull_resistor_40 (.node(decoder_3_out4));
  Register register_29 (.D(8'h24), .en(init), .Q(register_29_q[7:0]), .clk(init), .clr(_14_prime_prime_prime));
  Register register_30 (.D(8'h18), .en(init), .Q(register_29_q[15:8]), .clk(init), .clr(_13_prime_prime_prime));
  Register register_31 (.D(8'h18), .en(init), .Q(register_29_q[23:16]), .clk(init), .clr(_12_prime_prime_prime));
  Register register_32 (.D(8'h24), .en(init), .Q(register_29_q[31:24]), .clk(init), .clr(_11_prime_prime_prime));
  assign enem = r ? demultiplexer_3_out4 : 8'bz;  // Controlled_Buffer controlled_buffer_40
  assign io_data = w ? multiplexer_6_out : 8'bz;  // Controlled_Buffer controlled_buffer_41
  Multiplexer #(.select(4), .width(8)) multiplexer_6 (
    .in0(Oarr0), .in1(Oarr1), .in2(Oarr2), .in3(Oarr3), .in4(out), .out(multiplexer_6_out), .sel(addr[3:0]),
    .en(w));  // open: in5, in6, in7, in8, in9, in10, in11, in12, in13, in14, in15
  or or_33 (or_33_out, decoder_3_out0, boom);
  or or_34 (or_34_out, decoder_3_out1, boom);
  or or_35 (or_35_out, decoder_3_out2, boom);
  or or_36 (or_36_out, decoder_3_out3, boom);
  Counter #(.width(3), .max('h2)) counter_2 (
    .count(decoder_3_out4), .Q(counter_2_q), .clk(decoder_3_out4), .clr(not_7_out));  // open: load, D, carry
  not not_7 (not_7_out, boom);
  Register register_33 (.D(8'h24), .en(init), .Q(register_36_q[7:0]), .clk(init), .clr(_4_prime_prime_prime));
  Register register_34 (.D(8'h18), .en(init), .Q(register_36_q[15:8]), .clk(init), .clr(_3_prime_prime_prime));
  Register register_35 (.D(8'h18), .en(init), .Q(register_36_q[23:16]), .clk(init), .clr(_2_prime_prime_prime));
  Register register_36 (.D(8'h24), .en(init), .Q(register_36_q[31:24]), .clk(init), .clr(_1_prime_prime_prime));
  Pull_Resistor pull_resistor_41 (.node(pull_resistor_41_node));
  Register register_37 (.D(arr0), .en(or_33_out), .Q(Oarr0), .clk(clk_t));  // open: clr
  Register register_38 (.D(arr1), .en(or_34_out), .Q(Oarr1), .clk(clk_t));  // open: clr
  Register register_39 (.D(arr2), .en(or_35_out), .Q(Oarr2), .clk(clk_t));  // open: clr
  Register register_40 (.D(arr3), .en(or_36_out), .Q(Oarr3), .clk(clk_t));  // open: clr
  Register register_41 (.D(enem), .en(decoder_3_out4), .Q(out), .clk(clk_t));  // open: clr
  Comparator #(.width(3), .mode("unsigned")) comparator_5 (
    .a(counter_2_q), .b(3'b010), .eq(comparator_5_eq));  // open: gt, lt
  \сдвиги  \u_сдвиги_1  (
    .\Выход_2 (_2e), .\Вход_0 (register_36_q), .\Выход_3 (_3e), .in_2(register_25_q), .out_14(out_51),
    .in_3({register_5_q, register_7_q, register_13_q, register_15_q}), .out_15(_5e),
    .in_4({register_12_q, register_11_q, register_10_q, register_9_q}), .out_16(_6e),
    .in_5(pull_resistor_41_node), .\Выход_7 (_7e), .in_6(register_29_q), .out_18(_8e), .in_7(register_22_q),
    .out_19(_9e), .in_8({register_6_q, register_8_q, register_14_q, register_16_q}), .out_20(_10e),
    .in_9({register_20_q, register_19_q, register_18_q, register_17_q}), .out_21(_11e),
    .clock(controlled_buffer_38_out), .\Выход_12 (_12e), .out_23(_13e), .\Очистка__когда_0 (initgame),
    .out_24(_14e), .info(info), .out_26(_15e), .height(height_t), .\Выход_16 (_16e), .out_29(_17e),
    .out_30(_18e), .out_31(_19e), .out_32(_20e), .out_33(_21e), .out_34(_22e), .out_35(_23e), .out_36(_24e),
    .out_37(_25e), .out_38(_26e), .out_39(_27e), .out_40(_28e), .out_41(_29e), .out_42(_30e), .out_43(_31e));
  Register #(.width(1)) register_42 (
    .D(comparator_5_eq), .Q(DONE), .clk(comparator_5_eq), .clr(not_8_out));  // open: en
  not not_8 (not_8_out, boom);

  // Other names for the same wires on the sheet: _0[31:0] = out_48; _0f[31:0] = out_48; _1[31:0] = out_52;
  //   _1f[31:0] = out_52; _2[31:0] = out_55; _2bul[31:0] = in_17; _3[31:0] = out_58; _3bul[31:0] = in_20;
  //   _4[31:0] = out_61; _4bul[31:0] = in_23; _4e[31:0] = out_51; _5[31:0] = out_64; _5bul[31:0] = in_26;
  //   _6[31:0] = out_68; _6bul[31:0] = in_29; _7[31:0] = out_71; _7bul[31:0] = in_32; _8[31:0] = out_69;
  //   _8bul[31:0] = in_33; _9[31:0] = out_66; _9bul[31:0] = in_30; _10[31:0] = out_62; _10bul[31:0] = in_27;
  //   _11[31:0] = out_59; _11bul[31:0] = in_24; _12[31:0] = out_56; _12bul[31:0] = in_21; _13[31:0] = out_53;
  //   _13bul[31:0] = in_18; _14[31:0] = out_49; _14bul[31:0] = in_15; _15[31:0] = out_46; _15bul[31:0] = in_13;
  //   _16[31:0] = out_44; _16bul[31:0] = in_11; _17[31:0] = out_42; _17bul[31:0] = in_9; _18[31:0] = out_39;
  //   _18bul[31:0] = in_7; _19[31:0] = out_37; _19bul[31:0] = in_5; _20[31:0] = out_70; _20bul[31:0] = in_34;
  //   _21[31:0] = out_67; _21bul[31:0] = in_31; _22[31:0] = out_63; _22bul[31:0] = in_28; _23[31:0] = out_60;
  //   _23bul[31:0] = in_25; _24[31:0] = out_57; _25[31:0] = out_54; _25bul[31:0] = in_19; _26[31:0] = out_50;
  //   _26bul[31:0] = in_16; _27[31:0] = out_47; _27bul[31:0] = in_14; _28[31:0] = out_45; _28bul[31:0] = in_12;
  //   _29[31:0] = out_43; _29bul[31:0] = in_10; _30[31:0] = out_40; _30bul[31:0] = in_8; _31[31:0] = out_38;
  //   _31bul[31:0] = in_6; IOaddr[3:0] = addr[3:0]; gen = clk; Oenem[7:0] = out; res = wall; StartGame = initgame

  // Notes on the sheet:
  //   эта штука должна сделать невозможным стрельбу мертвого
  //   Сохранение строки для кода
  //   buffer_1 drives only 1 and floats otherwise
  //   Выключение пули
  //   contents of rom_1 (hex, n*v repeats v):
  //   c0 c4 c0 d1 ff d2 f4 a9 c4 d1 f0 d0 0 d2 3 7 a eb 1e bd 5 e0 19 ee 1e 8f 8c 8a ee 10 d1 1 d2 f4 ba 0
  //   e0 2a 25 88 ee 23 7 4b f e1 38 d0 4 0 e0 38 25 88 ee 31 66 d0 f4 a2 a e0 41 d6 8 d6 1 173*0 1 0 0 4
  //   ff
  //   запись в регитсры (st)
  //   чтение из регитров (ld)
  //   Указывает, завершилась ли обработка попадания
endmodule
module \сдвиги  (
  input  [31:0] \Вход_0 ,
  input  [31:0] in_2,
  input  [31:0] in_3,
  input  [31:0] in_4,
  input  [31:0] in_5,
  input  [31:0] in_6,
  input  [31:0] in_7,
  input  [31:0] in_8,
  input  [31:0] in_9,
  input  clock,
  input  \Очистка__когда_0 ,
  output [31:0] \Выход_2 ,
  output [31:0] \Выход_3 ,
  output [31:0] out_14,
  output [31:0] out_15,
  output [31:0] out_16,
  output [31:0] \Выход_7 ,
  output [31:0] out_18,
  output [31:0] out_19,
  output [31:0] out_20,
  output [31:0] out_21,
  output [31:0] \Выход_12 ,
  output [31:0] out_23,
  output [31:0] out_24,
  output [7:0] info,
  output [31:0] out_26,
  output [4:0] height,
  output [31:0] \Выход_16 ,
  output [31:0] out_29,
  output [31:0] out_30,
  output [31:0] out_31,
  output [31:0] out_32,
  output [31:0] out_33,
  output [31:0] out_34,
  output [31:0] out_35,
  output [31:0] out_36,
  output [31:0] out_37,
  output [31:0] out_38,
  output [31:0] out_39,
  output [31:0] out_40,
  output [31:0] out_41,
  output [31:0] out_42,
  output [31:0] out_43
);

  wire comparator_1_eq, comparator_2_eq, comparator_3_eq, comparator_4_eq, comparator_5_eq, comparator_6_eq,
       L, nor_1_out, or_1_out, or_2_out, or_3_out, R, START;
  wire [2:0] counter_1_q;
  wire [4:0] counter_2_q;
  wire [7:0] adder_1_out;
  wire [31:0] controlled_buffer_1_out, controlled_buffer_2_out, controlled_buffer_3_out,
       controlled_buffer_4_out, controlled_buffer_5_out, controlled_buffer_6_out, controlled_buffer_7_out,
       controlled_buffer_8_out, controlled_buffer_9_out, pull_resistor_2_node, shifterright_1_out_11,
       shifterright_1_out_12, shifterright_1_out_13, shifterright_1_out_14, shifterright_1_out_15,
       shifterright_1_out_16, shifterright_1_out_17, shifterright_1_out_18, shifterright_1_out_19,
       shifterright_2_out_11, shifterright_2_out_12, shifterright_2_out_13, shifterright_2_out_14,
       shifterright_2_out_15, shifterright_2_out_16, shifterright_2_out_17, shifterright_2_out_18,
       shifterright_2_out_19;

  Adder adder_1 (.a({{7{1'b0}}, R}), .b({8{1'b0}}), .out(adder_1_out));  // open: cin, cout
  Counter #(.width(3), .max('h5)) counter_1 (.Q(counter_1_q), .clk(clock), .clr(START));  // open: load, D, count, carry
  Subtractor subtractor_1 (.a(adder_1_out), .b({{7{1'b0}}, L}), .out(info));  // open: bin, bout
  Comparator #(.width(3)) comparator_1 (.a(counter_1_q), .b(3'b010), .eq(comparator_1_eq));  // open: gt, lt
  Comparator #(.width(3)) comparator_2 (.a(counter_1_q), .b(3'b101), .eq(comparator_2_eq));  // open: gt, lt
  Comparator #(.width(3)) comparator_3 (.a(counter_1_q), .b(3'b001), .eq(comparator_3_eq));  // open: gt, lt
  Comparator #(.width(3)) comparator_4 (.a(counter_1_q), .b(3'b011), .eq(comparator_4_eq));  // open: gt, lt
  Comparator #(.width(3)) comparator_5 (.a(counter_1_q), .b(3'b100), .eq(comparator_5_eq));  // open: gt, lt
  Comparator #(.width(3)) comparator_6 (.a(counter_1_q), .b(3'b000), .eq(comparator_6_eq));  // open: gt, lt
  Counter #(.width(5), .max('h1f)) counter_2 (
    .Q(counter_2_q), .clk(or_1_out), .clr(START));  // open: load, D, count, carry
  or or_1 (or_1_out, comparator_1_eq, comparator_2_eq);
  Counter #(.width(1), .max('h1)) counter_3 (.Q(L), .clk(or_2_out), .clr(START));  // open: load, D, count, carry
  or or_2 (or_2_out, comparator_3_eq, comparator_4_eq);
  Counter #(.width(1), .max('h1)) counter_4 (.Q(R), .clk(or_3_out), .clr(START));  // open: load, D, count, carry
  or or_3 (or_3_out, comparator_5_eq, comparator_6_eq);
  Adder #(.width(5)) adder_2 (.a(5'b00011), .b(counter_2_q), .out(height));  // open: cin, cout
  not not_1 (START, \Очистка__когда_0 );
  Pull_Resistor pull_resistor_1 (.node(\Очистка__когда_0 ));
  Pull_Resistor pull_resistor_2 (.node(pull_resistor_2_node));
  assign controlled_buffer_1_out = nor_1_out ? \Вход_0  : 32'bz;  // Controlled_Buffer controlled_buffer_1
  assign controlled_buffer_2_out = nor_1_out ? in_2 : 32'bz;  // Controlled_Buffer controlled_buffer_2
  assign controlled_buffer_3_out = nor_1_out ? in_3 : 32'bz;  // Controlled_Buffer controlled_buffer_3
  assign controlled_buffer_4_out = nor_1_out ? in_4 : 32'bz;  // Controlled_Buffer controlled_buffer_4
  assign controlled_buffer_5_out = nor_1_out ? in_5 : 32'bz;  // Controlled_Buffer controlled_buffer_5
  assign controlled_buffer_6_out = nor_1_out ? in_6 : 32'bz;  // Controlled_Buffer controlled_buffer_6
  assign controlled_buffer_7_out = nor_1_out ? in_7 : 32'bz;  // Controlled_Buffer controlled_buffer_7
  assign controlled_buffer_8_out = nor_1_out ? in_8 : 32'bz;  // Controlled_Buffer controlled_buffer_8
  assign controlled_buffer_9_out = nor_1_out ? in_9 : 32'bz;  // Controlled_Buffer controlled_buffer_9
  nor nor_1 (nor_1_out, L, R);
  assign controlled_buffer_1_out = R ? shifterright_1_out_11 : 32'bz;  // Controlled_Buffer controlled_buffer_10
  ShifterRight shifterright_1 (
    .\Вход_0 (\Вход_0 ), .out_11(shifterright_1_out_11), .in_2(in_2), .out_12(shifterright_1_out_12),
    .in_3(in_3), .out_13(shifterright_1_out_13), .in_4(in_4), .out_14(shifterright_1_out_14), .in_5(in_5),
    .out_15(shifterright_1_out_15), .in_6(in_6), .out_16(shifterright_1_out_16), .in_7(in_7),
    .out_17(shifterright_1_out_17), .in_8(in_8), .out_18(shifterright_1_out_18), .in_9(in_9),
    .out_19(shifterright_1_out_19), .in_10(R));
  assign controlled_buffer_2_out = R ? shifterright_1_out_12 : 32'bz;  // Controlled_Buffer controlled_buffer_11
  assign controlled_buffer_3_out = R ? shifterright_1_out_13 : 32'bz;  // Controlled_Buffer controlled_buffer_12
  assign controlled_buffer_4_out = R ? shifterright_1_out_14 : 32'bz;  // Controlled_Buffer controlled_buffer_13
  assign controlled_buffer_5_out = R ? shifterright_1_out_15 : 32'bz;  // Controlled_Buffer controlled_buffer_14
  assign controlled_buffer_6_out = R ? shifterright_1_out_16 : 32'bz;  // Controlled_Buffer controlled_buffer_15
  assign controlled_buffer_7_out = R ? shifterright_1_out_17 : 32'bz;  // Controlled_Buffer controlled_buffer_16
  assign controlled_buffer_8_out = R ? shifterright_1_out_18 : 32'bz;  // Controlled_Buffer controlled_buffer_17
  assign controlled_buffer_9_out = R ? shifterright_1_out_19 : 32'bz;  // Controlled_Buffer controlled_buffer_18
  ShifterRight shifterright_2 (
    .\Вход_0 (\Вход_0 ), .out_11(shifterright_2_out_11), .in_2(in_2), .out_12(shifterright_2_out_12),
    .in_3(in_3), .out_13(shifterright_2_out_13), .in_4(in_4), .out_14(shifterright_2_out_14), .in_5(in_5),
    .out_15(shifterright_2_out_15), .in_6(in_6), .out_16(shifterright_2_out_16), .in_7(in_7),
    .out_17(shifterright_2_out_17), .in_8(in_8), .out_18(shifterright_2_out_18), .in_9(in_9),
    .out_19(shifterright_2_out_19), .in_10(L));
  assign controlled_buffer_1_out = L ? shifterright_2_out_11 : 32'bz;  // Controlled_Buffer controlled_buffer_19
  assign controlled_buffer_2_out = L ? shifterright_2_out_12 : 32'bz;  // Controlled_Buffer controlled_buffer_20
  assign controlled_buffer_3_out = L ? shifterright_2_out_13 : 32'bz;  // Controlled_Buffer controlled_buffer_21
  assign controlled_buffer_4_out = L ? shifterright_2_out_14 : 32'bz;  // Controlled_Buffer controlled_buffer_22
  assign controlled_buffer_5_out = L ? shifterright_2_out_15 : 32'bz;  // Controlled_Buffer controlled_buffer_23
  assign controlled_buffer_6_out = L ? shifterright_2_out_16 : 32'bz;  // Controlled_Buffer controlled_buffer_24
  assign controlled_buffer_7_out = L ? shifterright_2_out_17 : 32'bz;  // Controlled_Buffer controlled_buffer_25
  assign controlled_buffer_8_out = L ? shifterright_2_out_18 : 32'bz;  // Controlled_Buffer controlled_buffer_26
  assign controlled_buffer_9_out = L ? shifterright_2_out_19 : 32'bz;  // Controlled_Buffer controlled_buffer_27
  shifterDown shifterdown_1 (
    .\Вход_0 (controlled_buffer_1_out), .\Выход_0 (out_43), .in_2(controlled_buffer_2_out), .out_36(out_42),
    .in_3(controlled_buffer_3_out), .out_37(out_41), .in_4(controlled_buffer_4_out), .out_38(out_40),
    .in_5(controlled_buffer_5_out), .out_39(out_39), .in_6(counter_2_q), .En(\Очистка__когда_0 ),
    .in_8(controlled_buffer_6_out), .out_40(out_38), .in_9(controlled_buffer_7_out), .out_41(out_37),
    .in_10(controlled_buffer_8_out), .out_42(out_36), .in_11(controlled_buffer_9_out), .out_43(out_35),
    .in_12(pull_resistor_2_node), .out_44(out_34), .in_13(pull_resistor_2_node), .out_45(out_33),
    .in_14(pull_resistor_2_node), .out_46(out_32), .in_15(pull_resistor_2_node), .out_47(out_31),
    .in_16(pull_resistor_2_node), .out_48(out_30), .in_17(pull_resistor_2_node), .out_49(out_29),
    .in_18(pull_resistor_2_node), .out_50(\Выход_16 ), .\Вход_16 (pull_resistor_2_node), .\Выход_16 (out_26),
    .in_20(pull_resistor_2_node), .out_52(out_24), .in_21(pull_resistor_2_node), .out_53(out_23),
    .in_22(pull_resistor_2_node), .out_54(\Выход_12 ), .in_23(pull_resistor_2_node), .out_55(out_21),
    .in_24(pull_resistor_2_node), .out_56(out_20), .in_25(pull_resistor_2_node), .out_57(out_19),
    .in_26(pull_resistor_2_node), .out_58(out_18), .in_27(pull_resistor_2_node), .out_59(\Выход_7 ),
    .in_28(pull_resistor_2_node), .out_60(out_16), .in_29(pull_resistor_2_node), .out_61(out_15),
    .in_30(pull_resistor_2_node), .out_62(out_14), .in_31(pull_resistor_2_node), .out_63(\Выход_3 ),
    .in_32(pull_resistor_2_node), .out_64(\Выход_2 ), .in_33(pull_resistor_2_node),
    .in_34(pull_resistor_2_node));  // open: out_65, out_66

  // Other names for the same wires on the sheet: _2e[31:0] = \Выход_2 ; _3e[31:0] = \Выход_3 ; _4e[31:0] = out_14;
  //   _5e[31:0] = out_15; _6e[31:0] = out_16; _7e[31:0] = \Выход_7 ; _8e[31:0] = out_18; _9e[31:0] = out_19;
  //   _10e[31:0] = out_20; _11e[31:0] = out_21; _12e[31:0] = \Выход_12 ; _13e[31:0] = out_23; _14e[31:0] = out_24;
  //   _15e[31:0] = out_26; _16e[31:0] = \Выход_16 ; _17e[31:0] = out_29; _18e[31:0] = out_30; _19e[31:0] = out_31;
  //   _20e[31:0] = out_32; _21e[31:0] = out_33; _22e[31:0] = out_34; _23e[31:0] = out_35; _24e[31:0] = out_36;
  //   _25e[31:0] = out_37; _26e[31:0] = out_38; _27e[31:0] = out_39; _28e[31:0] = out_40; _29e[31:0] = out_41;
  //   _30e[31:0] = out_42; _31e[31:0] = out_43; En = \Очистка__когда_0 ; Heght[4:0] = height

  // Notes on the sheet:
  //   V
  //   >
  //   <
endmodule

module shifterDown (
  input  [31:0] \Вход_0 ,
  input  [31:0] in_2,
  input  [31:0] in_3,
  input  [31:0] in_4,
  input  [31:0] in_5,
  input  [4:0] in_6,
  input  En,
  input  [31:0] in_8,
  input  [31:0] in_9,
  input  [31:0] in_10,
  input  [31:0] in_11,
  input  [31:0] in_12,
  input  [31:0] in_13,
  input  [31:0] in_14,
  input  [31:0] in_15,
  input  [31:0] in_16,
  input  [31:0] in_17,
  input  [31:0] in_18,
  input  [31:0] \Вход_16 ,
  input  [31:0] in_20,
  input  [31:0] in_21,
  input  [31:0] in_22,
  input  [31:0] in_23,
  input  [31:0] in_24,
  input  [31:0] in_25,
  input  [31:0] in_26,
  input  [31:0] in_27,
  input  [31:0] in_28,
  input  [31:0] in_29,
  input  [31:0] in_30,
  input  [31:0] in_31,
  input  [31:0] in_32,
  input  [31:0] in_33,
  input  [31:0] in_34,
  output [31:0] \Выход_0 ,
  output [31:0] out_36,
  output [31:0] out_37,
  output [31:0] out_38,
  output [31:0] out_39,
  output [31:0] out_40,
  output [31:0] out_41,
  output [31:0] out_42,
  output [31:0] out_43,
  output [31:0] out_44,
  output [31:0] out_45,
  output [31:0] out_46,
  output [31:0] out_47,
  output [31:0] out_48,
  output [31:0] out_49,
  output [31:0] out_50,
  output [31:0] \Выход_16 ,
  output [31:0] out_52,
  output [31:0] out_53,
  output [31:0] out_54,
  output [31:0] out_55,
  output [31:0] out_56,
  output [31:0] out_57,
  output [31:0] out_58,
  output [31:0] out_59,
  output [31:0] out_60,
  output [31:0] out_61,
  output [31:0] out_62,
  output [31:0] out_63,
  output [31:0] out_64,
  output [31:0] out_65,
  output [31:0] out_66
);

  wire not_1_out;
  wire [4:0] controlled_buffer_1_out, inc5_1_r, inc5_2_r, inc5_3_r, inc5_4_r, inc5_5_r, inc5_6_r, inc5_7_r,
       inc5_8_r, inc5_9_r, inc5_10_r, inc5_11_r, inc5_12_r, inc5_13_r, inc5_14_r, inc5_15_r, inc5_16_r,
       inc5_17_r, inc5_18_r, inc5_19_r, inc5_20_r, inc5_21_r, inc5_22_r, inc5_23_r, inc5_24_r, inc5_25_r,
       inc5_26_r, inc5_27_r, inc5_28_r, inc5_29_r, inc5_30_r, inc5_31_r;
  wire [31:0] demultiplexer_1_out0, demultiplexer_1_out1, demultiplexer_1_out2, demultiplexer_1_out3,
       demultiplexer_1_out4, demultiplexer_1_out5, demultiplexer_1_out6, demultiplexer_1_out7,
       demultiplexer_1_out8, demultiplexer_1_out9, demultiplexer_1_out10, demultiplexer_1_out11,
       demultiplexer_1_out12, demultiplexer_1_out13, demultiplexer_1_out14, demultiplexer_1_out15,
       demultiplexer_1_out16, demultiplexer_1_out17, demultiplexer_1_out18, demultiplexer_1_out19,
       demultiplexer_1_out20, demultiplexer_1_out21, demultiplexer_1_out22, demultiplexer_1_out23,
       demultiplexer_1_out24, demultiplexer_1_out25, demultiplexer_1_out26, demultiplexer_1_out27,
       demultiplexer_1_out28, demultiplexer_1_out29, demultiplexer_1_out30, demultiplexer_1_out31,
       demultiplexer_2_out4, demultiplexer_2_out5, demultiplexer_2_out6, demultiplexer_2_out7,
       demultiplexer_2_out8, demultiplexer_2_out9, demultiplexer_2_out10, demultiplexer_2_out11,
       demultiplexer_2_out12, demultiplexer_2_out13, demultiplexer_2_out14, demultiplexer_2_out15,
       demultiplexer_2_out16, demultiplexer_2_out17, demultiplexer_2_out18, demultiplexer_2_out19,
       demultiplexer_2_out20, demultiplexer_2_out21, demultiplexer_2_out22, demultiplexer_2_out23,
       demultiplexer_2_out24, demultiplexer_2_out25, demultiplexer_2_out26, demultiplexer_2_out27,
       demultiplexer_2_out28, demultiplexer_2_out29, demultiplexer_2_out30, demultiplexer_2_out31,
       demultiplexer_3_out8, demultiplexer_3_out9, demultiplexer_3_out10, demultiplexer_3_out11,
       demultiplexer_3_out12, demultiplexer_3_out13, demultiplexer_3_out14, demultiplexer_3_out15,
       demultiplexer_3_out16, demultiplexer_3_out17, demultiplexer_3_out18, demultiplexer_3_out19,
       demultiplexer_3_out20, demultiplexer_3_out21, demultiplexer_3_out22, demultiplexer_3_out23,
       demultiplexer_3_out24, demultiplexer_3_out25, demultiplexer_3_out26, demultiplexer_3_out27,
       demultiplexer_3_out28, demultiplexer_3_out29, demultiplexer_3_out30, demultiplexer_3_out31,
       demultiplexer_4_out12, demultiplexer_4_out13, demultiplexer_4_out14, demultiplexer_4_out15,
       demultiplexer_4_out16, demultiplexer_4_out17, demultiplexer_4_out18, demultiplexer_4_out19,
       demultiplexer_4_out20, demultiplexer_4_out21, demultiplexer_4_out22, demultiplexer_4_out23,
       demultiplexer_4_out24, demultiplexer_4_out25, demultiplexer_4_out26, demultiplexer_4_out27,
       demultiplexer_4_out28, demultiplexer_4_out29, demultiplexer_4_out30, demultiplexer_4_out31,
       demultiplexer_5_out1, demultiplexer_5_out2, demultiplexer_5_out3, demultiplexer_5_out4,
       demultiplexer_5_out5, demultiplexer_5_out6, demultiplexer_5_out7, demultiplexer_5_out8,
       demultiplexer_5_out9, demultiplexer_5_out10, demultiplexer_5_out11, demultiplexer_5_out12,
       demultiplexer_5_out13, demultiplexer_5_out14, demultiplexer_5_out15, demultiplexer_5_out16,
       demultiplexer_5_out17, demultiplexer_5_out18, demultiplexer_5_out19, demultiplexer_5_out20,
       demultiplexer_5_out21, demultiplexer_5_out22, demultiplexer_5_out23, demultiplexer_5_out24,
       demultiplexer_5_out25, demultiplexer_5_out26, demultiplexer_5_out27, demultiplexer_5_out28,
       demultiplexer_5_out29, demultiplexer_5_out30, demultiplexer_5_out31, demultiplexer_6_out5,
       demultiplexer_6_out6, demultiplexer_6_out7, demultiplexer_6_out8, demultiplexer_6_out9,
       demultiplexer_6_out10, demultiplexer_6_out11, demultiplexer_6_out12, demultiplexer_6_out13,
       demultiplexer_6_out14, demultiplexer_6_out15, demultiplexer_6_out16, demultiplexer_6_out17,
       demultiplexer_6_out18, demultiplexer_6_out19, demultiplexer_6_out20, demultiplexer_6_out21,
       demultiplexer_6_out22, demultiplexer_6_out23, demultiplexer_6_out24, demultiplexer_6_out25,
       demultiplexer_6_out26, demultiplexer_6_out27, demultiplexer_6_out28, demultiplexer_6_out29,
       demultiplexer_6_out30, demultiplexer_6_out31, demultiplexer_7_out9, demultiplexer_7_out10,
       demultiplexer_7_out11, demultiplexer_7_out12, demultiplexer_7_out13, demultiplexer_7_out14,
       demultiplexer_7_out15, demultiplexer_7_out16, demultiplexer_7_out17, demultiplexer_7_out18,
       demultiplexer_7_out19, demultiplexer_7_out20, demultiplexer_7_out21, demultiplexer_7_out22,
       demultiplexer_7_out23, demultiplexer_7_out24, demultiplexer_7_out25, demultiplexer_7_out26,
       demultiplexer_7_out27, demultiplexer_7_out28, demultiplexer_7_out29, demultiplexer_7_out30,
       demultiplexer_7_out31, demultiplexer_8_out13, demultiplexer_8_out14, demultiplexer_8_out15,
       demultiplexer_8_out16, demultiplexer_8_out17, demultiplexer_8_out18, demultiplexer_8_out19,
       demultiplexer_8_out20, demultiplexer_8_out21, demultiplexer_8_out22, demultiplexer_8_out23,
       demultiplexer_8_out24, demultiplexer_8_out25, demultiplexer_8_out26, demultiplexer_8_out27,
       demultiplexer_8_out28, demultiplexer_8_out29, demultiplexer_8_out30, demultiplexer_8_out31,
       demultiplexer_9_out2, demultiplexer_9_out3, demultiplexer_9_out4, demultiplexer_9_out5,
       demultiplexer_9_out6, demultiplexer_9_out7, demultiplexer_9_out8, demultiplexer_9_out9,
       demultiplexer_9_out10, demultiplexer_9_out11, demultiplexer_9_out12, demultiplexer_9_out13,
       demultiplexer_9_out14, demultiplexer_9_out15, demultiplexer_9_out16, demultiplexer_9_out17,
       demultiplexer_9_out18, demultiplexer_9_out19, demultiplexer_9_out20, demultiplexer_9_out21,
       demultiplexer_9_out22, demultiplexer_9_out23, demultiplexer_9_out24, demultiplexer_9_out25,
       demultiplexer_9_out26, demultiplexer_9_out27, demultiplexer_9_out28, demultiplexer_9_out29,
       demultiplexer_9_out30, demultiplexer_9_out31, demultiplexer_10_out6, demultiplexer_10_out7,
       demultiplexer_10_out8, demultiplexer_10_out9, demultiplexer_10_out10, demultiplexer_10_out11,
       demultiplexer_10_out12, demultiplexer_10_out13, demultiplexer_10_out14, demultiplexer_10_out15,
       demultiplexer_10_out16, demultiplexer_10_out17, demultiplexer_10_out18, demultiplexer_10_out19,
       demultiplexer_10_out20, demultiplexer_10_out21, demultiplexer_10_out22, demultiplexer_10_out23,
       demultiplexer_10_out24, demultiplexer_10_out25, demultiplexer_10_out26, demultiplexer_10_out27,
       demultiplexer_10_out28, demultiplexer_10_out29, demultiplexer_10_out30, demultiplexer_10_out31,
       demultiplexer_11_out10, demultiplexer_11_out11, demultiplexer_11_out12, demultiplexer_11_out13,
       demultiplexer_11_out14, demultiplexer_11_out15, demultiplexer_11_out16, demultiplexer_11_out17,
       demultiplexer_11_out18, demultiplexer_11_out19, demultiplexer_11_out20, demultiplexer_11_out21,
       demultiplexer_11_out22, demultiplexer_11_out23, demultiplexer_11_out24, demultiplexer_11_out25,
       demultiplexer_11_out26, demultiplexer_11_out27, demultiplexer_11_out28, demultiplexer_11_out29,
       demultiplexer_11_out30, demultiplexer_11_out31, demultiplexer_12_out14, demultiplexer_12_out15,
       demultiplexer_12_out16, demultiplexer_12_out17, demultiplexer_12_out18, demultiplexer_12_out19,
       demultiplexer_12_out20, demultiplexer_12_out21, demultiplexer_12_out22, demultiplexer_12_out23,
       demultiplexer_12_out24, demultiplexer_12_out25, demultiplexer_12_out26, demultiplexer_12_out27,
       demultiplexer_12_out28, demultiplexer_12_out29, demultiplexer_12_out30, demultiplexer_12_out31,
       demultiplexer_13_out3, demultiplexer_13_out4, demultiplexer_13_out5, demultiplexer_13_out6,
       demultiplexer_13_out7, demultiplexer_13_out8, demultiplexer_13_out9, demultiplexer_13_out10,
       demultiplexer_13_out11, demultiplexer_13_out12, demultiplexer_13_out13, demultiplexer_13_out14,
       demultiplexer_13_out15, demultiplexer_13_out16, demultiplexer_13_out17, demultiplexer_13_out18,
       demultiplexer_13_out19, demultiplexer_13_out20, demultiplexer_13_out21, demultiplexer_13_out22,
       demultiplexer_13_out23, demultiplexer_13_out24, demultiplexer_13_out25, demultiplexer_13_out26,
       demultiplexer_13_out27, demultiplexer_13_out28, demultiplexer_13_out29, demultiplexer_13_out30,
       demultiplexer_13_out31, demultiplexer_14_out7, demultiplexer_14_out8, demultiplexer_14_out9,
       demultiplexer_14_out10, demultiplexer_14_out11, demultiplexer_14_out12, demultiplexer_14_out13,
       demultiplexer_14_out14, demultiplexer_14_out15, demultiplexer_14_out16, demultiplexer_14_out17,
       demultiplexer_14_out18, demultiplexer_14_out19, demultiplexer_14_out20, demultiplexer_14_out21,
       demultiplexer_14_out22, demultiplexer_14_out23, demultiplexer_14_out24, demultiplexer_14_out25,
       demultiplexer_14_out26, demultiplexer_14_out27, demultiplexer_14_out28, demultiplexer_14_out29,
       demultiplexer_14_out30, demultiplexer_14_out31, demultiplexer_15_out11, demultiplexer_15_out12,
       demultiplexer_15_out13, demultiplexer_15_out14, demultiplexer_15_out15, demultiplexer_15_out16,
       demultiplexer_15_out17, demultiplexer_15_out18, demultiplexer_15_out19, demultiplexer_15_out20,
       demultiplexer_15_out21, demultiplexer_15_out22, demultiplexer_15_out23, demultiplexer_15_out24,
       demultiplexer_15_out25, demultiplexer_15_out26, demultiplexer_15_out27, demultiplexer_15_out28,
       demultiplexer_15_out29, demultiplexer_15_out30, demultiplexer_15_out31, demultiplexer_16_out15,
       demultiplexer_16_out16, demultiplexer_16_out17, demultiplexer_16_out18, demultiplexer_16_out19,
       demultiplexer_16_out20, demultiplexer_16_out21, demultiplexer_16_out22, demultiplexer_16_out23,
       demultiplexer_16_out24, demultiplexer_16_out25, demultiplexer_16_out26, demultiplexer_16_out27,
       demultiplexer_16_out28, demultiplexer_16_out29, demultiplexer_16_out30, demultiplexer_16_out31,
       demultiplexer_17_out16, demultiplexer_17_out17, demultiplexer_17_out18, demultiplexer_17_out19,
       demultiplexer_17_out20, demultiplexer_17_out21, demultiplexer_17_out22, demultiplexer_17_out23,
       demultiplexer_17_out24, demultiplexer_17_out25, demultiplexer_17_out26, demultiplexer_17_out27,
       demultiplexer_17_out28, demultiplexer_17_out29, demultiplexer_17_out30, demultiplexer_17_out31,
       demultiplexer_18_out20, demultiplexer_18_out21, demultiplexer_18_out22, demultiplexer_18_out23,
       demultiplexer_18_out24, demultiplexer_18_out25, demultiplexer_18_out26, demultiplexer_18_out27,
       demultiplexer_18_out28, demultiplexer_18_out29, demultiplexer_18_out30, demultiplexer_18_out31,
       demultiplexer_19_out24, demultiplexer_19_out25, demultiplexer_19_out26, demultiplexer_19_out27,
       demultiplexer_19_out28, demultiplexer_19_out29, demultiplexer_19_out30, demultiplexer_19_out31,
       demultiplexer_20_out28, demultiplexer_20_out29, demultiplexer_20_out30, demultiplexer_20_out31,
       demultiplexer_21_out21, demultiplexer_21_out22, demultiplexer_21_out23, demultiplexer_21_out24,
       demultiplexer_21_out25, demultiplexer_21_out26, demultiplexer_21_out27, demultiplexer_21_out28,
       demultiplexer_21_out29, demultiplexer_21_out30, demultiplexer_21_out31, demultiplexer_22_out25,
       demultiplexer_22_out26, demultiplexer_22_out27, demultiplexer_22_out28, demultiplexer_22_out29,
       demultiplexer_22_out30, demultiplexer_22_out31, demultiplexer_23_out29, demultiplexer_23_out30,
       demultiplexer_23_out31, demultiplexer_24_out17, demultiplexer_24_out18, demultiplexer_24_out19,
       demultiplexer_24_out20, demultiplexer_24_out21, demultiplexer_24_out22, demultiplexer_24_out23,
       demultiplexer_24_out24, demultiplexer_24_out25, demultiplexer_24_out26, demultiplexer_24_out27,
       demultiplexer_24_out28, demultiplexer_24_out29, demultiplexer_24_out30, demultiplexer_24_out31,
       demultiplexer_25_out18, demultiplexer_25_out19, demultiplexer_25_out20, demultiplexer_25_out21,
       demultiplexer_25_out22, demultiplexer_25_out23, demultiplexer_25_out24, demultiplexer_25_out25,
       demultiplexer_25_out26, demultiplexer_25_out27, demultiplexer_25_out28, demultiplexer_25_out29,
       demultiplexer_25_out30, demultiplexer_25_out31, demultiplexer_26_out22, demultiplexer_26_out23,
       demultiplexer_26_out24, demultiplexer_26_out25, demultiplexer_26_out26, demultiplexer_26_out27,
       demultiplexer_26_out28, demultiplexer_26_out29, demultiplexer_26_out30, demultiplexer_26_out31,
       demultiplexer_27_out26, demultiplexer_27_out27, demultiplexer_27_out28, demultiplexer_27_out29,
       demultiplexer_27_out30, demultiplexer_27_out31, demultiplexer_28_out30, demultiplexer_28_out31,
       demultiplexer_29_out19, demultiplexer_29_out20, demultiplexer_29_out21, demultiplexer_29_out22,
       demultiplexer_29_out23, demultiplexer_29_out24, demultiplexer_29_out25, demultiplexer_29_out26,
       demultiplexer_29_out27, demultiplexer_29_out28, demultiplexer_29_out29, demultiplexer_29_out30,
       demultiplexer_29_out31, demultiplexer_30_out23, demultiplexer_30_out24, demultiplexer_30_out25,
       demultiplexer_30_out26, demultiplexer_30_out27, demultiplexer_30_out28, demultiplexer_30_out29,
       demultiplexer_30_out30, demultiplexer_30_out31, demultiplexer_31_out27, demultiplexer_31_out28,
       demultiplexer_31_out29, demultiplexer_31_out30, demultiplexer_31_out31, demultiplexer_32_out31;

  Pull_Resistor pull_resistor_1 (.node(\Выход_0 ));
  Pull_Resistor pull_resistor_2 (.node(out_36));
  Pull_Resistor pull_resistor_3 (.node(out_37));
  Pull_Resistor pull_resistor_4 (.node(out_38));
  Pull_Resistor pull_resistor_5 (.node(out_39));
  Pull_Resistor pull_resistor_6 (.node(out_40));
  Pull_Resistor pull_resistor_7 (.node(out_41));
  Pull_Resistor pull_resistor_8 (.node(out_42));
  Pull_Resistor pull_resistor_9 (.node(out_43));
  Pull_Resistor pull_resistor_10 (.node(out_44));
  Pull_Resistor pull_resistor_11 (.node(out_45));
  Pull_Resistor pull_resistor_12 (.node(out_46));
  Pull_Resistor pull_resistor_13 (.node(out_47));
  Pull_Resistor pull_resistor_14 (.node(out_48));
  Pull_Resistor pull_resistor_15 (.node(out_49));
  Pull_Resistor pull_resistor_16 (.node(out_50));
  Pull_Resistor pull_resistor_17 (.node(\Выход_16 ));
  Pull_Resistor pull_resistor_18 (.node(out_52));
  Pull_Resistor pull_resistor_19 (.node(out_53));
  Pull_Resistor pull_resistor_20 (.node(out_54));
  Pull_Resistor pull_resistor_21 (.node(out_55));
  Pull_Resistor pull_resistor_22 (.node(out_56));
  Pull_Resistor pull_resistor_23 (.node(out_57));
  Pull_Resistor pull_resistor_24 (.node(out_58));
  Pull_Resistor pull_resistor_25 (.node(out_59));
  Pull_Resistor pull_resistor_26 (.node(out_60));
  Pull_Resistor pull_resistor_27 (.node(out_61));
  Pull_Resistor pull_resistor_28 (.node(out_62));
  Pull_Resistor pull_resistor_29 (.node(out_63));
  Pull_Resistor pull_resistor_30 (.node(out_64));
  Pull_Resistor pull_resistor_31 (.node(out_65));
  Pull_Resistor pull_resistor_32 (.node(out_66));
  assign controlled_buffer_1_out = En ? in_6 : 5'bz;  // Controlled_Buffer controlled_buffer_1
  not not_1 (not_1_out, En);
  assign controlled_buffer_1_out = not_1_out ? {5{1'b0}} : 5'bz;  // Controlled_Buffer controlled_buffer_2
  Demultiplexer #(.select(5), .width(32), .enable("false")) demultiplexer_1 (
    .out0(demultiplexer_1_out0), .out1(demultiplexer_1_out1), .out2(demultiplexer_1_out2),
    .out3(demultiplexer_1_out3), .out4(demultiplexer_1_out4), .out5(demultiplexer_1_out5),
    .out6(demultiplexer_1_out6), .out7(demultiplexer_1_out7), .out8(demultiplexer_1_out8),
    .out9(demultiplexer_1_out9), .out10(demultiplexer_1_out10), .out11(demultiplexer_1_out11),
    .out12(demultiplexer_1_out12), .out13(demultiplexer_1_out13), .out14(demultiplexer_1_out14),
    .out15(demultiplexer_1_out15), .out16(demultiplexer_1_out16), .out17(demultiplexer_1_out17),
    .out18(demultiplexer_1_out18), .out19(demultiplexer_1_out19), .out20(demultiplexer_1_out20),
    .out21(demultiplexer_1_out21), .out22(demultiplexer_1_out22), .out23(demultiplexer_1_out23),
    .out24(demultiplexer_1_out24), .out25(demultiplexer_1_out25), .out26(demultiplexer_1_out26),
    .out27(demultiplexer_1_out27), .out28(demultiplexer_1_out28), .out29(demultiplexer_1_out29),
    .out30(demultiplexer_1_out30), .out31(demultiplexer_1_out31), .in(\Вход_0 ), .sel(controlled_buffer_1_out));
  Demultiplexer #(.select(5), .width(32), .enable("false")) demultiplexer_2 (
    .out4(demultiplexer_2_out4), .out5(demultiplexer_2_out5), .out6(demultiplexer_2_out6),
    .out7(demultiplexer_2_out7), .out8(demultiplexer_2_out8), .out9(demultiplexer_2_out9),
    .out10(demultiplexer_2_out10), .out11(demultiplexer_2_out11), .out12(demultiplexer_2_out12),
    .out13(demultiplexer_2_out13), .out14(demultiplexer_2_out14), .out15(demultiplexer_2_out15),
    .out16(demultiplexer_2_out16), .out17(demultiplexer_2_out17), .out18(demultiplexer_2_out18),
    .out19(demultiplexer_2_out19), .out20(demultiplexer_2_out20), .out21(demultiplexer_2_out21),
    .out22(demultiplexer_2_out22), .out23(demultiplexer_2_out23), .out24(demultiplexer_2_out24),
    .out25(demultiplexer_2_out25), .out26(demultiplexer_2_out26), .out27(demultiplexer_2_out27),
    .out28(demultiplexer_2_out28), .out29(demultiplexer_2_out29), .out30(demultiplexer_2_out30),
    .out31(demultiplexer_2_out31), .in(in_5), .sel(inc5_1_r));  // open: out0, out1, out2, out3
  inc5 inc5_1 (.X(inc5_12_r), .R(inc5_1_r));  // open: Cout
  Demultiplexer #(.select(5), .width(32), .enable("false")) demultiplexer_3 (
    .out8(demultiplexer_3_out8), .out9(demultiplexer_3_out9), .out10(demultiplexer_3_out10),
    .out11(demultiplexer_3_out11), .out12(demultiplexer_3_out12), .out13(demultiplexer_3_out13),
    .out14(demultiplexer_3_out14), .out15(demultiplexer_3_out15), .out16(demultiplexer_3_out16),
    .out17(demultiplexer_3_out17), .out18(demultiplexer_3_out18), .out19(demultiplexer_3_out19),
    .out20(demultiplexer_3_out20), .out21(demultiplexer_3_out21), .out22(demultiplexer_3_out22),
    .out23(demultiplexer_3_out23), .out24(demultiplexer_3_out24), .out25(demultiplexer_3_out25),
    .out26(demultiplexer_3_out26), .out27(demultiplexer_3_out27), .out28(demultiplexer_3_out28),
    .out29(demultiplexer_3_out29), .out30(demultiplexer_3_out30), .out31(demultiplexer_3_out31), .in(in_11),
    .sel(inc5_2_r));  // open: out0, out1, out2, out3, out4, out5, out6, out7
  inc5 inc5_2 (.X(inc5_13_r), .R(inc5_2_r));  // open: Cout
  Demultiplexer #(.select(5), .width(32), .enable("false")) demultiplexer_4 (
    .out12(demultiplexer_4_out12), .out13(demultiplexer_4_out13), .out14(demultiplexer_4_out14),
    .out15(demultiplexer_4_out15), .out16(demultiplexer_4_out16), .out17(demultiplexer_4_out17),
    .out18(demultiplexer_4_out18), .out19(demultiplexer_4_out19), .out20(demultiplexer_4_out20),
    .out21(demultiplexer_4_out21), .out22(demultiplexer_4_out22), .out23(demultiplexer_4_out23),
    .out24(demultiplexer_4_out24), .out25(demultiplexer_4_out25), .out26(demultiplexer_4_out26),
    .out27(demultiplexer_4_out27), .out28(demultiplexer_4_out28), .out29(demultiplexer_4_out29),
    .out30(demultiplexer_4_out30), .out31(demultiplexer_4_out31), .in(in_15), .sel(inc5_3_r));  // open: out0, out1, out2, out3, out4, out5, out6, out7, out8, out9, out10, out11
  inc5 inc5_3 (.X(inc5_14_r), .R(inc5_3_r));  // open: Cout
  decodBufer decodbufer_1 (.in_1(demultiplexer_1_out0), .out_2(\Выход_0 ));
  decodBufer decodbufer_2 (.in_1(demultiplexer_1_out1), .out_2(out_36));
  decodBufer decodbufer_3 (.in_1(demultiplexer_1_out2), .out_2(out_37));
  decodBufer decodbufer_4 (.in_1(demultiplexer_1_out3), .out_2(out_38));
  decodBufer decodbufer_5 (.in_1(demultiplexer_1_out4), .out_2(out_39));
  decodBufer decodbufer_6 (.in_1(demultiplexer_1_out5), .out_2(out_40));
  decodBufer decodbufer_7 (.in_1(demultiplexer_1_out6), .out_2(out_41));
  decodBufer decodbufer_8 (.in_1(demultiplexer_1_out7), .out_2(out_42));
  decodBufer decodbufer_9 (.in_1(demultiplexer_1_out8), .out_2(out_43));
  decodBufer decodbufer_10 (.in_1(demultiplexer_1_out9), .out_2(out_44));
  decodBufer decodbufer_11 (.in_1(demultiplexer_1_out10), .out_2(out_45));
  decodBufer decodbufer_12 (.in_1(demultiplexer_1_out11), .out_2(out_46));
  decodBufer decodbufer_13 (.in_1(demultiplexer_1_out12), .out_2(out_47));
  decodBufer decodbufer_14 (.in_1(demultiplexer_1_out13), .out_2(out_48));
  decodBufer decodbufer_15 (.in_1(demultiplexer_1_out14), .out_2(out_49));
  decodBufer decodbufer_16 (.in_1(demultiplexer_1_out15), .out_2(out_50));
  decodBufer decodbufer_17 (.in_1(demultiplexer_1_out16), .out_2(\Выход_16 ));
  decodBufer decodbufer_18 (.in_1(demultiplexer_1_out17), .out_2(out_52));
  decodBufer decodbufer_19 (.in_1(demultiplexer_1_out18), .out_2(out_53));
  decodBufer decodbufer_20 (.in_1(demultiplexer_1_out19), .out_2(out_54));
  decodBufer decodbufer_21 (.in_1(demultiplexer_1_out20), .out_2(out_55));
  decodBufer decodbufer_22 (.in_1(demultiplexer_1_out21), .out_2(out_56));
  decodBufer decodbufer_23 (.in_1(demultiplexer_1_out22), .out_2(out_57));
  decodBufer decodbufer_24 (.in_1(demultiplexer_1_out23), .out_2(out_58));
  decodBufer decodbufer_25 (.in_1(demultiplexer_1_out24), .out_2(out_59));
  decodBufer decodbufer_26 (.in_1(demultiplexer_1_out25), .out_2(out_60));
  decodBufer decodbufer_27 (.in_1(demultiplexer_1_out26), .out_2(out_61));
  decodBufer decodbufer_28 (.in_1(demultiplexer_1_out27), .out_2(out_62));
  decodBufer decodbufer_29 (.in_1(demultiplexer_1_out28), .out_2(out_63));
  decodBufer decodbufer_30 (.in_1(demultiplexer_1_out29), .out_2(out_64));
  decodBufer decodbufer_31 (.in_1(demultiplexer_1_out30), .out_2(out_65));
  decodBufer decodbufer_32 (.in_1(demultiplexer_1_out31), .out_2(out_66));
  inc5 inc5_4 (.X(controlled_buffer_1_out), .R(inc5_4_r));  // open: Cout
  decodBufer decodbufer_33 (.in_1(demultiplexer_2_out4), .out_2(out_39));
  decodBufer decodbufer_34 (.in_1(demultiplexer_2_out5), .out_2(out_40));
  decodBufer decodbufer_35 (.in_1(demultiplexer_2_out6), .out_2(out_41));
  decodBufer decodbufer_36 (.in_1(demultiplexer_2_out7), .out_2(out_42));
  decodBufer decodbufer_37 (.in_1(demultiplexer_2_out8), .out_2(out_43));
  decodBufer decodbufer_38 (.in_1(demultiplexer_2_out9), .out_2(out_44));
  decodBufer decodbufer_39 (.in_1(demultiplexer_2_out10), .out_2(out_45));
  decodBufer decodbufer_40 (.in_1(demultiplexer_2_out11), .out_2(out_46));
  decodBufer decodbufer_41 (.in_1(demultiplexer_2_out12), .out_2(out_47));
  decodBufer decodbufer_42 (.in_1(demultiplexer_2_out13), .out_2(out_48));
  decodBufer decodbufer_43 (.in_1(demultiplexer_2_out14), .out_2(out_49));
  decodBufer decodbufer_44 (.in_1(demultiplexer_2_out15), .out_2(out_50));
  decodBufer decodbufer_45 (.in_1(demultiplexer_2_out16), .out_2(\Выход_16 ));
  decodBufer decodbufer_46 (.in_1(demultiplexer_2_out17), .out_2(out_52));
  decodBufer decodbufer_47 (.in_1(demultiplexer_2_out18), .out_2(out_53));
  decodBufer decodbufer_48 (.in_1(demultiplexer_2_out19), .out_2(out_54));
  decodBufer decodbufer_49 (.in_1(demultiplexer_2_out20), .out_2(out_55));
  decodBufer decodbufer_50 (.in_1(demultiplexer_2_out21), .out_2(out_56));
  decodBufer decodbufer_51 (.in_1(demultiplexer_2_out22), .out_2(out_57));
  decodBufer decodbufer_52 (.in_1(demultiplexer_2_out23), .out_2(out_58));
  decodBufer decodbufer_53 (.in_1(demultiplexer_2_out24), .out_2(out_59));
  decodBufer decodbufer_54 (.in_1(demultiplexer_2_out25), .out_2(out_60));
  decodBufer decodbufer_55 (.in_1(demultiplexer_2_out26), .out_2(out_61));
  decodBufer decodbufer_56 (.in_1(demultiplexer_2_out27), .out_2(out_62));
  decodBufer decodbufer_57 (.in_1(demultiplexer_2_out28), .out_2(out_63));
  decodBufer decodbufer_58 (.in_1(demultiplexer_2_out29), .out_2(out_64));
  decodBufer decodbufer_59 (.in_1(demultiplexer_2_out30), .out_2(out_65));
  decodBufer decodbufer_60 (.in_1(demultiplexer_2_out31), .out_2(out_66));
  inc5 inc5_5 (.X(inc5_1_r), .R(inc5_5_r));  // open: Cout
  decodBufer decodbufer_61 (.in_1(demultiplexer_3_out8), .out_2(out_43));
  decodBufer decodbufer_62 (.in_1(demultiplexer_3_out9), .out_2(out_44));
  decodBufer decodbufer_63 (.in_1(demultiplexer_3_out10), .out_2(out_45));
  decodBufer decodbufer_64 (.in_1(demultiplexer_3_out11), .out_2(out_46));
  decodBufer decodbufer_65 (.in_1(demultiplexer_3_out12), .out_2(out_47));
  decodBufer decodbufer_66 (.in_1(demultiplexer_3_out13), .out_2(out_48));
  decodBufer decodbufer_67 (.in_1(demultiplexer_3_out14), .out_2(out_49));
  decodBufer decodbufer_68 (.in_1(demultiplexer_3_out15), .out_2(out_50));
  decodBufer decodbufer_69 (.in_1(demultiplexer_3_out16), .out_2(\Выход_16 ));
  decodBufer decodbufer_70 (.in_1(demultiplexer_3_out17), .out_2(out_52));
  decodBufer decodbufer_71 (.in_1(demultiplexer_3_out18), .out_2(out_53));
  decodBufer decodbufer_72 (.in_1(demultiplexer_3_out19), .out_2(out_54));
  decodBufer decodbufer_73 (.in_1(demultiplexer_3_out20), .out_2(out_55));
  decodBufer decodbufer_74 (.in_1(demultiplexer_3_out21), .out_2(out_56));
  decodBufer decodbufer_75 (.in_1(demultiplexer_3_out22), .out_2(out_57));
  decodBufer decodbufer_76 (.in_1(demultiplexer_3_out23), .out_2(out_58));
  decodBufer decodbufer_77 (.in_1(demultiplexer_3_out24), .out_2(out_59));
  decodBufer decodbufer_78 (.in_1(demultiplexer_3_out25), .out_2(out_60));
  decodBufer decodbufer_79 (.in_1(demultiplexer_3_out26), .out_2(out_61));
  decodBufer decodbufer_80 (.in_1(demultiplexer_3_out27), .out_2(out_62));
  decodBufer decodbufer_81 (.in_1(demultiplexer_3_out28), .out_2(out_63));
  decodBufer decodbufer_82 (.in_1(demultiplexer_3_out29), .out_2(out_64));
  decodBufer decodbufer_83 (.in_1(demultiplexer_3_out30), .out_2(out_65));
  decodBufer decodbufer_84 (.in_1(demultiplexer_3_out31), .out_2(out_66));
  inc5 inc5_6 (.X(inc5_2_r), .R(inc5_6_r));  // open: Cout
  decodBufer decodbufer_85 (.in_1(demultiplexer_4_out12), .out_2(out_47));
  decodBufer decodbufer_86 (.in_1(demultiplexer_4_out13), .out_2(out_48));
  decodBufer decodbufer_87 (.in_1(demultiplexer_4_out14), .out_2(out_49));
  decodBufer decodbufer_88 (.in_1(demultiplexer_4_out15), .out_2(out_50));
  decodBufer decodbufer_89 (.in_1(demultiplexer_4_out16), .out_2(\Выход_16 ));
  decodBufer decodbufer_90 (.in_1(demultiplexer_4_out17), .out_2(out_52));
  decodBufer decodbufer_91 (.in_1(demultiplexer_4_out18), .out_2(out_53));
  decodBufer decodbufer_92 (.in_1(demultiplexer_4_out19), .out_2(out_54));
  decodBufer decodbufer_93 (.in_1(demultiplexer_4_out20), .out_2(out_55));
  decodBufer decodbufer_94 (.in_1(demultiplexer_4_out21), .out_2(out_56));
  decodBufer decodbufer_95 (.in_1(demultiplexer_4_out22), .out_2(out_57));
  decodBufer decodbufer_96 (.in_1(demultiplexer_4_out23), .out_2(out_58));
  decodBufer decodbufer_97 (.in_1(demultiplexer_4_out24), .out_2(out_59));
  decodBufer decodbufer_98 (.in_1(demultiplexer_4_out25), .out_2(out_60));
  decodBufer decodbufer_99 (.in_1(demultiplexer_4_out26), .out_2(out_61));
  decodBufer decodbufer_100 (.in_1(demultiplexer_4_out27), .out_2(out_62));
  decodBufer decodbufer_101 (.in_1(demultiplexer_4_out28), .out_2(out_63));
  decodBufer decodbufer_102 (.in_1(demultiplexer_4_out29), .out_2(out_64));
  decodBufer decodbufer_103 (.in_1(demultiplexer_4_out30), .out_2(out_65));
  decodBufer decodbufer_104 (.in_1(demultiplexer_4_out31), .out_2(out_66));
  inc5 inc5_7 (.X(inc5_3_r), .R(inc5_7_r));  // open: Cout
  Demultiplexer #(.select(5), .width(32), .enable("false")) demultiplexer_5 (
    .out1(demultiplexer_5_out1), .out2(demultiplexer_5_out2), .out3(demultiplexer_5_out3),
    .out4(demultiplexer_5_out4), .out5(demultiplexer_5_out5), .out6(demultiplexer_5_out6),
    .out7(demultiplexer_5_out7), .out8(demultiplexer_5_out8), .out9(demultiplexer_5_out9),
    .out10(demultiplexer_5_out10), .out11(demultiplexer_5_out11), .out12(demultiplexer_5_out12),
    .out13(demultiplexer_5_out13), .out14(demultiplexer_5_out14), .out15(demultiplexer_5_out15),
    .out16(demultiplexer_5_out16), .out17(demultiplexer_5_out17), .out18(demultiplexer_5_out18),
    .out19(demultiplexer_5_out19), .out20(demultiplexer_5_out20), .out21(demultiplexer_5_out21),
    .out22(demultiplexer_5_out22), .out23(demultiplexer_5_out23), .out24(demultiplexer_5_out24),
    .out25(demultiplexer_5_out25), .out26(demultiplexer_5_out26), .out27(demultiplexer_5_out27),
    .out28(demultiplexer_5_out28), .out29(demultiplexer_5_out29), .out30(demultiplexer_5_out30),
    .out31(demultiplexer_5_out31), .in(in_2), .sel(inc5_4_r));  // open: out0
  Demultiplexer #(.select(5), .width(32), .enable("false")) demultiplexer_6 (
    .out5(demultiplexer_6_out5), .out6(demultiplexer_6_out6), .out7(demultiplexer_6_out7),
    .out8(demultiplexer_6_out8), .out9(demultiplexer_6_out9), .out10(demultiplexer_6_out10),
    .out11(demultiplexer_6_out11), .out12(demultiplexer_6_out12), .out13(demultiplexer_6_out13),
    .out14(demultiplexer_6_out14), .out15(demultiplexer_6_out15), .out16(demultiplexer_6_out16),
    .out17(demultiplexer_6_out17), .out18(demultiplexer_6_out18), .out19(demultiplexer_6_out19),
    .out20(demultiplexer_6_out20), .out21(demultiplexer_6_out21), .out22(demultiplexer_6_out22),
    .out23(demultiplexer_6_out23), .out24(demultiplexer_6_out24), .out25(demultiplexer_6_out25),
    .out26(demultiplexer_6_out26), .out27(demultiplexer_6_out27), .out28(demultiplexer_6_out28),
    .out29(demultiplexer_6_out29), .out30(demultiplexer_6_out30), .out31(demultiplexer_6_out31), .in(in_8),
    .sel(inc5_5_r));  // open: out0, out1, out2, out3, out4
  Demultiplexer #(.select(5), .width(32), .enable("false")) demultiplexer_7 (
    .out9(demultiplexer_7_out9), .out10(demultiplexer_7_out10), .out11(demultiplexer_7_out11),
    .out12(demultiplexer_7_out12), .out13(demultiplexer_7_out13), .out14(demultiplexer_7_out14),
    .out15(demultiplexer_7_out15), .out16(demultiplexer_7_out16), .out17(demultiplexer_7_out17),
    .out18(demultiplexer_7_out18), .out19(demultiplexer_7_out19), .out20(demultiplexer_7_out20),
    .out21(demultiplexer_7_out21), .out22(demultiplexer_7_out22), .out23(demultiplexer_7_out23),
    .out24(demultiplexer_7_out24), .out25(demultiplexer_7_out25), .out26(demultiplexer_7_out26),
    .out27(demultiplexer_7_out27), .out28(demultiplexer_7_out28), .out29(demultiplexer_7_out29),
    .out30(demultiplexer_7_out30), .out31(demultiplexer_7_out31), .in(in_12), .sel(inc5_6_r));  // open: out0, out1, out2, out3, out4, out5, out6, out7, out8
  Demultiplexer #(.select(5), .width(32), .enable("false")) demultiplexer_8 (
    .out13(demultiplexer_8_out13), .out14(demultiplexer_8_out14), .out15(demultiplexer_8_out15),
    .out16(demultiplexer_8_out16), .out17(demultiplexer_8_out17), .out18(demultiplexer_8_out18),
    .out19(demultiplexer_8_out19), .out20(demultiplexer_8_out20), .out21(demultiplexer_8_out21),
    .out22(demultiplexer_8_out22), .out23(demultiplexer_8_out23), .out24(demultiplexer_8_out24),
    .out25(demultiplexer_8_out25), .out26(demultiplexer_8_out26), .out27(demultiplexer_8_out27),
    .out28(demultiplexer_8_out28), .out29(demultiplexer_8_out29), .out30(demultiplexer_8_out30),
    .out31(demultiplexer_8_out31), .in(in_16), .sel(inc5_7_r));  // open: out0, out1, out2, out3, out4, out5, out6, out7, out8, out9, out10, out11, out12
  decodBufer decodbufer_105 (.in_1(demultiplexer_5_out1), .out_2(out_36));
  decodBufer decodbufer_106 (.in_1(demultiplexer_5_out2), .out_2(out_37));
  decodBufer decodbufer_107 (.in_1(demultiplexer_5_out3), .out_2(out_38));
  decodBufer decodbufer_108 (.in_1(demultiplexer_5_out4), .out_2(out_39));
  decodBufer decodbufer_109 (.in_1(demultiplexer_5_out5), .out_2(out_40));
  decodBufer decodbufer_110 (.in_1(demultiplexer_5_out6), .out_2(out_41));
  decodBufer decodbufer_111 (.in_1(demultiplexer_5_out7), .out_2(out_42));
  decodBufer decodbufer_112 (.in_1(demultiplexer_5_out8), .out_2(out_43));
  decodBufer decodbufer_113 (.in_1(demultiplexer_5_out9), .out_2(out_44));
  decodBufer decodbufer_114 (.in_1(demultiplexer_5_out10), .out_2(out_45));
  decodBufer decodbufer_115 (.in_1(demultiplexer_5_out11), .out_2(out_46));
  decodBufer decodbufer_116 (.in_1(demultiplexer_5_out12), .out_2(out_47));
  decodBufer decodbufer_117 (.in_1(demultiplexer_5_out13), .out_2(out_48));
  decodBufer decodbufer_118 (.in_1(demultiplexer_5_out14), .out_2(out_49));
  decodBufer decodbufer_119 (.in_1(demultiplexer_5_out15), .out_2(out_50));
  decodBufer decodbufer_120 (.in_1(demultiplexer_5_out16), .out_2(\Выход_16 ));
  Demultiplexer #(.select(5), .width(32), .enable("false")) demultiplexer_9 (
    .out2(demultiplexer_9_out2), .out3(demultiplexer_9_out3), .out4(demultiplexer_9_out4),
    .out5(demultiplexer_9_out5), .out6(demultiplexer_9_out6), .out7(demultiplexer_9_out7),
    .out8(demultiplexer_9_out8), .out9(demultiplexer_9_out9), .out10(demultiplexer_9_out10),
    .out11(demultiplexer_9_out11), .out12(demultiplexer_9_out12), .out13(demultiplexer_9_out13),
    .out14(demultiplexer_9_out14), .out15(demultiplexer_9_out15), .out16(demultiplexer_9_out16),
    .out17(demultiplexer_9_out17), .out18(demultiplexer_9_out18), .out19(demultiplexer_9_out19),
    .out20(demultiplexer_9_out20), .out21(demultiplexer_9_out21), .out22(demultiplexer_9_out22),
    .out23(demultiplexer_9_out23), .out24(demultiplexer_9_out24), .out25(demultiplexer_9_out25),
    .out26(demultiplexer_9_out26), .out27(demultiplexer_9_out27), .out28(demultiplexer_9_out28),
    .out29(demultiplexer_9_out29), .out30(demultiplexer_9_out30), .out31(demultiplexer_9_out31), .in(in_3),
    .sel(inc5_8_r));  // open: out0, out1
  decodBufer decodbufer_121 (.in_1(demultiplexer_5_out17), .out_2(out_52));
  decodBufer decodbufer_122 (.in_1(demultiplexer_5_out18), .out_2(out_53));
  decodBufer decodbufer_123 (.in_1(demultiplexer_5_out19), .out_2(out_54));
  decodBufer decodbufer_124 (.in_1(demultiplexer_5_out20), .out_2(out_55));
  decodBufer decodbufer_125 (.in_1(demultiplexer_5_out21), .out_2(out_56));
  decodBufer decodbufer_126 (.in_1(demultiplexer_5_out22), .out_2(out_57));
  decodBufer decodbufer_127 (.in_1(demultiplexer_5_out23), .out_2(out_58));
  decodBufer decodbufer_128 (.in_1(demultiplexer_5_out24), .out_2(out_59));
  decodBufer decodbufer_129 (.in_1(demultiplexer_5_out25), .out_2(out_60));
  decodBufer decodbufer_130 (.in_1(demultiplexer_5_out26), .out_2(out_61));
  decodBufer decodbufer_131 (.in_1(demultiplexer_5_out27), .out_2(out_62));
  decodBufer decodbufer_132 (.in_1(demultiplexer_5_out28), .out_2(out_63));
  decodBufer decodbufer_133 (.in_1(demultiplexer_5_out29), .out_2(out_64));
  decodBufer decodbufer_134 (.in_1(demultiplexer_5_out30), .out_2(out_65));
  decodBufer decodbufer_135 (.in_1(demultiplexer_5_out31), .out_2(out_66));
  inc5 inc5_8 (.X(inc5_4_r), .R(inc5_8_r));  // open: Cout
  decodBufer decodbufer_136 (.in_1(demultiplexer_6_out5), .out_2(out_40));
  decodBufer decodbufer_137 (.in_1(demultiplexer_6_out6), .out_2(out_41));
  decodBufer decodbufer_138 (.in_1(demultiplexer_6_out7), .out_2(out_42));
  decodBufer decodbufer_139 (.in_1(demultiplexer_6_out8), .out_2(out_43));
  decodBufer decodbufer_140 (.in_1(demultiplexer_6_out9), .out_2(out_44));
  decodBufer decodbufer_141 (.in_1(demultiplexer_6_out10), .out_2(out_45));
  decodBufer decodbufer_142 (.in_1(demultiplexer_6_out11), .out_2(out_46));
  decodBufer decodbufer_143 (.in_1(demultiplexer_6_out12), .out_2(out_47));
  decodBufer decodbufer_144 (.in_1(demultiplexer_6_out13), .out_2(out_48));
  decodBufer decodbufer_145 (.in_1(demultiplexer_6_out14), .out_2(out_49));
  decodBufer decodbufer_146 (.in_1(demultiplexer_6_out15), .out_2(out_50));
  Demultiplexer #(.select(5), .width(32), .enable("false")) demultiplexer_10 (
    .out6(demultiplexer_10_out6), .out7(demultiplexer_10_out7), .out8(demultiplexer_10_out8),
    .out9(demultiplexer_10_out9), .out10(demultiplexer_10_out10), .out11(demultiplexer_10_out11),
    .out12(demultiplexer_10_out12), .out13(demultiplexer_10_out13), .out14(demultiplexer_10_out14),
    .out15(demultiplexer_10_out15), .out16(demultiplexer_10_out16), .out17(demultiplexer_10_out17),
    .out18(demultiplexer_10_out18), .out19(demultiplexer_10_out19), .out20(demultiplexer_10_out20),
    .out21(demultiplexer_10_out21), .out22(demultiplexer_10_out22), .out23(demultiplexer_10_out23),
    .out24(demultiplexer_10_out24), .out25(demultiplexer_10_out25), .out26(demultiplexer_10_out26),
    .out27(demultiplexer_10_out27), .out28(demultiplexer_10_out28), .out29(demultiplexer_10_out29),
    .out30(demultiplexer_10_out30), .out31(demultiplexer_10_out31), .in(in_9), .sel(inc5_9_r));  // open: out0, out1, out2, out3, out4, out5
  decodBufer decodbufer_147 (.in_1(demultiplexer_6_out16), .out_2(\Выход_16 ));
  decodBufer decodbufer_148 (.in_1(demultiplexer_6_out17), .out_2(out_52));
  decodBufer decodbufer_149 (.in_1(demultiplexer_6_out18), .out_2(out_53));
  decodBufer decodbufer_150 (.in_1(demultiplexer_6_out19), .out_2(out_54));
  decodBufer decodbufer_151 (.in_1(demultiplexer_6_out20), .out_2(out_55));
  decodBufer decodbufer_152 (.in_1(demultiplexer_6_out21), .out_2(out_56));
  decodBufer decodbufer_153 (.in_1(demultiplexer_6_out22), .out_2(out_57));
  decodBufer decodbufer_154 (.in_1(demultiplexer_6_out23), .out_2(out_58));
  decodBufer decodbufer_155 (.in_1(demultiplexer_6_out24), .out_2(out_59));
  decodBufer decodbufer_156 (.in_1(demultiplexer_6_out25), .out_2(out_60));
  decodBufer decodbufer_157 (.in_1(demultiplexer_6_out26), .out_2(out_61));
  decodBufer decodbufer_158 (.in_1(demultiplexer_6_out27), .out_2(out_62));
  decodBufer decodbufer_159 (.in_1(demultiplexer_6_out28), .out_2(out_63));
  decodBufer decodbufer_160 (.in_1(demultiplexer_6_out29), .out_2(out_64));
  decodBufer decodbufer_161 (.in_1(demultiplexer_6_out30), .out_2(out_65));
  decodBufer decodbufer_162 (.in_1(demultiplexer_6_out31), .out_2(out_66));
  inc5 inc5_9 (.X(inc5_5_r), .R(inc5_9_r));  // open: Cout
  decodBufer decodbufer_163 (.in_1(demultiplexer_7_out9), .out_2(out_44));
  decodBufer decodbufer_164 (.in_1(demultiplexer_7_out10), .out_2(out_45));
  decodBufer decodbufer_165 (.in_1(demultiplexer_7_out11), .out_2(out_46));
  decodBufer decodbufer_166 (.in_1(demultiplexer_7_out12), .out_2(out_47));
  decodBufer decodbufer_167 (.in_1(demultiplexer_7_out13), .out_2(out_48));
  decodBufer decodbufer_168 (.in_1(demultiplexer_7_out14), .out_2(out_49));
  decodBufer decodbufer_169 (.in_1(demultiplexer_7_out15), .out_2(out_50));
  Demultiplexer #(.select(5), .width(32), .enable("false")) demultiplexer_11 (
    .out10(demultiplexer_11_out10), .out11(demultiplexer_11_out11), .out12(demultiplexer_11_out12),
    .out13(demultiplexer_11_out13), .out14(demultiplexer_11_out14), .out15(demultiplexer_11_out15),
    .out16(demultiplexer_11_out16), .out17(demultiplexer_11_out17), .out18(demultiplexer_11_out18),
    .out19(demultiplexer_11_out19), .out20(demultiplexer_11_out20), .out21(demultiplexer_11_out21),
    .out22(demultiplexer_11_out22), .out23(demultiplexer_11_out23), .out24(demultiplexer_11_out24),
    .out25(demultiplexer_11_out25), .out26(demultiplexer_11_out26), .out27(demultiplexer_11_out27),
    .out28(demultiplexer_11_out28), .out29(demultiplexer_11_out29), .out30(demultiplexer_11_out30),
    .out31(demultiplexer_11_out31), .in(in_13), .sel(inc5_10_r));  // open: out0, out1, out2, out3, out4, out5, out6, out7, out8, out9
  decodBufer decodbufer_170 (.in_1(demultiplexer_7_out16), .out_2(\Выход_16 ));
  decodBufer decodbufer_171 (.in_1(demultiplexer_7_out17), .out_2(out_52));
  decodBufer decodbufer_172 (.in_1(demultiplexer_7_out18), .out_2(out_53));
  decodBufer decodbufer_173 (.in_1(demultiplexer_7_out19), .out_2(out_54));
  decodBufer decodbufer_174 (.in_1(demultiplexer_7_out20), .out_2(out_55));
  decodBufer decodbufer_175 (.in_1(demultiplexer_7_out21), .out_2(out_56));
  decodBufer decodbufer_176 (.in_1(demultiplexer_7_out22), .out_2(out_57));
  decodBufer decodbufer_177 (.in_1(demultiplexer_7_out23), .out_2(out_58));
  decodBufer decodbufer_178 (.in_1(demultiplexer_7_out24), .out_2(out_59));
  decodBufer decodbufer_179 (.in_1(demultiplexer_7_out25), .out_2(out_60));
  decodBufer decodbufer_180 (.in_1(demultiplexer_7_out26), .out_2(out_61));
  decodBufer decodbufer_181 (.in_1(demultiplexer_7_out27), .out_2(out_62));
  decodBufer decodbufer_182 (.in_1(demultiplexer_7_out28), .out_2(out_63));
  decodBufer decodbufer_183 (.in_1(demultiplexer_7_out29), .out_2(out_64));
  decodBufer decodbufer_184 (.in_1(demultiplexer_7_out30), .out_2(out_65));
  decodBufer decodbufer_185 (.in_1(demultiplexer_7_out31), .out_2(out_66));
  inc5 inc5_10 (.X(inc5_6_r), .R(inc5_10_r));  // open: Cout
  decodBufer decodbufer_186 (.in_1(demultiplexer_8_out13), .out_2(out_48));
  decodBufer decodbufer_187 (.in_1(demultiplexer_8_out14), .out_2(out_49));
  decodBufer decodbufer_188 (.in_1(demultiplexer_8_out15), .out_2(out_50));
  Demultiplexer #(.select(5), .width(32), .enable("false")) demultiplexer_12 (
    .out14(demultiplexer_12_out14), .out15(demultiplexer_12_out15), .out16(demultiplexer_12_out16),
    .out17(demultiplexer_12_out17), .out18(demultiplexer_12_out18), .out19(demultiplexer_12_out19),
    .out20(demultiplexer_12_out20), .out21(demultiplexer_12_out21), .out22(demultiplexer_12_out22),
    .out23(demultiplexer_12_out23), .out24(demultiplexer_12_out24), .out25(demultiplexer_12_out25),
    .out26(demultiplexer_12_out26), .out27(demultiplexer_12_out27), .out28(demultiplexer_12_out28),
    .out29(demultiplexer_12_out29), .out30(demultiplexer_12_out30), .out31(demultiplexer_12_out31),
    .in(in_17), .sel(inc5_11_r));  // open: out0, out1, out2, out3, out4, out5, out6, out7, out8, out9, out10, out11, out12, out13
  decodBufer decodbufer_189 (.in_1(demultiplexer_8_out16), .out_2(\Выход_16 ));
  decodBufer decodbufer_190 (.in_1(demultiplexer_8_out17), .out_2(out_52));
  decodBufer decodbufer_191 (.in_1(demultiplexer_8_out18), .out_2(out_53));
  decodBufer decodbufer_192 (.in_1(demultiplexer_8_out19), .out_2(out_54));
  decodBufer decodbufer_193 (.in_1(demultiplexer_8_out20), .out_2(out_55));
  decodBufer decodbufer_194 (.in_1(demultiplexer_8_out21), .out_2(out_56));
  decodBufer decodbufer_195 (.in_1(demultiplexer_8_out22), .out_2(out_57));
  decodBufer decodbufer_196 (.in_1(demultiplexer_8_out23), .out_2(out_58));
  decodBufer decodbufer_197 (.in_1(demultiplexer_8_out24), .out_2(out_59));
  decodBufer decodbufer_198 (.in_1(demultiplexer_8_out25), .out_2(out_60));
  decodBufer decodbufer_199 (.in_1(demultiplexer_8_out26), .out_2(out_61));
  decodBufer decodbufer_200 (.in_1(demultiplexer_8_out27), .out_2(out_62));
  decodBufer decodbufer_201 (.in_1(demultiplexer_8_out28), .out_2(out_63));
  decodBufer decodbufer_202 (.in_1(demultiplexer_8_out29), .out_2(out_64));
  decodBufer decodbufer_203 (.in_1(demultiplexer_8_out30), .out_2(out_65));
  decodBufer decodbufer_204 (.in_1(demultiplexer_8_out31), .out_2(out_66));
  inc5 inc5_11 (.X(inc5_7_r), .R(inc5_11_r));  // open: Cout
  decodBufer decodbufer_205 (.in_1(demultiplexer_9_out2), .out_2(out_37));
  decodBufer decodbufer_206 (.in_1(demultiplexer_9_out3), .out_2(out_38));
  decodBufer decodbufer_207 (.in_1(demultiplexer_9_out4), .out_2(out_39));
  decodBufer decodbufer_208 (.in_1(demultiplexer_9_out5), .out_2(out_40));
  decodBufer decodbufer_209 (.in_1(demultiplexer_9_out6), .out_2(out_41));
  decodBufer decodbufer_210 (.in_1(demultiplexer_9_out7), .out_2(out_42));
  decodBufer decodbufer_211 (.in_1(demultiplexer_9_out8), .out_2(out_43));
  decodBufer decodbufer_212 (.in_1(demultiplexer_9_out9), .out_2(out_44));
  decodBufer decodbufer_213 (.in_1(demultiplexer_9_out10), .out_2(out_45));
  decodBufer decodbufer_214 (.in_1(demultiplexer_9_out11), .out_2(out_46));
  decodBufer decodbufer_215 (.in_1(demultiplexer_9_out12), .out_2(out_47));
  decodBufer decodbufer_216 (.in_1(demultiplexer_9_out13), .out_2(out_48));
  decodBufer decodbufer_217 (.in_1(demultiplexer_9_out14), .out_2(out_49));
  decodBufer decodbufer_218 (.in_1(demultiplexer_9_out15), .out_2(out_50));
  decodBufer decodbufer_219 (.in_1(demultiplexer_9_out16), .out_2(\Выход_16 ));
  decodBufer decodbufer_220 (.in_1(demultiplexer_9_out17), .out_2(out_52));
  decodBufer decodbufer_221 (.in_1(demultiplexer_9_out18), .out_2(out_53));
  decodBufer decodbufer_222 (.in_1(demultiplexer_9_out19), .out_2(out_54));
  decodBufer decodbufer_223 (.in_1(demultiplexer_9_out20), .out_2(out_55));
  decodBufer decodbufer_224 (.in_1(demultiplexer_9_out21), .out_2(out_56));
  decodBufer decodbufer_225 (.in_1(demultiplexer_9_out22), .out_2(out_57));
  decodBufer decodbufer_226 (.in_1(demultiplexer_9_out23), .out_2(out_58));
  decodBufer decodbufer_227 (.in_1(demultiplexer_9_out24), .out_2(out_59));
  decodBufer decodbufer_228 (.in_1(demultiplexer_9_out25), .out_2(out_60));
  decodBufer decodbufer_229 (.in_1(demultiplexer_9_out26), .out_2(out_61));
  decodBufer decodbufer_230 (.in_1(demultiplexer_9_out27), .out_2(out_62));
  decodBufer decodbufer_231 (.in_1(demultiplexer_9_out28), .out_2(out_63));
  decodBufer decodbufer_232 (.in_1(demultiplexer_9_out29), .out_2(out_64));
  decodBufer decodbufer_233 (.in_1(demultiplexer_9_out30), .out_2(out_65));
  decodBufer decodbufer_234 (.in_1(demultiplexer_9_out31), .out_2(out_66));
  decodBufer decodbufer_235 (.in_1(demultiplexer_10_out6), .out_2(out_41));
  decodBufer decodbufer_236 (.in_1(demultiplexer_10_out7), .out_2(out_42));
  decodBufer decodbufer_237 (.in_1(demultiplexer_10_out8), .out_2(out_43));
  decodBufer decodbufer_238 (.in_1(demultiplexer_10_out9), .out_2(out_44));
  decodBufer decodbufer_239 (.in_1(demultiplexer_10_out10), .out_2(out_45));
  decodBufer decodbufer_240 (.in_1(demultiplexer_10_out11), .out_2(out_46));
  decodBufer decodbufer_241 (.in_1(demultiplexer_10_out12), .out_2(out_47));
  decodBufer decodbufer_242 (.in_1(demultiplexer_10_out13), .out_2(out_48));
  decodBufer decodbufer_243 (.in_1(demultiplexer_10_out14), .out_2(out_49));
  decodBufer decodbufer_244 (.in_1(demultiplexer_10_out15), .out_2(out_50));
  decodBufer decodbufer_245 (.in_1(demultiplexer_10_out16), .out_2(\Выход_16 ));
  decodBufer decodbufer_246 (.in_1(demultiplexer_10_out17), .out_2(out_52));
  decodBufer decodbufer_247 (.in_1(demultiplexer_10_out18), .out_2(out_53));
  decodBufer decodbufer_248 (.in_1(demultiplexer_10_out19), .out_2(out_54));
  decodBufer decodbufer_249 (.in_1(demultiplexer_10_out20), .out_2(out_55));
  decodBufer decodbufer_250 (.in_1(demultiplexer_10_out21), .out_2(out_56));
  decodBufer decodbufer_251 (.in_1(demultiplexer_10_out22), .out_2(out_57));
  decodBufer decodbufer_252 (.in_1(demultiplexer_10_out23), .out_2(out_58));
  decodBufer decodbufer_253 (.in_1(demultiplexer_10_out24), .out_2(out_59));
  decodBufer decodbufer_254 (.in_1(demultiplexer_10_out25), .out_2(out_60));
  decodBufer decodbufer_255 (.in_1(demultiplexer_10_out26), .out_2(out_61));
  decodBufer decodbufer_256 (.in_1(demultiplexer_10_out27), .out_2(out_62));
  decodBufer decodbufer_257 (.in_1(demultiplexer_10_out28), .out_2(out_63));
  decodBufer decodbufer_258 (.in_1(demultiplexer_10_out29), .out_2(out_64));
  decodBufer decodbufer_259 (.in_1(demultiplexer_10_out30), .out_2(out_65));
  decodBufer decodbufer_260 (.in_1(demultiplexer_10_out31), .out_2(out_66));
  decodBufer decodbufer_261 (.in_1(demultiplexer_11_out10), .out_2(out_45));
  decodBufer decodbufer_262 (.in_1(demultiplexer_11_out11), .out_2(out_46));
  decodBufer decodbufer_263 (.in_1(demultiplexer_11_out12), .out_2(out_47));
  decodBufer decodbufer_264 (.in_1(demultiplexer_11_out13), .out_2(out_48));
  decodBufer decodbufer_265 (.in_1(demultiplexer_11_out14), .out_2(out_49));
  decodBufer decodbufer_266 (.in_1(demultiplexer_11_out15), .out_2(out_50));
  decodBufer decodbufer_267 (.in_1(demultiplexer_11_out16), .out_2(\Выход_16 ));
  decodBufer decodbufer_268 (.in_1(demultiplexer_11_out17), .out_2(out_52));
  decodBufer decodbufer_269 (.in_1(demultiplexer_11_out18), .out_2(out_53));
  decodBufer decodbufer_270 (.in_1(demultiplexer_11_out19), .out_2(out_54));
  decodBufer decodbufer_271 (.in_1(demultiplexer_11_out20), .out_2(out_55));
  decodBufer decodbufer_272 (.in_1(demultiplexer_11_out21), .out_2(out_56));
  decodBufer decodbufer_273 (.in_1(demultiplexer_11_out22), .out_2(out_57));
  decodBufer decodbufer_274 (.in_1(demultiplexer_11_out23), .out_2(out_58));
  decodBufer decodbufer_275 (.in_1(demultiplexer_11_out24), .out_2(out_59));
  decodBufer decodbufer_276 (.in_1(demultiplexer_11_out25), .out_2(out_60));
  decodBufer decodbufer_277 (.in_1(demultiplexer_11_out26), .out_2(out_61));
  decodBufer decodbufer_278 (.in_1(demultiplexer_11_out27), .out_2(out_62));
  decodBufer decodbufer_279 (.in_1(demultiplexer_11_out28), .out_2(out_63));
  decodBufer decodbufer_280 (.in_1(demultiplexer_11_out29), .out_2(out_64));
  decodBufer decodbufer_281 (.in_1(demultiplexer_11_out30), .out_2(out_65));
  decodBufer decodbufer_282 (.in_1(demultiplexer_11_out31), .out_2(out_66));
  decodBufer decodbufer_283 (.in_1(demultiplexer_12_out14), .out_2(out_49));
  decodBufer decodbufer_284 (.in_1(demultiplexer_12_out15), .out_2(out_50));
  decodBufer decodbufer_285 (.in_1(demultiplexer_12_out16), .out_2(\Выход_16 ));
  decodBufer decodbufer_286 (.in_1(demultiplexer_12_out17), .out_2(out_52));
  decodBufer decodbufer_287 (.in_1(demultiplexer_12_out18), .out_2(out_53));
  decodBufer decodbufer_288 (.in_1(demultiplexer_12_out19), .out_2(out_54));
  decodBufer decodbufer_289 (.in_1(demultiplexer_12_out20), .out_2(out_55));
  decodBufer decodbufer_290 (.in_1(demultiplexer_12_out21), .out_2(out_56));
  decodBufer decodbufer_291 (.in_1(demultiplexer_12_out22), .out_2(out_57));
  decodBufer decodbufer_292 (.in_1(demultiplexer_12_out23), .out_2(out_58));
  decodBufer decodbufer_293 (.in_1(demultiplexer_12_out24), .out_2(out_59));
  decodBufer decodbufer_294 (.in_1(demultiplexer_12_out25), .out_2(out_60));
  decodBufer decodbufer_295 (.in_1(demultiplexer_12_out26), .out_2(out_61));
  decodBufer decodbufer_296 (.in_1(demultiplexer_12_out27), .out_2(out_62));
  decodBufer decodbufer_297 (.in_1(demultiplexer_12_out28), .out_2(out_63));
  decodBufer decodbufer_298 (.in_1(demultiplexer_12_out29), .out_2(out_64));
  decodBufer decodbufer_299 (.in_1(demultiplexer_12_out30), .out_2(out_65));
  decodBufer decodbufer_300 (.in_1(demultiplexer_12_out31), .out_2(out_66));
  Demultiplexer #(.select(5), .width(32), .enable("false")) demultiplexer_13 (
    .out3(demultiplexer_13_out3), .out4(demultiplexer_13_out4), .out5(demultiplexer_13_out5),
    .out6(demultiplexer_13_out6), .out7(demultiplexer_13_out7), .out8(demultiplexer_13_out8),
    .out9(demultiplexer_13_out9), .out10(demultiplexer_13_out10), .out11(demultiplexer_13_out11),
    .out12(demultiplexer_13_out12), .out13(demultiplexer_13_out13), .out14(demultiplexer_13_out14),
    .out15(demultiplexer_13_out15), .out16(demultiplexer_13_out16), .out17(demultiplexer_13_out17),
    .out18(demultiplexer_13_out18), .out19(demultiplexer_13_out19), .out20(demultiplexer_13_out20),
    .out21(demultiplexer_13_out21), .out22(demultiplexer_13_out22), .out23(demultiplexer_13_out23),
    .out24(demultiplexer_13_out24), .out25(demultiplexer_13_out25), .out26(demultiplexer_13_out26),
    .out27(demultiplexer_13_out27), .out28(demultiplexer_13_out28), .out29(demultiplexer_13_out29),
    .out30(demultiplexer_13_out30), .out31(demultiplexer_13_out31), .in(in_4), .sel(inc5_12_r));  // open: out0, out1, out2
  inc5 inc5_12 (.X(inc5_8_r), .R(inc5_12_r));  // open: Cout
  Demultiplexer #(.select(5), .width(32), .enable("false")) demultiplexer_14 (
    .out7(demultiplexer_14_out7), .out8(demultiplexer_14_out8), .out9(demultiplexer_14_out9),
    .out10(demultiplexer_14_out10), .out11(demultiplexer_14_out11), .out12(demultiplexer_14_out12),
    .out13(demultiplexer_14_out13), .out14(demultiplexer_14_out14), .out15(demultiplexer_14_out15),
    .out16(demultiplexer_14_out16), .out17(demultiplexer_14_out17), .out18(demultiplexer_14_out18),
    .out19(demultiplexer_14_out19), .out20(demultiplexer_14_out20), .out21(demultiplexer_14_out21),
    .out22(demultiplexer_14_out22), .out23(demultiplexer_14_out23), .out24(demultiplexer_14_out24),
    .out25(demultiplexer_14_out25), .out26(demultiplexer_14_out26), .out27(demultiplexer_14_out27),
    .out28(demultiplexer_14_out28), .out29(demultiplexer_14_out29), .out30(demultiplexer_14_out30),
    .out31(demultiplexer_14_out31), .in(in_10), .sel(inc5_13_r));  // open: out0, out1, out2, out3, out4, out5, out6
  inc5 inc5_13 (.X(inc5_9_r), .R(inc5_13_r));  // open: Cout
  Demultiplexer #(.select(5), .width(32), .enable("false")) demultiplexer_15 (
    .out11(demultiplexer_15_out11), .out12(demultiplexer_15_out12), .out13(demultiplexer_15_out13),
    .out14(demultiplexer_15_out14), .out15(demultiplexer_15_out15), .out16(demultiplexer_15_out16),
    .out17(demultiplexer_15_out17), .out18(demultiplexer_15_out18), .out19(demultiplexer_15_out19),
    .out20(demultiplexer_15_out20), .out21(demultiplexer_15_out21), .out22(demultiplexer_15_out22),
    .out23(demultiplexer_15_out23), .out24(demultiplexer_15_out24), .out25(demultiplexer_15_out25),
    .out26(demultiplexer_15_out26), .out27(demultiplexer_15_out27), .out28(demultiplexer_15_out28),
    .out29(demultiplexer_15_out29), .out30(demultiplexer_15_out30), .out31(demultiplexer_15_out31),
    .in(in_14), .sel(inc5_14_r));  // open: out0, out1, out2, out3, out4, out5, out6, out7, out8, out9, out10
  inc5 inc5_14 (.X(inc5_10_r), .R(inc5_14_r));  // open: Cout
  Demultiplexer #(.select(5), .width(32), .enable("false")) demultiplexer_16 (
    .out15(demultiplexer_16_out15), .out16(demultiplexer_16_out16), .out17(demultiplexer_16_out17),
    .out18(demultiplexer_16_out18), .out19(demultiplexer_16_out19), .out20(demultiplexer_16_out20),
    .out21(demultiplexer_16_out21), .out22(demultiplexer_16_out22), .out23(demultiplexer_16_out23),
    .out24(demultiplexer_16_out24), .out25(demultiplexer_16_out25), .out26(demultiplexer_16_out26),
    .out27(demultiplexer_16_out27), .out28(demultiplexer_16_out28), .out29(demultiplexer_16_out29),
    .out30(demultiplexer_16_out30), .out31(demultiplexer_16_out31), .in(in_18), .sel(inc5_15_r));  // open: out0, out1, out2, out3, out4, out5, out6, out7, out8, out9, out10, out11, out12, out13, out14
  inc5 inc5_15 (.X(inc5_11_r), .R(inc5_15_r));  // open: Cout
  decodBufer decodbufer_301 (.in_1(demultiplexer_13_out3), .out_2(out_38));
  decodBufer decodbufer_302 (.in_1(demultiplexer_13_out4), .out_2(out_39));
  decodBufer decodbufer_303 (.in_1(demultiplexer_13_out5), .out_2(out_40));
  decodBufer decodbufer_304 (.in_1(demultiplexer_13_out6), .out_2(out_41));
  decodBufer decodbufer_305 (.in_1(demultiplexer_13_out7), .out_2(out_42));
  decodBufer decodbufer_306 (.in_1(demultiplexer_13_out8), .out_2(out_43));
  decodBufer decodbufer_307 (.in_1(demultiplexer_13_out9), .out_2(out_44));
  decodBufer decodbufer_308 (.in_1(demultiplexer_13_out10), .out_2(out_45));
  decodBufer decodbufer_309 (.in_1(demultiplexer_13_out11), .out_2(out_46));
  decodBufer decodbufer_310 (.in_1(demultiplexer_13_out12), .out_2(out_47));
  decodBufer decodbufer_311 (.in_1(demultiplexer_13_out13), .out_2(out_48));
  decodBufer decodbufer_312 (.in_1(demultiplexer_13_out14), .out_2(out_49));
  decodBufer decodbufer_313 (.in_1(demultiplexer_13_out15), .out_2(out_50));
  decodBufer decodbufer_314 (.in_1(demultiplexer_13_out16), .out_2(\Выход_16 ));
  decodBufer decodbufer_315 (.in_1(demultiplexer_13_out17), .out_2(out_52));
  decodBufer decodbufer_316 (.in_1(demultiplexer_13_out18), .out_2(out_53));
  decodBufer decodbufer_317 (.in_1(demultiplexer_13_out19), .out_2(out_54));
  decodBufer decodbufer_318 (.in_1(demultiplexer_13_out20), .out_2(out_55));
  decodBufer decodbufer_319 (.in_1(demultiplexer_13_out21), .out_2(out_56));
  decodBufer decodbufer_320 (.in_1(demultiplexer_13_out22), .out_2(out_57));
  decodBufer decodbufer_321 (.in_1(demultiplexer_13_out23), .out_2(out_58));
  decodBufer decodbufer_322 (.in_1(demultiplexer_13_out24), .out_2(out_59));
  decodBufer decodbufer_323 (.in_1(demultiplexer_13_out25), .out_2(out_60));
  decodBufer decodbufer_324 (.in_1(demultiplexer_13_out26), .out_2(out_61));
  decodBufer decodbufer_325 (.in_1(demultiplexer_13_out27), .out_2(out_62));
  decodBufer decodbufer_326 (.in_1(demultiplexer_13_out28), .out_2(out_63));
  decodBufer decodbufer_327 (.in_1(demultiplexer_13_out29), .out_2(out_64));
  decodBufer decodbufer_328 (.in_1(demultiplexer_13_out30), .out_2(out_65));
  decodBufer decodbufer_329 (.in_1(demultiplexer_13_out31), .out_2(out_66));
  decodBufer decodbufer_330 (.in_1(demultiplexer_14_out7), .out_2(out_42));
  decodBufer decodbufer_331 (.in_1(demultiplexer_14_out8), .out_2(out_43));
  decodBufer decodbufer_332 (.in_1(demultiplexer_14_out9), .out_2(out_44));
  decodBufer decodbufer_333 (.in_1(demultiplexer_14_out10), .out_2(out_45));
  decodBufer decodbufer_334 (.in_1(demultiplexer_14_out11), .out_2(out_46));
  decodBufer decodbufer_335 (.in_1(demultiplexer_14_out12), .out_2(out_47));
  decodBufer decodbufer_336 (.in_1(demultiplexer_14_out13), .out_2(out_48));
  decodBufer decodbufer_337 (.in_1(demultiplexer_14_out14), .out_2(out_49));
  decodBufer decodbufer_338 (.in_1(demultiplexer_14_out15), .out_2(out_50));
  decodBufer decodbufer_339 (.in_1(demultiplexer_14_out16), .out_2(\Выход_16 ));
  decodBufer decodbufer_340 (.in_1(demultiplexer_14_out17), .out_2(out_52));
  decodBufer decodbufer_341 (.in_1(demultiplexer_14_out18), .out_2(out_53));
  decodBufer decodbufer_342 (.in_1(demultiplexer_14_out19), .out_2(out_54));
  decodBufer decodbufer_343 (.in_1(demultiplexer_14_out20), .out_2(out_55));
  decodBufer decodbufer_344 (.in_1(demultiplexer_14_out21), .out_2(out_56));
  decodBufer decodbufer_345 (.in_1(demultiplexer_14_out22), .out_2(out_57));
  decodBufer decodbufer_346 (.in_1(demultiplexer_14_out23), .out_2(out_58));
  decodBufer decodbufer_347 (.in_1(demultiplexer_14_out24), .out_2(out_59));
  decodBufer decodbufer_348 (.in_1(demultiplexer_14_out25), .out_2(out_60));
  decodBufer decodbufer_349 (.in_1(demultiplexer_14_out26), .out_2(out_61));
  decodBufer decodbufer_350 (.in_1(demultiplexer_14_out27), .out_2(out_62));
  decodBufer decodbufer_351 (.in_1(demultiplexer_14_out28), .out_2(out_63));
  decodBufer decodbufer_352 (.in_1(demultiplexer_14_out29), .out_2(out_64));
  decodBufer decodbufer_353 (.in_1(demultiplexer_14_out30), .out_2(out_65));
  decodBufer decodbufer_354 (.in_1(demultiplexer_14_out31), .out_2(out_66));
  decodBufer decodbufer_355 (.in_1(demultiplexer_15_out11), .out_2(out_46));
  decodBufer decodbufer_356 (.in_1(demultiplexer_15_out12), .out_2(out_47));
  decodBufer decodbufer_357 (.in_1(demultiplexer_15_out13), .out_2(out_48));
  decodBufer decodbufer_358 (.in_1(demultiplexer_15_out14), .out_2(out_49));
  decodBufer decodbufer_359 (.in_1(demultiplexer_15_out15), .out_2(out_50));
  decodBufer decodbufer_360 (.in_1(demultiplexer_15_out16), .out_2(\Выход_16 ));
  decodBufer decodbufer_361 (.in_1(demultiplexer_15_out17), .out_2(out_52));
  decodBufer decodbufer_362 (.in_1(demultiplexer_15_out18), .out_2(out_53));
  decodBufer decodbufer_363 (.in_1(demultiplexer_15_out19), .out_2(out_54));
  decodBufer decodbufer_364 (.in_1(demultiplexer_15_out20), .out_2(out_55));
  decodBufer decodbufer_365 (.in_1(demultiplexer_15_out21), .out_2(out_56));
  decodBufer decodbufer_366 (.in_1(demultiplexer_15_out22), .out_2(out_57));
  decodBufer decodbufer_367 (.in_1(demultiplexer_15_out23), .out_2(out_58));
  decodBufer decodbufer_368 (.in_1(demultiplexer_15_out24), .out_2(out_59));
  decodBufer decodbufer_369 (.in_1(demultiplexer_15_out25), .out_2(out_60));
  decodBufer decodbufer_370 (.in_1(demultiplexer_15_out26), .out_2(out_61));
  decodBufer decodbufer_371 (.in_1(demultiplexer_15_out27), .out_2(out_62));
  decodBufer decodbufer_372 (.in_1(demultiplexer_15_out28), .out_2(out_63));
  decodBufer decodbufer_373 (.in_1(demultiplexer_15_out29), .out_2(out_64));
  decodBufer decodbufer_374 (.in_1(demultiplexer_15_out30), .out_2(out_65));
  decodBufer decodbufer_375 (.in_1(demultiplexer_15_out31), .out_2(out_66));
  decodBufer decodbufer_376 (.in_1(demultiplexer_16_out15), .out_2(out_50));
  decodBufer decodbufer_377 (.in_1(demultiplexer_16_out16), .out_2(\Выход_16 ));
  decodBufer decodbufer_378 (.in_1(demultiplexer_16_out17), .out_2(out_52));
  decodBufer decodbufer_379 (.in_1(demultiplexer_16_out18), .out_2(out_53));
  decodBufer decodbufer_380 (.in_1(demultiplexer_16_out19), .out_2(out_54));
  decodBufer decodbufer_381 (.in_1(demultiplexer_16_out20), .out_2(out_55));
  decodBufer decodbufer_382 (.in_1(demultiplexer_16_out21), .out_2(out_56));
  decodBufer decodbufer_383 (.in_1(demultiplexer_16_out22), .out_2(out_57));
  decodBufer decodbufer_384 (.in_1(demultiplexer_16_out23), .out_2(out_58));
  decodBufer decodbufer_385 (.in_1(demultiplexer_16_out24), .out_2(out_59));
  decodBufer decodbufer_386 (.in_1(demultiplexer_16_out25), .out_2(out_60));
  decodBufer decodbufer_387 (.in_1(demultiplexer_16_out26), .out_2(out_61));
  decodBufer decodbufer_388 (.in_1(demultiplexer_16_out27), .out_2(out_62));
  decodBufer decodbufer_389 (.in_1(demultiplexer_16_out28), .out_2(out_63));
  decodBufer decodbufer_390 (.in_1(demultiplexer_16_out29), .out_2(out_64));
  decodBufer decodbufer_391 (.in_1(demultiplexer_16_out30), .out_2(out_65));
  decodBufer decodbufer_392 (.in_1(demultiplexer_16_out31), .out_2(out_66));
  Demultiplexer #(.select(5), .width(32), .enable("false")) demultiplexer_17 (
    .out16(demultiplexer_17_out16), .out17(demultiplexer_17_out17), .out18(demultiplexer_17_out18),
    .out19(demultiplexer_17_out19), .out20(demultiplexer_17_out20), .out21(demultiplexer_17_out21),
    .out22(demultiplexer_17_out22), .out23(demultiplexer_17_out23), .out24(demultiplexer_17_out24),
    .out25(demultiplexer_17_out25), .out26(demultiplexer_17_out26), .out27(demultiplexer_17_out27),
    .out28(demultiplexer_17_out28), .out29(demultiplexer_17_out29), .out30(demultiplexer_17_out30),
    .out31(demultiplexer_17_out31), .in(\Вход_16 ), .sel(inc5_16_r));  // open: out0, out1, out2, out3, out4, out5, out6, out7, out8, out9, out10, out11, out12, out13, out14, out15
  inc5 inc5_16 (.X(inc5_15_r), .R(inc5_16_r));  // open: Cout
  Demultiplexer #(.select(5), .width(32), .enable("false")) demultiplexer_18 (
    .out20(demultiplexer_18_out20), .out21(demultiplexer_18_out21), .out22(demultiplexer_18_out22),
    .out23(demultiplexer_18_out23), .out24(demultiplexer_18_out24), .out25(demultiplexer_18_out25),
    .out26(demultiplexer_18_out26), .out27(demultiplexer_18_out27), .out28(demultiplexer_18_out28),
    .out29(demultiplexer_18_out29), .out30(demultiplexer_18_out30), .out31(demultiplexer_18_out31),
    .in(in_23), .sel(inc5_17_r));  // open: out0, out1, out2, out3, out4, out5, out6, out7, out8, out9, out10, out11, out12, out13, out14, out15, out16, out17, out18, out19
  inc5 inc5_17 (.X(inc5_28_r), .R(inc5_17_r));  // open: Cout
  Demultiplexer #(.select(5), .width(32), .enable("false")) demultiplexer_19 (
    .out24(demultiplexer_19_out24), .out25(demultiplexer_19_out25), .out26(demultiplexer_19_out26),
    .out27(demultiplexer_19_out27), .out28(demultiplexer_19_out28), .out29(demultiplexer_19_out29),
    .out30(demultiplexer_19_out30), .out31(demultiplexer_19_out31), .in(in_27), .sel(inc5_18_r));  // open: out0, out1, out2, out3, out4, out5, out6, out7, out8, out9, out10, out11, out12, out13, out14, out15, out16, out17, out18, out19, out20, out21, out22, out23
  inc5 inc5_18 (.X(inc5_29_r), .R(inc5_18_r));  // open: Cout
  Demultiplexer #(.select(5), .width(32), .enable("false")) demultiplexer_20 (
    .out28(demultiplexer_20_out28), .out29(demultiplexer_20_out29), .out30(demultiplexer_20_out30),
    .out31(demultiplexer_20_out31), .in(in_31), .sel(inc5_19_r));  // open: out0, out1, out2, out3, out4, out5, out6, out7, out8, out9, out10, out11, out12, out13, out14, out15, out16, out17, out18, out19, out20, out21, out22, out23, out24, out25, out26, out27
  inc5 inc5_19 (.X(inc5_30_r), .R(inc5_19_r));  // open: Cout
  decodBufer decodbufer_393 (.in_1(demultiplexer_17_out16), .out_2(\Выход_16 ));
  decodBufer decodbufer_394 (.in_1(demultiplexer_17_out17), .out_2(out_52));
  decodBufer decodbufer_395 (.in_1(demultiplexer_17_out18), .out_2(out_53));
  decodBufer decodbufer_396 (.in_1(demultiplexer_17_out19), .out_2(out_54));
  decodBufer decodbufer_397 (.in_1(demultiplexer_17_out20), .out_2(out_55));
  decodBufer decodbufer_398 (.in_1(demultiplexer_17_out21), .out_2(out_56));
  decodBufer decodbufer_399 (.in_1(demultiplexer_17_out22), .out_2(out_57));
  decodBufer decodbufer_400 (.in_1(demultiplexer_17_out23), .out_2(out_58));
  decodBufer decodbufer_401 (.in_1(demultiplexer_17_out24), .out_2(out_59));
  decodBufer decodbufer_402 (.in_1(demultiplexer_17_out25), .out_2(out_60));
  decodBufer decodbufer_403 (.in_1(demultiplexer_17_out26), .out_2(out_61));
  decodBufer decodbufer_404 (.in_1(demultiplexer_17_out27), .out_2(out_62));
  decodBufer decodbufer_405 (.in_1(demultiplexer_17_out28), .out_2(out_63));
  decodBufer decodbufer_406 (.in_1(demultiplexer_17_out29), .out_2(out_64));
  decodBufer decodbufer_407 (.in_1(demultiplexer_17_out30), .out_2(out_65));
  decodBufer decodbufer_408 (.in_1(demultiplexer_17_out31), .out_2(out_66));
  inc5 inc5_20 (.X(inc5_16_r), .R(inc5_20_r));  // open: Cout
  Demultiplexer #(.select(5), .width(32), .enable("false")) demultiplexer_21 (
    .out21(demultiplexer_21_out21), .out22(demultiplexer_21_out22), .out23(demultiplexer_21_out23),
    .out24(demultiplexer_21_out24), .out25(demultiplexer_21_out25), .out26(demultiplexer_21_out26),
    .out27(demultiplexer_21_out27), .out28(demultiplexer_21_out28), .out29(demultiplexer_21_out29),
    .out30(demultiplexer_21_out30), .out31(demultiplexer_21_out31), .in(in_24), .sel(inc5_21_r));  // open: out0, out1, out2, out3, out4, out5, out6, out7, out8, out9, out10, out11, out12, out13, out14, out15, out16, out17, out18, out19, out20
  decodBufer decodbufer_409 (.in_1(demultiplexer_18_out20), .out_2(out_55));
  decodBufer decodbufer_410 (.in_1(demultiplexer_18_out21), .out_2(out_56));
  decodBufer decodbufer_411 (.in_1(demultiplexer_18_out22), .out_2(out_57));
  decodBufer decodbufer_412 (.in_1(demultiplexer_18_out23), .out_2(out_58));
  decodBufer decodbufer_413 (.in_1(demultiplexer_18_out24), .out_2(out_59));
  decodBufer decodbufer_414 (.in_1(demultiplexer_18_out25), .out_2(out_60));
  decodBufer decodbufer_415 (.in_1(demultiplexer_18_out26), .out_2(out_61));
  decodBufer decodbufer_416 (.in_1(demultiplexer_18_out27), .out_2(out_62));
  decodBufer decodbufer_417 (.in_1(demultiplexer_18_out28), .out_2(out_63));
  decodBufer decodbufer_418 (.in_1(demultiplexer_18_out29), .out_2(out_64));
  decodBufer decodbufer_419 (.in_1(demultiplexer_18_out30), .out_2(out_65));
  decodBufer decodbufer_420 (.in_1(demultiplexer_18_out31), .out_2(out_66));
  decodBufer decodbufer_421 ();  // open: in_1, out_2
  inc5 inc5_21 (.X(inc5_17_r), .R(inc5_21_r));  // open: Cout
  Demultiplexer #(.select(5), .width(32), .enable("false")) demultiplexer_22 (
    .out25(demultiplexer_22_out25), .out26(demultiplexer_22_out26), .out27(demultiplexer_22_out27),
    .out28(demultiplexer_22_out28), .out29(demultiplexer_22_out29), .out30(demultiplexer_22_out30),
    .out31(demultiplexer_22_out31), .in(in_28), .sel(inc5_22_r));  // open: out0, out1, out2, out3, out4, out5, out6, out7, out8, out9, out10, out11, out12, out13, out14, out15, out16, out17, out18, out19, out20, out21, out22, out23, out24
  decodBufer decodbufer_422 (.in_1(demultiplexer_19_out24), .out_2(out_59));
  decodBufer decodbufer_423 (.in_1(demultiplexer_19_out25), .out_2(out_60));
  decodBufer decodbufer_424 (.in_1(demultiplexer_19_out26), .out_2(out_61));
  decodBufer decodbufer_425 (.in_1(demultiplexer_19_out27), .out_2(out_62));
  decodBufer decodbufer_426 (.in_1(demultiplexer_19_out28), .out_2(out_63));
  decodBufer decodbufer_427 (.in_1(demultiplexer_19_out29), .out_2(out_64));
  decodBufer decodbufer_428 (.in_1(demultiplexer_19_out30), .out_2(out_65));
  decodBufer decodbufer_429 (.in_1(demultiplexer_19_out31), .out_2(out_66));
  inc5 inc5_22 (.X(inc5_18_r), .R(inc5_22_r));  // open: Cout
  Demultiplexer #(.select(5), .width(32), .enable("false")) demultiplexer_23 (
    .out29(demultiplexer_23_out29), .out30(demultiplexer_23_out30), .out31(demultiplexer_23_out31),
    .in(in_32), .sel(inc5_23_r));  // open: out0, out1, out2, out3, out4, out5, out6, out7, out8, out9, out10, out11, out12, out13, out14, out15, out16, out17, out18, out19, out20, out21, out22, out23, out24, out25, out26, out27, out28
  decodBufer decodbufer_430 (.in_1(demultiplexer_20_out28), .out_2(out_63));
  decodBufer decodbufer_431 (.in_1(demultiplexer_20_out29), .out_2(out_64));
  decodBufer decodbufer_432 (.in_1(demultiplexer_20_out30), .out_2(out_65));
  decodBufer decodbufer_433 (.in_1(demultiplexer_20_out31), .out_2(out_66));
  inc5 inc5_23 (.X(inc5_19_r), .R(inc5_23_r));  // open: Cout
  Demultiplexer #(.select(5), .width(32), .enable("false")) demultiplexer_24 (
    .out17(demultiplexer_24_out17), .out18(demultiplexer_24_out18), .out19(demultiplexer_24_out19),
    .out20(demultiplexer_24_out20), .out21(demultiplexer_24_out21), .out22(demultiplexer_24_out22),
    .out23(demultiplexer_24_out23), .out24(demultiplexer_24_out24), .out25(demultiplexer_24_out25),
    .out26(demultiplexer_24_out26), .out27(demultiplexer_24_out27), .out28(demultiplexer_24_out28),
    .out29(demultiplexer_24_out29), .out30(demultiplexer_24_out30), .out31(demultiplexer_24_out31),
    .in(in_20), .sel(inc5_20_r));  // open: out0, out1, out2, out3, out4, out5, out6, out7, out8, out9, out10, out11, out12, out13, out14, out15, out16
  decodBufer decodbufer_434 (.in_1(demultiplexer_21_out21), .out_2(out_56));
  decodBufer decodbufer_435 (.in_1(demultiplexer_21_out22), .out_2(out_57));
  decodBufer decodbufer_436 (.in_1(demultiplexer_21_out23), .out_2(out_58));
  decodBufer decodbufer_437 (.in_1(demultiplexer_21_out24), .out_2(out_59));
  decodBufer decodbufer_438 (.in_1(demultiplexer_21_out25), .out_2(out_60));
  decodBufer decodbufer_439 (.in_1(demultiplexer_21_out26), .out_2(out_61));
  decodBufer decodbufer_440 (.in_1(demultiplexer_21_out27), .out_2(out_62));
  decodBufer decodbufer_441 (.in_1(demultiplexer_21_out28), .out_2(out_63));
  decodBufer decodbufer_442 (.in_1(demultiplexer_21_out29), .out_2(out_64));
  decodBufer decodbufer_443 (.in_1(demultiplexer_21_out30), .out_2(out_65));
  decodBufer decodbufer_444 (.in_1(demultiplexer_21_out31), .out_2(out_66));
  decodBufer decodbufer_445 (.in_1(demultiplexer_22_out25), .out_2(out_60));
  decodBufer decodbufer_446 (.in_1(demultiplexer_22_out26), .out_2(out_61));
  decodBufer decodbufer_447 (.in_1(demultiplexer_22_out27), .out_2(out_62));
  decodBufer decodbufer_448 (.in_1(demultiplexer_22_out28), .out_2(out_63));
  decodBufer decodbufer_449 (.in_1(demultiplexer_22_out29), .out_2(out_64));
  decodBufer decodbufer_450 (.in_1(demultiplexer_22_out30), .out_2(out_65));
  decodBufer decodbufer_451 (.in_1(demultiplexer_22_out31), .out_2(out_66));
  decodBufer decodbufer_452 (.in_1(demultiplexer_23_out29), .out_2(out_64));
  decodBufer decodbufer_453 (.in_1(demultiplexer_23_out30), .out_2(out_65));
  decodBufer decodbufer_454 (.in_1(demultiplexer_23_out31), .out_2(out_66));
  Demultiplexer #(.select(5), .width(32), .enable("false")) demultiplexer_25 (
    .out18(demultiplexer_25_out18), .out19(demultiplexer_25_out19), .out20(demultiplexer_25_out20),
    .out21(demultiplexer_25_out21), .out22(demultiplexer_25_out22), .out23(demultiplexer_25_out23),
    .out24(demultiplexer_25_out24), .out25(demultiplexer_25_out25), .out26(demultiplexer_25_out26),
    .out27(demultiplexer_25_out27), .out28(demultiplexer_25_out28), .out29(demultiplexer_25_out29),
    .out30(demultiplexer_25_out30), .out31(demultiplexer_25_out31), .in(in_21), .sel(inc5_24_r));  // open: out0, out1, out2, out3, out4, out5, out6, out7, out8, out9, out10, out11, out12, out13, out14, out15, out16, out17
  decodBufer decodbufer_455 (.in_1(demultiplexer_24_out17), .out_2(out_52));
  decodBufer decodbufer_456 (.in_1(demultiplexer_24_out18), .out_2(out_53));
  decodBufer decodbufer_457 (.in_1(demultiplexer_24_out19), .out_2(out_54));
  decodBufer decodbufer_458 (.in_1(demultiplexer_24_out20), .out_2(out_55));
  decodBufer decodbufer_459 (.in_1(demultiplexer_24_out21), .out_2(out_56));
  decodBufer decodbufer_460 (.in_1(demultiplexer_24_out22), .out_2(out_57));
  decodBufer decodbufer_461 (.in_1(demultiplexer_24_out23), .out_2(out_58));
  decodBufer decodbufer_462 (.in_1(demultiplexer_24_out24), .out_2(out_59));
  decodBufer decodbufer_463 (.in_1(demultiplexer_24_out25), .out_2(out_60));
  decodBufer decodbufer_464 (.in_1(demultiplexer_24_out26), .out_2(out_61));
  decodBufer decodbufer_465 (.in_1(demultiplexer_24_out27), .out_2(out_62));
  decodBufer decodbufer_466 (.in_1(demultiplexer_24_out28), .out_2(out_63));
  decodBufer decodbufer_467 (.in_1(demultiplexer_24_out29), .out_2(out_64));
  decodBufer decodbufer_468 (.in_1(demultiplexer_24_out30), .out_2(out_65));
  decodBufer decodbufer_469 (.in_1(demultiplexer_24_out31), .out_2(out_66));
  inc5 inc5_24 (.X(inc5_20_r), .R(inc5_24_r));  // open: Cout
  Demultiplexer #(.select(5), .width(32), .enable("false")) demultiplexer_26 (
    .out22(demultiplexer_26_out22), .out23(demultiplexer_26_out23), .out24(demultiplexer_26_out24),
    .out25(demultiplexer_26_out25), .out26(demultiplexer_26_out26), .out27(demultiplexer_26_out27),
    .out28(demultiplexer_26_out28), .out29(demultiplexer_26_out29), .out30(demultiplexer_26_out30),
    .out31(demultiplexer_26_out31), .in(in_25), .sel(inc5_25_r));  // open: out0, out1, out2, out3, out4, out5, out6, out7, out8, out9, out10, out11, out12, out13, out14, out15, out16, out17, out18, out19, out20, out21
  inc5 inc5_25 (.X(inc5_21_r), .R(inc5_25_r));  // open: Cout
  Demultiplexer #(.select(5), .width(32), .enable("false")) demultiplexer_27 (
    .out26(demultiplexer_27_out26), .out27(demultiplexer_27_out27), .out28(demultiplexer_27_out28),
    .out29(demultiplexer_27_out29), .out30(demultiplexer_27_out30), .out31(demultiplexer_27_out31),
    .in(in_29), .sel(inc5_26_r));  // open: out0, out1, out2, out3, out4, out5, out6, out7, out8, out9, out10, out11, out12, out13, out14, out15, out16, out17, out18, out19, out20, out21, out22, out23, out24, out25
  inc5 inc5_26 (.X(inc5_22_r), .R(inc5_26_r));  // open: Cout
  Demultiplexer #(.select(5), .width(32), .enable("false")) demultiplexer_28 (
    .out30(demultiplexer_28_out30), .out31(demultiplexer_28_out31), .in(in_33), .sel(inc5_27_r));  // open: out0, out1, out2, out3, out4, out5, out6, out7, out8, out9, out10, out11, out12, out13, out14, out15, out16, out17, out18, out19, out20, out21, out22, out23, out24, out25, out26, out27, out28, out29
  inc5 inc5_27 (.X(inc5_23_r), .R(inc5_27_r));  // open: Cout
  decodBufer decodbufer_470 (.in_1(demultiplexer_25_out18), .out_2(out_53));
  decodBufer decodbufer_471 (.in_1(demultiplexer_25_out19), .out_2(out_54));
  decodBufer decodbufer_472 (.in_1(demultiplexer_25_out20), .out_2(out_55));
  decodBufer decodbufer_473 (.in_1(demultiplexer_25_out21), .out_2(out_56));
  decodBufer decodbufer_474 (.in_1(demultiplexer_25_out22), .out_2(out_57));
  decodBufer decodbufer_475 (.in_1(demultiplexer_25_out23), .out_2(out_58));
  decodBufer decodbufer_476 (.in_1(demultiplexer_25_out24), .out_2(out_59));
  decodBufer decodbufer_477 (.in_1(demultiplexer_25_out25), .out_2(out_60));
  decodBufer decodbufer_478 (.in_1(demultiplexer_25_out26), .out_2(out_61));
  decodBufer decodbufer_479 (.in_1(demultiplexer_25_out27), .out_2(out_62));
  decodBufer decodbufer_480 (.in_1(demultiplexer_25_out28), .out_2(out_63));
  decodBufer decodbufer_481 (.in_1(demultiplexer_25_out29), .out_2(out_64));
  decodBufer decodbufer_482 (.in_1(demultiplexer_25_out30), .out_2(out_65));
  decodBufer decodbufer_483 (.in_1(demultiplexer_25_out31), .out_2(out_66));
  decodBufer decodbufer_484 (.in_1(demultiplexer_26_out22), .out_2(out_57));
  decodBufer decodbufer_485 (.in_1(demultiplexer_26_out23), .out_2(out_58));
  decodBufer decodbufer_486 (.in_1(demultiplexer_26_out24), .out_2(out_59));
  decodBufer decodbufer_487 (.in_1(demultiplexer_26_out25), .out_2(out_60));
  decodBufer decodbufer_488 (.in_1(demultiplexer_26_out26), .out_2(out_61));
  decodBufer decodbufer_489 (.in_1(demultiplexer_26_out27), .out_2(out_62));
  decodBufer decodbufer_490 (.in_1(demultiplexer_26_out28), .out_2(out_63));
  decodBufer decodbufer_491 (.in_1(demultiplexer_26_out29), .out_2(out_64));
  decodBufer decodbufer_492 (.in_1(demultiplexer_26_out30), .out_2(out_65));
  decodBufer decodbufer_493 (.in_1(demultiplexer_26_out31), .out_2(out_66));
  decodBufer decodbufer_494 (.in_1(demultiplexer_27_out26), .out_2(out_61));
  decodBufer decodbufer_495 (.in_1(demultiplexer_27_out27), .out_2(out_62));
  decodBufer decodbufer_496 (.in_1(demultiplexer_27_out28), .out_2(out_63));
  decodBufer decodbufer_497 (.in_1(demultiplexer_27_out29), .out_2(out_64));
  decodBufer decodbufer_498 (.in_1(demultiplexer_27_out30), .out_2(out_65));
  decodBufer decodbufer_499 (.in_1(demultiplexer_27_out31), .out_2(out_66));
  decodBufer decodbufer_500 (.in_1(demultiplexer_28_out30), .out_2(out_65));
  decodBufer decodbufer_501 (.in_1(demultiplexer_28_out31), .out_2(out_66));
  Demultiplexer #(.select(5), .width(32), .enable("false")) demultiplexer_29 (
    .out19(demultiplexer_29_out19), .out20(demultiplexer_29_out20), .out21(demultiplexer_29_out21),
    .out22(demultiplexer_29_out22), .out23(demultiplexer_29_out23), .out24(demultiplexer_29_out24),
    .out25(demultiplexer_29_out25), .out26(demultiplexer_29_out26), .out27(demultiplexer_29_out27),
    .out28(demultiplexer_29_out28), .out29(demultiplexer_29_out29), .out30(demultiplexer_29_out30),
    .out31(demultiplexer_29_out31), .in(in_22), .sel(inc5_28_r));  // open: out0, out1, out2, out3, out4, out5, out6, out7, out8, out9, out10, out11, out12, out13, out14, out15, out16, out17, out18
  inc5 inc5_28 (.X(inc5_24_r), .R(inc5_28_r));  // open: Cout
  Demultiplexer #(.select(5), .width(32), .enable("false")) demultiplexer_30 (
    .out23(demultiplexer_30_out23), .out24(demultiplexer_30_out24), .out25(demultiplexer_30_out25),
    .out26(demultiplexer_30_out26), .out27(demultiplexer_30_out27), .out28(demultiplexer_30_out28),
    .out29(demultiplexer_30_out29), .out30(demultiplexer_30_out30), .out31(demultiplexer_30_out31),
    .in(in_26), .sel(inc5_29_r));  // open: out0, out1, out2, out3, out4, out5, out6, out7, out8, out9, out10, out11, out12, out13, out14, out15, out16, out17, out18, out19, out20, out21, out22
  inc5 inc5_29 (.X(inc5_25_r), .R(inc5_29_r));  // open: Cout
  Demultiplexer #(.select(5), .width(32), .enable("false")) demultiplexer_31 (
    .out27(demultiplexer_31_out27), .out28(demultiplexer_31_out28), .out29(demultiplexer_31_out29),
    .out30(demultiplexer_31_out30), .out31(demultiplexer_31_out31), .in(in_30), .sel(inc5_30_r));  // open: out0, out1, out2, out3, out4, out5, out6, out7, out8, out9, out10, out11, out12, out13, out14, out15, out16, out17, out18, out19, out20, out21, out22, out23, out24, out25, out26
  inc5 inc5_30 (.X(inc5_26_r), .R(inc5_30_r));  // open: Cout
  Demultiplexer #(.select(5), .width(32), .enable("false")) demultiplexer_32 (
    .out31(demultiplexer_32_out31), .in(in_34), .sel(inc5_31_r));  // open: out0, out1, out2, out3, out4, out5, out6, out7, out8, out9, out10, out11, out12, out13, out14, out15, out16, out17, out18, out19, out20, out21, out22, out23, out24, out25, out26, out27, out28, out29, out30
  inc5 inc5_31 (.X(inc5_27_r), .R(inc5_31_r));  // open: Cout
  decodBufer decodbufer_502 (.in_1(demultiplexer_29_out19), .out_2(out_54));
  decodBufer decodbufer_503 (.in_1(demultiplexer_29_out20), .out_2(out_55));
  decodBufer decodbufer_504 (.in_1(demultiplexer_29_out21), .out_2(out_56));
  decodBufer decodbufer_505 (.in_1(demultiplexer_29_out22), .out_2(out_57));
  decodBufer decodbufer_506 (.in_1(demultiplexer_29_out23), .out_2(out_58));
  decodBufer decodbufer_507 (.in_1(demultiplexer_29_out24), .out_2(out_59));
  decodBufer decodbufer_508 (.in_1(demultiplexer_29_out25), .out_2(out_60));
  decodBufer decodbufer_509 (.in_1(demultiplexer_29_out26), .out_2(out_61));
  decodBufer decodbufer_510 (.in_1(demultiplexer_29_out27), .out_2(out_62));
  decodBufer decodbufer_511 (.in_1(demultiplexer_29_out28), .out_2(out_63));
  decodBufer decodbufer_512 (.in_1(demultiplexer_29_out29), .out_2(out_64));
  decodBufer decodbufer_513 (.in_1(demultiplexer_29_out30), .out_2(out_65));
  decodBufer decodbufer_514 (.in_1(demultiplexer_29_out31), .out_2(out_66));
  decodBufer decodbufer_515 (.in_1(demultiplexer_30_out23), .out_2(out_58));
  decodBufer decodbufer_516 (.in_1(demultiplexer_30_out24), .out_2(out_59));
  decodBufer decodbufer_517 (.in_1(demultiplexer_30_out25), .out_2(out_60));
  decodBufer decodbufer_518 (.in_1(demultiplexer_30_out26), .out_2(out_61));
  decodBufer decodbufer_519 (.in_1(demultiplexer_30_out27), .out_2(out_62));
  decodBufer decodbufer_520 (.in_1(demultiplexer_30_out28), .out_2(out_63));
  decodBufer decodbufer_521 (.in_1(demultiplexer_30_out29), .out_2(out_64));
  decodBufer decodbufer_522 (.in_1(demultiplexer_30_out30), .out_2(out_65));
  decodBufer decodbufer_523 (.in_1(demultiplexer_30_out31), .out_2(out_66));
  decodBufer decodbufer_524 (.in_1(demultiplexer_31_out27), .out_2(out_62));
  decodBufer decodbufer_525 (.in_1(demultiplexer_31_out28), .out_2(out_63));
  decodBufer decodbufer_526 (.in_1(demultiplexer_31_out29), .out_2(out_64));
  decodBufer decodbufer_527 (.in_1(demultiplexer_31_out30), .out_2(out_65));
  decodBufer decodbufer_528 (.in_1(demultiplexer_31_out31), .out_2(out_66));
  decodBufer decodbufer_529 (.in_1(demultiplexer_32_out31), .out_2(out_66));

  // Other names for the same wires on the sheet: _0[31:0] = \Вход_0 ; _0_prime[31:0] = \Выход_0 ; _1[31:0] = in_2;
  //   _1_prime[31:0] = out_36; _2[31:0] = in_3; _2_prime[31:0] = out_37; _3[31:0] = in_4; _3_prime[31:0] = out_38;
  //   _4[31:0] = in_5; _4_prime[31:0] = out_39; _5[31:0] = in_8; _5_prime[31:0] = out_40; _6[31:0] = in_9;
  //   _6_prime[31:0] = out_41; _7[31:0] = in_10; _7_prime[31:0] = out_42; _8[31:0] = in_11; _8_prime[31:0] = out_43;
  //   _9[31:0] = in_12; _9_prime[31:0] = out_44; _10[31:0] = in_13; _10_prime[31:0] = out_45; _11[31:0] = in_14;
  //   _11_prime[31:0] = out_46; _12[31:0] = in_15; _12_prime[31:0] = out_47; _13[31:0] = in_16;
  //   _13_prime[31:0] = out_48; _14[31:0] = in_17; _14_prime[31:0] = out_49; _15[31:0] = in_18;
  //   _15_prime[31:0] = out_50; _16[31:0] = \Вход_16 ; _16_prime[31:0] = \Выход_16 ; _17[31:0] = in_20;
  //   _17_prime[31:0] = out_52; _18[31:0] = in_21; _18_prime[31:0] = out_53; _19[31:0] = in_22;
  //   _19_prime[31:0] = out_54; _20[31:0] = in_23; _20_prime[31:0] = out_55; _21[31:0] = in_24;
  //   _21_prime[31:0] = out_56; _22[31:0] = in_25; _22_prime[31:0] = out_57; _23[31:0] = in_26;
  //   _23_prime[31:0] = out_58; _24[31:0] = in_27; _24_prime[31:0] = out_59; _25[31:0] = in_28;
  //   _25_prime[31:0] = out_60; _26[31:0] = in_29; _26_prime[31:0] = out_61; _27[31:0] = in_30;
  //   _27_prime[31:0] = out_62; _28[31:0] = in_31; _28_prime[31:0] = out_63; _29[31:0] = in_32;
  //   _29_prime[31:0] = out_64; _30[31:0] = in_33; _30_prime[31:0] = out_65; _31[31:0] = in_34;
  //   _31_prime[31:0] = out_66
endmodule

module decodBufer (
  input  [31:0] in_1,
  output [31:0] out_2
);

  wire oradd32_1_out;

  oradd32 oradd32_1 (.in(in_1), .out(oradd32_1_out));
  assign out_2 = oradd32_1_out ? in_1 : 32'bz;  // Controlled_Buffer controlled_buffer_1

  // Notes on the sheet:
  //   out_2: pull=down
endmodule

module ShifterLeft (
  input  [31:0] \Вход_0 ,
  input  [31:0] in_2,
  input  [31:0] in_3,
  input  [31:0] in_4,
  input  [31:0] in_5,
  input  [31:0] in_6,
  input  [31:0] in_7,
  input  [31:0] in_8,
  input  [31:0] in_9,
  input  in_10,
  output [31:0] out_11,
  output [31:0] out_12,
  output [31:0] out_13,
  output [31:0] out_14,
  output [31:0] out_15,
  output [31:0] out_16,
  output [31:0] out_17,
  output [31:0] out_18,
  output [31:0] out_19
);

  wire [4:4] pull_resistor_1_node;
  wire [31:0] pull_resistor_5_node, pull_resistor_6_node, pull_resistor_7_node, pull_resistor_8_node,
       shifter_1_out, shifter_2_out, shifter_3_out, shifter_8_out, shifter_9_out;

  Pull_Resistor pull_resistor_1 (.node(pull_resistor_1_node[4]));
  Shifter #(.width(32)) shifter_1 (.in(\Вход_0 ), .\dist ({{4{pull_resistor_1_node[4]}}, in_10}), .out(shifter_1_out));
  Pull_Resistor pull_resistor_2 (.node(shifter_1_out));
  Shifter #(.width(32)) shifter_2 (.in(in_2), .\dist ({{4{pull_resistor_1_node[4]}}, in_10}), .out(shifter_2_out));
  Pull_Resistor pull_resistor_3 (.node(shifter_2_out));
  Shifter #(.width(32)) shifter_3 (.in(in_3), .\dist ({{4{pull_resistor_1_node[4]}}, in_10}), .out(shifter_3_out));
  Pull_Resistor pull_resistor_4 (.node(shifter_3_out));
  Pull_Resistor pull_resistor_5 (.node(pull_resistor_5_node));
  Shifter #(.width(32)) shifter_4 (
    .in(in_4), .\dist ({{4{pull_resistor_1_node[4]}}, in_10}), .out(pull_resistor_5_node));
  Pull_Resistor pull_resistor_6 (.node(pull_resistor_6_node));
  Shifter #(.width(32)) shifter_5 (
    .in(in_5), .\dist ({{4{pull_resistor_1_node[4]}}, in_10}), .out(pull_resistor_6_node));
  Pull_Resistor pull_resistor_7 (.node(pull_resistor_7_node));
  Shifter #(.width(32)) shifter_6 (
    .in(in_6), .\dist ({{4{pull_resistor_1_node[4]}}, in_10}), .out(pull_resistor_7_node));
  Pull_Resistor pull_resistor_8 (.node(pull_resistor_8_node));
  Shifter #(.width(32)) shifter_7 (
    .in(in_7), .\dist ({{4{pull_resistor_1_node[4]}}, in_10}), .out(pull_resistor_8_node));
  Shifter #(.width(32)) shifter_8 (.in(in_8), .\dist ({{4{pull_resistor_1_node[4]}}, in_10}), .out(shifter_8_out));
  Pull_Resistor pull_resistor_9 (.node(shifter_8_out));
  Shifter #(.width(32)) shifter_9 (.in(in_9), .\dist ({{4{pull_resistor_1_node[4]}}, in_10}), .out(shifter_9_out));
  Pull_Resistor pull_resistor_10 (.node(shifter_9_out));
  assign out_11 = in_10 ? shifter_1_out : 32'bz;  // Controlled_Buffer controlled_buffer_1
  assign out_12 = in_10 ? shifter_2_out : 32'bz;  // Controlled_Buffer controlled_buffer_2
  assign out_13 = in_10 ? shifter_3_out : 32'bz;  // Controlled_Buffer controlled_buffer_3
  assign out_14 = in_10 ? pull_resistor_5_node : 32'bz;  // Controlled_Buffer controlled_buffer_4
  assign out_15 = in_10 ? pull_resistor_6_node : 32'bz;  // Controlled_Buffer controlled_buffer_5
  assign out_16 = in_10 ? pull_resistor_7_node : 32'bz;  // Controlled_Buffer controlled_buffer_6
  assign out_17 = in_10 ? pull_resistor_8_node : 32'bz;  // Controlled_Buffer controlled_buffer_7
  assign out_18 = in_10 ? shifter_8_out : 32'bz;  // Controlled_Buffer controlled_buffer_8
  assign out_19 = in_10 ? shifter_9_out : 32'bz;  // Controlled_Buffer controlled_buffer_9

  // Other names for the same wires on the sheet: On = in_10
endmodule
module ShifterRight (
  input  [31:0] \Вход_0 ,
  input  [31:0] in_2,
  input  [31:0] in_3,
  input  [31:0] in_4,
  input  [31:0] in_5,
  input  [31:0] in_6,
  input  [31:0] in_7,
  input  [31:0] in_8,
  input  [31:0] in_9,
  input  in_10,
  output [31:0] out_11,
  output [31:0] out_12,
  output [31:0] out_13,
  output [31:0] out_14,
  output [31:0] out_15,
  output [31:0] out_16,
  output [31:0] out_17,
  output [31:0] out_18,
  output [31:0] out_19
);

  wire [4:4] pull_resistor_1_node;
  wire [31:0] pull_resistor_3_node, pull_resistor_5_node, pull_resistor_7_node, pull_resistor_8_node,
       pull_resistor_9_node, shifter_1_out, shifter_3_out, shifter_5_out, shifter_9_out;

  Pull_Resistor pull_resistor_1 (.node(pull_resistor_1_node[4]));
  Shifter #(.width(32), .shift("lr")) shifter_1 (
    .in(\Вход_0 ), .\dist ({{4{pull_resistor_1_node[4]}}, in_10}), .out(shifter_1_out));
  Pull_Resistor pull_resistor_2 (.node(shifter_1_out));
  Pull_Resistor pull_resistor_3 (.node(pull_resistor_3_node));
  Shifter #(.width(32), .shift("lr")) shifter_2 (
    .in(in_2), .\dist ({{4{pull_resistor_1_node[4]}}, in_10}), .out(pull_resistor_3_node));
  Shifter #(.width(32), .shift("lr")) shifter_3 (
    .in(in_3), .\dist ({{4{pull_resistor_1_node[4]}}, in_10}), .out(shifter_3_out));
  Pull_Resistor pull_resistor_4 (.node(shifter_3_out));
  Pull_Resistor pull_resistor_5 (.node(pull_resistor_5_node));
  Shifter #(.width(32), .shift("lr")) shifter_4 (
    .in(in_4), .\dist ({{4{pull_resistor_1_node[4]}}, in_10}), .out(pull_resistor_5_node));
  Shifter #(.width(32), .shift("lr")) shifter_5 (
    .in(in_5), .\dist ({{4{pull_resistor_1_node[4]}}, in_10}), .out(shifter_5_out));
  Pull_Resistor pull_resistor_6 (.node(shifter_5_out));
  Pull_Resistor pull_resistor_7 (.node(pull_resistor_7_node));
  Shifter #(.width(32), .shift("lr")) shifter_6 (
    .in(in_6), .\dist ({{4{pull_resistor_1_node[4]}}, in_10}), .out(pull_resistor_7_node));
  Pull_Resistor pull_resistor_8 (.node(pull_resistor_8_node));
  Shifter #(.width(32), .shift("lr")) shifter_7 (
    .in(in_7), .\dist ({{4{pull_resistor_1_node[4]}}, in_10}), .out(pull_resistor_8_node));
  Pull_Resistor pull_resistor_9 (.node(pull_resistor_9_node));
  Shifter #(.width(32), .shift("lr")) shifter_8 (
    .in(in_8), .\dist ({{4{pull_resistor_1_node[4]}}, in_10}), .out(pull_resistor_9_node));
  Shifter #(.width(32), .shift("lr")) shifter_9 (
    .in(in_9), .\dist ({{4{pull_resistor_1_node[4]}}, in_10}), .out(shifter_9_out));
  Pull_Resistor pull_resistor_10 (.node(shifter_9_out));
  assign out_11 = in_10 ? shifter_1_out : 32'bz;  // Controlled_Buffer controlled_buffer_1
  assign out_12 = in_10 ? pull_resistor_3_node : 32'bz;  // Controlled_Buffer controlled_buffer_2
  assign out_13 = in_10 ? shifter_3_out : 32'bz;  // Controlled_Buffer controlled_buffer_3
  assign out_14 = in_10 ? pull_resistor_5_node : 32'bz;  // Controlled_Buffer controlled_buffer_4
  assign out_15 = in_10 ? shifter_5_out : 32'bz;  // Controlled_Buffer controlled_buffer_5
  assign out_16 = in_10 ? pull_resistor_7_node : 32'bz;  // Controlled_Buffer controlled_buffer_6
  assign out_17 = in_10 ? pull_resistor_8_node : 32'bz;  // Controlled_Buffer controlled_buffer_7
  assign out_18 = in_10 ? pull_resistor_9_node : 32'bz;  // Controlled_Buffer controlled_buffer_8
  assign out_19 = in_10 ? shifter_9_out : 32'bz;  // Controlled_Buffer controlled_buffer_9

  // Other names for the same wires on the sheet: On = in_10
endmodule

module cdmEnemShoot (
  input  [1:0] \rand ,
  input  [7:0] shift,
  input  \Частота_процессора ,
  input  En,
  output [7:0] out,
  output Ready
);

  wire and_2_out, and_3_out, and_4_out, cdm_8_mark5_1_data_inst, cdm_8_mark5_1_mem_cycle, clr, d_ff_1_q,
       d_ff_2_q, decoder_1_out0, decoder_1_out1, decoder_3_out0, decoder_3_out1, decoder_3_out2, I_O_sel,
       not_1_out, not_2_out, or_1_out, pull_resistor_1_node, r, r_w, w;
  wire [7:0] addr, cdm_8_mark5_1_data_out, cdm_8_mark5_1_ps, cdm_8_mark5_1_r0, cdm_8_mark5_1_r1,
       cdm_8_mark5_1_r2, cdm_8_mark5_1_r3, cdm_8_mark5_1_sp, controlled_buffer_2_out,
       controlled_buffer_3_out, demultiplexer_1_out2, io_data, multiplexer_2_out, PC, reg0, reg1, res;

  and and_1 (I_O_sel, and_3_out, decoder_1_out1);
  Comparator comparator_1 (.a(PC), .b(8'h1), .eq(Ready));  // open: gt, lt
  D_Flip_Flop #(.trigger("falling")) d_ff_1 (
    .clk(\Частота_процессора ), .D(and_2_out), .Q(d_ff_1_q));  // open: Qn, preset, en, reset
  and and_2 (and_2_out, En, ~not_1_out);  // AND_Gate
  and and_3 (and_3_out, addr[4], addr[5], addr[6], addr[7], decoder_1_out1);
  // Probe on cdm_8_mark5_1_r1
  // Probe on cdm_8_mark5_1_r3
  // Probe on cdm_8_mark5_1_r2
  // Probe on cdm_8_mark5_1_r0
  Pull_Resistor pull_resistor_1 (.node(pull_resistor_1_node));
  Multiplexer #(.enable("false")) multiplexer_1 (
    .in0(1'b0), .in1(\Частота_процессора ), .out(pull_resistor_1_node), .sel(not_1_out));
  D_Flip_Flop #(.trigger("falling")) d_ff_2 (.Q(d_ff_2_q), .preset(Ready), .reset(d_ff_1_q));  // open: clk, D, Qn, en
  and and_4 (and_4_out, decoder_1_out1, ~and_3_out);  // AND_Gate
  // Probe on cdm_8_mark5_1_sp
  // Probe on PC
  // Probe on cdm_8_mark5_1_ps
  CdM_8_mark5 cdm_8_mark5_1 (
    .clock(pull_resistor_1_node), .addr(addr), .mem_read(r_w), .mem_cycle(cdm_8_mark5_1_mem_cycle),
    .data_inst(cdm_8_mark5_1_data_inst), .data_out(cdm_8_mark5_1_data_out),
    .data_in(controlled_buffer_2_out), .r0(cdm_8_mark5_1_r0), .r1(cdm_8_mark5_1_r1), .r2(cdm_8_mark5_1_r2),
    .r3(cdm_8_mark5_1_r3), .PC(PC), .SP(cdm_8_mark5_1_sp), .PS(cdm_8_mark5_1_ps));  // open: IAck, IRQ, vec, reset
  not not_1 (not_1_out, d_ff_2_q);
  Decoder #(.disabled(0)) decoder_1 (
    .out0(decoder_1_out0), .out1(decoder_1_out1), .sel(cdm_8_mark5_1_data_inst), .en(cdm_8_mark5_1_mem_cycle));
  not not_2 (not_2_out, r_w);
  assign io_data = not_2_out ? cdm_8_mark5_1_data_out : 8'bz;  // Controlled_Buffer controlled_buffer_1
  assign controlled_buffer_2_out = r_w ? io_data : 8'bz;  // Controlled_Buffer controlled_buffer_2
  // Probe on addr
  // Probe on io_data
  RAM ram_1 (.addr(addr), .data(io_data), .sel(and_4_out), .clk(\Частота_процессора ), .ld(r_w), .clr(clr));
  ROM rom_1 (.addr(addr), .data(io_data), .sel(decoder_1_out0));
  Decoder decoder_2 (.out0(r), .out1(w), .sel(r_w), .en(I_O_sel));
  Pull_Resistor pull_resistor_2 (.node(r));
  Pull_Resistor pull_resistor_3 (.node(w));
  or or_1 (or_1_out, r, w);
  Decoder #(.select(4)) decoder_3 (
    .out0(decoder_3_out0), .out1(decoder_3_out1), .out2(decoder_3_out2), .sel(addr[3:0]), .en(or_1_out));  // open: out3, out4, out5, out6, out7, out8, out9, out10, out11, out12, out13, out14, out15
  Pull_Resistor pull_resistor_4 (.node(decoder_3_out0));
  Pull_Resistor pull_resistor_5 (.node(decoder_3_out1));
  assign controlled_buffer_3_out = r ? io_data : 8'bz;  // Controlled_Buffer controlled_buffer_3
  Demultiplexer #(.select(4), .width(8)) demultiplexer_1 (
    .out2(demultiplexer_1_out2), .in(controlled_buffer_3_out), .sel(addr[3:0]), .en(r));  // open: out0, out1, out3, out4, out5, out6, out7, out8, out9, out10, out11, out12, out13, out14, out15
  Pull_Resistor pull_resistor_6 (.node(decoder_3_out2));
  assign res = r ? demultiplexer_1_out2 : 8'bz;  // Controlled_Buffer controlled_buffer_4
  assign io_data = w ? multiplexer_2_out : 8'bz;  // Controlled_Buffer controlled_buffer_5
  Multiplexer #(.select(4), .width(8)) multiplexer_2 (
    .in0(reg0), .in1(reg1), .out(multiplexer_2_out), .sel(addr[3:0]), .en(w));  // open: in2, in3, in4, in5, in6, in7, in8, in9, in10, in11, in12, in13, in14, in15
  Register register_1 (
    .D({{6{1'b0}}, \rand }), .en(decoder_3_out0), .Q(reg0), .clk(\Частота_процессора ));  // open: clr
  Register register_2 (.D(shift), .en(decoder_3_out1), .Q(reg1), .clk(\Частота_процессора ));  // open: clr
  Register register_3 (.D(res), .en(decoder_3_out2), .Q(out), .clk(\Частота_процессора ));  // open: clr

  // Other names for the same wires on the sheet: IOaddr[3:0] = addr[3:0]; clk = \Частота_процессора ;
  //   rand_t[1:0] = \rand 

  // Notes on the sheet:
  //   contents of rom_1 (hex, n*v repeats v):
  //   c0 c4 d2 f0 d0 8 d1 0 ba a e0 10 11 8a ee 9 d0 f1 b0 11 d0 4 14 d2 f2 a8 d6 1 213*0 1
  //   запись в регитсры (st)
  //   чтение из регитров (ld)
endmodule
